// Logisim project 16x16_matrix.circ as structural Verilog
module _16_16_matrix (
  input  [7:0] Lo_byte,
  input  Lo_byte_on,
  input  [7:0] Hi_byte,
  input  Hi_byte_On,
  input  [7:0] Selector,
  input  Selection_On,
  input  Bus_0
);

  wire clk, demultiplexer_1_out0, demultiplexer_1_out1, demultiplexer_1_out2, demultiplexer_1_out3,
       demultiplexer_1_out4, demultiplexer_1_out5, demultiplexer_1_out6, demultiplexer_1_out7,
       demultiplexer_1_out8, demultiplexer_1_out9, demultiplexer_1_out10, demultiplexer_1_out11,
       demultiplexer_1_out12, demultiplexer_1_out13, demultiplexer_1_out14, demultiplexer_1_out15;
  wire [7:0] register_1_q, register_2_q, register_3_q;
  wire [15:0] register_4_q, register_5_q, register_6_q, register_7_q, register_8_q, register_9_q,
       register_10_q, register_11_q, register_12_q, register_13_q, register_14_q, register_15_q,
       register_16_q, register_17_q, register_18_q, register_19_q;

  Clock clock_1 (.out(clk));
  Register register_1 (.D(Lo_byte), .en(Lo_byte_on), .Q(register_1_q), .clk(clk));  // open: clr
  Register register_2 (.D(Hi_byte), .en(Hi_byte_On), .Q(register_2_q), .clk(clk));  // open: clr
  Register #(.trigger("high")) register_3 (.D(Selector), .en(Selection_On), .Q(register_3_q), .clk(clk));  // open: clr
  // Probe on register_3_q
  Demultiplexer #(.select(4), .disabled(0)) demultiplexer_1 (
    .out0(demultiplexer_1_out0), .out1(demultiplexer_1_out1), .out2(demultiplexer_1_out2),
    .out3(demultiplexer_1_out3), .out4(demultiplexer_1_out4), .out5(demultiplexer_1_out5),
    .out6(demultiplexer_1_out6), .out7(demultiplexer_1_out7), .out8(demultiplexer_1_out8),
    .out9(demultiplexer_1_out9), .out10(demultiplexer_1_out10), .out11(demultiplexer_1_out11),
    .out12(demultiplexer_1_out12), .out13(demultiplexer_1_out13), .out14(demultiplexer_1_out14),
    .out15(demultiplexer_1_out15), .in(Selection_On), .sel(register_3_q[3:0]), .en(Selection_On));
  Register #(.width(16)) register_4 (
    .D({register_2_q, register_1_q}), .en(demultiplexer_1_out0), .Q(register_4_q), .clk(clk));  // open: clr
  Register #(.width(16)) register_5 (
    .D({register_2_q, register_1_q}), .en(demultiplexer_1_out1), .Q(register_5_q), .clk(clk));  // open: clr
  Register #(.width(16)) register_6 (
    .D({register_2_q, register_1_q}), .en(demultiplexer_1_out2), .Q(register_6_q), .clk(clk));  // open: clr
  Register #(.width(16)) register_7 (
    .D({register_2_q, register_1_q}), .en(demultiplexer_1_out3), .Q(register_7_q), .clk(clk));  // open: clr
  Register #(.width(16)) register_8 (
    .D({register_2_q, register_1_q}), .en(demultiplexer_1_out4), .Q(register_8_q), .clk(clk));  // open: clr
  Register #(.width(16)) register_9 (
    .D({register_2_q, register_1_q}), .en(demultiplexer_1_out5), .Q(register_9_q), .clk(clk));  // open: clr
  Register #(.width(16)) register_10 (
    .D({register_2_q, register_1_q}), .en(demultiplexer_1_out6), .Q(register_10_q), .clk(clk));  // open: clr
  Register #(.width(16)) register_11 (
    .D({register_2_q, register_1_q}), .en(demultiplexer_1_out7), .Q(register_11_q), .clk(clk));  // open: clr
  Register #(.width(16)) register_12 (
    .D({register_2_q, register_1_q}), .en(demultiplexer_1_out8), .Q(register_12_q), .clk(clk));  // open: clr
  Register #(.width(16)) register_13 (
    .D({register_2_q, register_1_q}), .en(demultiplexer_1_out9), .Q(register_13_q), .clk(clk));  // open: clr
  Register #(.width(16)) register_14 (
    .D({register_2_q, register_1_q}), .en(demultiplexer_1_out10), .Q(register_14_q), .clk(clk));  // open: clr
  Register #(.width(16)) register_15 (
    .D({register_2_q, register_1_q}), .en(demultiplexer_1_out11), .Q(register_15_q), .clk(clk));  // open: clr
  Register #(.width(16)) register_16 (
    .D({register_2_q, register_1_q}), .en(demultiplexer_1_out12), .Q(register_16_q), .clk(clk));  // open: clr
  Register #(.width(16)) register_17 (
    .D({register_2_q, register_1_q}), .en(demultiplexer_1_out13), .Q(register_17_q), .clk(clk));  // open: clr
  Register #(.width(16)) register_18 (
    .D({register_2_q, register_1_q}), .en(demultiplexer_1_out14), .Q(register_18_q), .clk(clk));  // open: clr
  Register #(.width(16)) register_19 (
    .D({register_2_q, register_1_q}), .en(demultiplexer_1_out15), .Q(register_19_q), .clk(clk));  // open: clr
  DotMatrix #(.inputtype("row"), .matrixcols(16), .matrixrows(16)) dotmatrix_1 (
    .row0(register_4_q), .row1(register_5_q), .row2(register_6_q), .row3(register_7_q), .row4(register_8_q),
    .row5(register_9_q), .row6(register_10_q), .row7(register_11_q), .row8(register_12_q),
    .row9(register_13_q), .row10(register_14_q), .row11(register_15_q), .row12(register_16_q),
    .row13(register_17_q), .row14(register_18_q), .row15(register_19_q));
endmodule

module _16_16_demonstration (
  input  Full_On,
  input  Selection_On,
  input  Bus_0
);

  wire clk, demultiplexer_1_out0, demultiplexer_1_out1, demultiplexer_1_out2, demultiplexer_1_out3,
       demultiplexer_1_out4, demultiplexer_1_out5, demultiplexer_1_out6, demultiplexer_1_out7,
       demultiplexer_1_out8, demultiplexer_1_out9, demultiplexer_1_out10, demultiplexer_1_out11,
       demultiplexer_1_out12, demultiplexer_1_out13, demultiplexer_1_out14, demultiplexer_1_out15, rst;
  wire [3:0] random_1_out;
  wire [15:0] random_2_out, register_1_q, register_2_q, register_3_q, register_4_q, register_5_q,
       register_6_q, register_7_q, register_8_q, register_9_q, register_10_q, register_11_q, register_12_q,
       register_13_q, register_14_q, register_15_q, register_16_q;

  Clock clock_1 (.out(clk));
  Button Reset (.out(rst));
  Demultiplexer #(.select(4), .disabled(0)) demultiplexer_1 (
    .out0(demultiplexer_1_out0), .out1(demultiplexer_1_out1), .out2(demultiplexer_1_out2),
    .out3(demultiplexer_1_out3), .out4(demultiplexer_1_out4), .out5(demultiplexer_1_out5),
    .out6(demultiplexer_1_out6), .out7(demultiplexer_1_out7), .out8(demultiplexer_1_out8),
    .out9(demultiplexer_1_out9), .out10(demultiplexer_1_out10), .out11(demultiplexer_1_out11),
    .out12(demultiplexer_1_out12), .out13(demultiplexer_1_out13), .out14(demultiplexer_1_out14),
    .out15(demultiplexer_1_out15), .in(Selection_On), .sel(random_1_out), .en(Selection_On));
  Random #(.width(4)) random_1 (.clk(clk), .next(Full_On), .out(random_1_out), .clr(rst));
  Random #(.width(16), .seed(5)) random_2 (.clk(clk), .next(Full_On), .out(random_2_out), .clr(rst));
  Register #(.width(16)) register_1 (
    .D(random_2_out), .en(demultiplexer_1_out0), .Q(register_1_q), .clk(clk), .clr(rst));
  Register #(.width(16)) register_2 (
    .D(random_2_out), .en(demultiplexer_1_out1), .Q(register_2_q), .clk(clk), .clr(rst));
  Register #(.width(16)) register_3 (
    .D(random_2_out), .en(demultiplexer_1_out2), .Q(register_3_q), .clk(clk), .clr(rst));
  Register #(.width(16)) register_4 (
    .D(random_2_out), .en(demultiplexer_1_out3), .Q(register_4_q), .clk(clk), .clr(rst));
  Register #(.width(16)) register_5 (
    .D(random_2_out), .en(demultiplexer_1_out4), .Q(register_5_q), .clk(clk), .clr(rst));
  Register #(.width(16)) register_6 (
    .D(random_2_out), .en(demultiplexer_1_out5), .Q(register_6_q), .clk(clk), .clr(rst));
  Register #(.width(16)) register_7 (
    .D(random_2_out), .en(demultiplexer_1_out6), .Q(register_7_q), .clk(clk), .clr(rst));
  Register #(.width(16)) register_8 (
    .D(random_2_out), .en(demultiplexer_1_out7), .Q(register_8_q), .clk(clk), .clr(rst));
  Register #(.width(16)) register_9 (
    .D(random_2_out), .en(demultiplexer_1_out8), .Q(register_9_q), .clk(clk), .clr(rst));
  Register #(.width(16)) register_10 (
    .D(random_2_out), .en(demultiplexer_1_out9), .Q(register_10_q), .clk(clk), .clr(rst));
  Register #(.width(16)) register_11 (
    .D(random_2_out), .en(demultiplexer_1_out10), .Q(register_11_q), .clk(clk), .clr(rst));
  Register #(.width(16)) register_12 (
    .D(random_2_out), .en(demultiplexer_1_out11), .Q(register_12_q), .clk(clk), .clr(rst));
  Register #(.width(16)) register_13 (
    .D(random_2_out), .en(demultiplexer_1_out12), .Q(register_13_q), .clk(clk), .clr(rst));
  Register #(.width(16)) register_14 (
    .D(random_2_out), .en(demultiplexer_1_out13), .Q(register_14_q), .clk(clk), .clr(rst));
  Register #(.width(16)) register_15 (
    .D(random_2_out), .en(demultiplexer_1_out14), .Q(register_15_q), .clk(clk), .clr(rst));
  Register #(.width(16)) register_16 (
    .D(random_2_out), .en(demultiplexer_1_out15), .Q(register_16_q), .clk(clk), .clr(rst));
  DotMatrix #(.inputtype("row"), .matrixcols(16), .matrixrows(16)) dotmatrix_1 (
    .row0(register_1_q), .row1(register_2_q), .row2(register_3_q), .row3(register_4_q), .row4(register_5_q),
    .row5(register_6_q), .row6(register_7_q), .row7(register_8_q), .row8(register_9_q), .row9(register_10_q),
    .row10(register_11_q), .row11(register_12_q), .row12(register_13_q), .row13(register_14_q),
    .row14(register_15_q), .row15(register_16_q));

  // Other names for the same wires on the sheet: on = Full_On
endmodule
