// Logisim project main.circ as structural Verilog: 10 circuits, main circuit Main
module Main (
  input  [7:0] Birth_s_conditions_bit_array,
  input  [7:0] Survival_conditions_bit_array
);

  wire clock_1_out, engine_1_selected_cell_s_state, engine_1_setting_mode, Start_out;
  wire [6:0] keyboard_1_data;
  wire [31:0] engine_1_row_0, engine_1_row_1, engine_1_row_2, engine_1_row_3, engine_1_row_4, engine_1_row_5,
       engine_1_row_6, engine_1_row_7, engine_1_row_8, engine_1_row_9, engine_1_row_10, engine_1_row_11,
       engine_1_row_12, engine_1_row_13, engine_1_row_14, engine_1_row_15, engine_1_row_16, engine_1_row_17,
       engine_1_row_18, engine_1_row_19, engine_1_row_20, engine_1_row_21, engine_1_row_22, engine_1_row_23,
       engine_1_row_24, engine_1_row_25, engine_1_row_26, engine_1_row_27, engine_1_row_28, engine_1_row_29,
       engine_1_row_30, engine_1_row_31;

  Clock clock_1 (.out(clock_1_out));
  Keyboard keyboard_1 (.clk(clock_1_out), .re(engine_1_setting_mode), .data(keyboard_1_data));  // open: clr, avail
  Button Start (.out(Start_out));
  Engine engine_1 (
    .clock(clock_1_out), .Birth_condtitions(Birth_s_conditions_bit_array), .Start(Start_out),
    .Keyboard_code(keyboard_1_data), .Death_conditins(Survival_conditions_bit_array), .Row_0(engine_1_row_0),
    .Row_1(engine_1_row_1), .Row_2(engine_1_row_2), .Row_3(engine_1_row_3), .Row_4(engine_1_row_4),
    .Row_5(engine_1_row_5), .Row_6(engine_1_row_6), .Row_7(engine_1_row_7), .Row_8(engine_1_row_8),
    .Row_9(engine_1_row_9), .Row_10(engine_1_row_10), .Row_11(engine_1_row_11), .Row_12(engine_1_row_12),
    .Row_13(engine_1_row_13), .Row_14(engine_1_row_14), .Row_15(engine_1_row_15), .Row_16(engine_1_row_16),
    .Row_17(engine_1_row_17), .Row_18(engine_1_row_18), .Row_19(engine_1_row_19), .Row_20(engine_1_row_20),
    .Row_21(engine_1_row_21), .Row_22(engine_1_row_22), .Row_23(engine_1_row_23), .Row_24(engine_1_row_24),
    .Row_25(engine_1_row_25), .Row_26(engine_1_row_26), .Row_27(engine_1_row_27), .Row_28(engine_1_row_28),
    .Row_29(engine_1_row_29), .Row_30(engine_1_row_30), .Row_31(engine_1_row_31),
    .Setting_mode(engine_1_setting_mode), .Selected_cell_s_state(engine_1_selected_cell_s_state));
  DotMatrix #(.inputtype("row"), .matrixcols(32), .matrixrows(32)) dotmatrix_1 (
    .row0(engine_1_row_0), .row1(engine_1_row_1), .row2(engine_1_row_2), .row3(engine_1_row_3),
    .row4(engine_1_row_4), .row5(engine_1_row_5), .row6(engine_1_row_6), .row7(engine_1_row_7),
    .row8(engine_1_row_8), .row9(engine_1_row_9), .row10(engine_1_row_10), .row11(engine_1_row_11),
    .row12(engine_1_row_12), .row13(engine_1_row_13), .row14(engine_1_row_14), .row15(engine_1_row_15),
    .row16(engine_1_row_16), .row17(engine_1_row_17), .row18(engine_1_row_18), .row19(engine_1_row_19),
    .row20(engine_1_row_20), .row21(engine_1_row_21), .row22(engine_1_row_22), .row23(engine_1_row_23),
    .row24(engine_1_row_24), .row25(engine_1_row_25), .row26(engine_1_row_26), .row27(engine_1_row_27),
    .row28(engine_1_row_28), .row29(engine_1_row_29), .row30(engine_1_row_30), .row31(engine_1_row_31));
  LED led_1 (.in(engine_1_selected_cell_s_state));

  // Notes on the sheet:
  //   Keyboard
endmodule

module Engine (
  input  clock,
  input  [7:0] Birth_condtitions,
  input  [7:0] Death_conditins,
  input  Start,
  input  [6:0] Keyboard_code,
  output [31:0] Row_0,
  output [31:0] Row_1,
  output [31:0] Row_2,
  output [31:0] Row_3,
  output [31:0] Row_4,
  output Selected_cell_s_state,
  output [31:0] Row_5,
  output [31:0] Row_6,
  output Setting_mode,
  output [31:0] Row_7,
  output [31:0] Row_8,
  output [31:0] Row_9,
  output [31:0] Row_10,
  output [31:0] Row_11,
  output [31:0] Row_12,
  output [31:0] Row_13,
  output [31:0] Row_14,
  output [31:0] Row_15,
  output [31:0] Row_16,
  output [31:0] Row_17,
  output [31:0] Row_18,
  output [31:0] Row_19,
  output [31:0] Row_20,
  output [31:0] Row_21,
  output [31:0] Row_22,
  output [31:0] Row_23,
  output [31:0] Row_24,
  output [31:0] Row_25,
  output [31:0] Row_26,
  output [31:0] Row_27,
  output [31:0] Row_28,
  output [31:0] Row_29,
  output [31:0] Row_30,
  output [31:0] Row_31
);

  wire and_1_out, and_2_out, and_3_out, and_4_out, and_5_out, and_6_out, and_7_out, and_10_out, and_11_out,
       and_12_out, and_13_out, and_14_out, cdm_8_mark5_1_p1, cdm_8_mark5_1_p2, cdm_8_mark5_1_p4,
       cdm_8_mark5_1_p5, cdm_8_mark5_1_p6, cdm_8_mark5_1_p7, cdm_8_mark5_1_p8, cdm_8_mark5_1_p9, change_bit,
       change_bit_slow, code, comparator_1_eq, comparator_2_eq, comparator_3_eq, comparator_4_eq,
       comparator_5_eq, comparator_6_eq, comparator_7_eq, comparator_8_eq, comparator_9_eq, comparator_10_eq,
       comparator_11_lt, comparator_12_eq, comparator_13_eq, comparator_14_eq, comparator_15_eq,
       comparator_16_eq, CPU_invert_bit, CPU_invert_bit_slow, data, decoder_1_out0, decoder_3_out0,
       decoder_4_out1, decoder_6_out0, decoder_7_out1, decoder_9_out1, decoder_10_out1, decoder_11_out1,
       decoder_12_out1, decoder_13_out1, in_out, IOsel, is_null_byte, is_row_null, mem, multiplexer_1_out,
       multiplexer_4_out, not_2_out, not_3_out, not_4_out, not_5_out, not_6_out, not_7_out, not_8_out,
       not_9_out, not_10_out, not_12_out, not_13_out, not_15_out, not_16_out, not_17_out, not_18_out,
       not_19_out, not_21_out, not_22_out, not_23_out, not_24_out, not_25_out, not_26_out, not_28_out,
       not_29_out, not_30_out, not_31_out, playing, RAM, update_generation, update_generation_slow,
       xnor_1_out, xnor_2_out, xnor_3_out;
  wire [4:0] cpuX, cpuY, keyboard_controller_1_x, keyboard_controller_1_y, multiplexer_2_out,
       multiplexer_3_out;
  wire [7:0] bus, cdm_8_mark5_1_p13, cdm_8_mark5_1_p14, controlled_buffer_1_out, controlled_buffer_3_out,
       env_sum, IOaddr, not_27_out, register_1_q, register_5_q, register_6_q;
  wire [7:1] register_3_q;
  wire [7:5] register_2_q, register_4_q;
  wire [31:0] inverted_row, random_write_buffer_1_row_0, random_write_buffer_1_row_1,
       random_write_buffer_1_row_2, random_write_buffer_1_row_3, random_write_buffer_1_row_4,
       random_write_buffer_1_row_5, random_write_buffer_1_row_6, random_write_buffer_1_row_7,
       random_write_buffer_1_row_8, random_write_buffer_1_row_9, random_write_buffer_1_row_10,
       random_write_buffer_1_row_11, random_write_buffer_1_row_12, random_write_buffer_1_row_13,
       random_write_buffer_1_row_14, random_write_buffer_1_row_15, random_write_buffer_1_row_16,
       random_write_buffer_1_row_17, random_write_buffer_1_row_18, random_write_buffer_1_row_19,
       random_write_buffer_1_row_20, random_write_buffer_1_row_21, random_write_buffer_1_row_22,
       random_write_buffer_1_row_23, random_write_buffer_1_row_24, random_write_buffer_1_row_25,
       random_write_buffer_1_row_26, random_write_buffer_1_row_27, random_write_buffer_1_row_28,
       random_write_buffer_1_row_29, random_write_buffer_1_row_30, random_write_buffer_1_row_31,
       stable_generation_s_buffer_1_row_0_2, stable_generation_s_buffer_1_row_1_2,
       stable_generation_s_buffer_1_row_2_2, stable_generation_s_buffer_1_row_3_2,
       stable_generation_s_buffer_1_row_4_2, stable_generation_s_buffer_1_row_5_2,
       stable_generation_s_buffer_1_row_6_2, stable_generation_s_buffer_1_row_7_2,
       stable_generation_s_buffer_1_row_8_2, stable_generation_s_buffer_1_row_9_2,
       stable_generation_s_buffer_1_row_10_2, stable_generation_s_buffer_1_row_11_2,
       stable_generation_s_buffer_1_row_12_2, stable_generation_s_buffer_1_row_13_2,
       stable_generation_s_buffer_1_row_14_2, stable_generation_s_buffer_1_row_15_2,
       stable_generation_s_buffer_1_row_16_2, stable_generation_s_buffer_1_row_17_2,
       stable_generation_s_buffer_1_row_18_2, stable_generation_s_buffer_1_row_19_2,
       stable_generation_s_buffer_1_row_20_2, stable_generation_s_buffer_1_row_21_2,
       stable_generation_s_buffer_1_row_22_2, stable_generation_s_buffer_1_row_23_2,
       stable_generation_s_buffer_1_row_24_2, stable_generation_s_buffer_1_row_25_2,
       stable_generation_s_buffer_1_row_26_2, stable_generation_s_buffer_1_row_27_2,
       stable_generation_s_buffer_1_row_28_2, stable_generation_s_buffer_1_row_29_2,
       stable_generation_s_buffer_1_row_30_2, stable_generation_s_buffer_1_row_31_2;

  Keyboard_controller keyboard_controller_1 (
    .ASCII_code(Keyboard_code), .X(keyboard_controller_1_x), .Y(keyboard_controller_1_y), .Switch(change_bit));
  // Probe on keyboard_controller_1_y
  // Probe on keyboard_controller_1_x
  not not_1 (change_bit_slow, not_2_out);
  not not_2 (not_2_out, change_bit);
  not not_3 (not_3_out, not_3_out);
  not not_4 (not_4_out, not_4_out);
  not not_5 (not_5_out, not_5_out);
  not not_6 (not_6_out, not_6_out);
  Multiplexer #(.disabled(0), .enable("false")) multiplexer_1 (
    .in0(change_bit), .in1(CPU_invert_bit), .out(multiplexer_1_out), .sel(playing));
  // Probe on multiplexer_2_out
  Multiplexer #(.width(5), .disabled(0), .enable("false")) multiplexer_2 (
    .in0(cpuY), .in1(keyboard_controller_1_y), .out(multiplexer_2_out), .sel(Setting_mode));
  Multiplexer #(.width(5), .disabled(0), .enable("false")) multiplexer_3 (
    .in0(keyboard_controller_1_x), .in1(cpuX), .out(multiplexer_3_out), .sel(playing));
  // Probe on multiplexer_3_out
  not not_7 (not_7_out, Start);
  Random_write_buffer random_write_buffer_1 (
    .Row_0(random_write_buffer_1_row_0), .Row_1(random_write_buffer_1_row_1),
    .Row_2(random_write_buffer_1_row_2), .Row_3(random_write_buffer_1_row_3),
    .Row_4(random_write_buffer_1_row_4), .Row_5(random_write_buffer_1_row_5),
    .Row_6(random_write_buffer_1_row_6), .Row_7(random_write_buffer_1_row_7),
    .Row_8(random_write_buffer_1_row_8), .Row_9(random_write_buffer_1_row_9),
    .Row_10(random_write_buffer_1_row_10), .Row_11(random_write_buffer_1_row_11),
    .Row_12(random_write_buffer_1_row_12), .Row_13(random_write_buffer_1_row_13),
    .Row_14(random_write_buffer_1_row_14), .Row_15(random_write_buffer_1_row_15),
    .Row_16(random_write_buffer_1_row_16), .Row_17(random_write_buffer_1_row_17),
    .Row_18(random_write_buffer_1_row_18), .Row_19(random_write_buffer_1_row_19),
    .Row_20(random_write_buffer_1_row_20), .Row_21(random_write_buffer_1_row_21),
    .Row_22(random_write_buffer_1_row_22), .Row_23(random_write_buffer_1_row_23),
    .Row_24(random_write_buffer_1_row_24), .Row_25(random_write_buffer_1_row_25),
    .Row_26(random_write_buffer_1_row_26), .Row_27(random_write_buffer_1_row_27),
    .Row_28(random_write_buffer_1_row_28), .Row_29(random_write_buffer_1_row_29),
    .Row_30(random_write_buffer_1_row_30), .Row_31(random_write_buffer_1_row_31),
    .Row_selector(multiplexer_2_out), .Write_row(multiplexer_1_out), .Input_row(inverted_row));
  Register register_1 (.D(bus), .Q(register_1_q), .clk(not_9_out));  // open: en, clr
  not not_8 (not_8_out, decoder_1_out0);
  not not_9 (not_9_out, not_8_out);
  not not_10 (not_10_out, CPU_invert_bit);
  not not_11 (CPU_invert_bit_slow, not_10_out);
  assign controlled_buffer_1_out = decoder_3_out0 ? bus : 8'bz;  // Controlled_Buffer controlled_buffer_1
  not not_12 (not_12_out, not_13_out);
  xnor xnor_1 (xnor_1_out, not_7_out, Start);
  Decoder #(.disabled(0)) decoder_1 (.out0(decoder_1_out0), .sel(in_out), .en(and_1_out));  // open: out1
  Decoder #(.disabled(0)) decoder_2 (.out0(CPU_invert_bit), .sel(in_out), .en(and_2_out));  // open: out1
  Decoder #(.disabled(0)) decoder_3 (.out0(decoder_3_out0), .sel(in_out), .en(and_3_out));  // open: out1
  Register register_2 (.D(controlled_buffer_1_out), .Q({register_2_q, cpuY}), .clk(not_12_out));  // open: en, clr
  not not_13 (not_13_out, decoder_3_out0);
  Decoder #(.disabled(0)) decoder_4 (.out1(decoder_4_out1), .sel(in_out), .en(and_4_out));  // open: out0
  assign bus = decoder_4_out1 ? {register_3_q, playing} : 8'bz;  // Controlled_Buffer controlled_buffer_2
  Register register_3 (.D(8'h1), .Q({register_3_q, playing}), .clk(xnor_1_out));  // open: en, clr
  Row_s_bit_invertor row_s_bit_invertor_1 (
    .Row_0(random_write_buffer_1_row_0), .Row_1(random_write_buffer_1_row_1),
    .Row_2(random_write_buffer_1_row_2), .Row_3(random_write_buffer_1_row_3),
    .Row_4(random_write_buffer_1_row_4), .Row_5(random_write_buffer_1_row_5),
    .Row_6(random_write_buffer_1_row_6), .Row_7(random_write_buffer_1_row_7),
    .Row_8(random_write_buffer_1_row_8), .Row_9(random_write_buffer_1_row_9),
    .Row_10(random_write_buffer_1_row_10), .Row_11(random_write_buffer_1_row_11),
    .Row_12(random_write_buffer_1_row_12), .Row_13(random_write_buffer_1_row_13),
    .Row_14(random_write_buffer_1_row_14), .Row_15(random_write_buffer_1_row_15),
    .Row_16(random_write_buffer_1_row_16), .Row_17(random_write_buffer_1_row_17),
    .Row_18(random_write_buffer_1_row_18), .Row_19(random_write_buffer_1_row_19),
    .Row_20(random_write_buffer_1_row_20), .Row_21(random_write_buffer_1_row_21),
    .Row_22(random_write_buffer_1_row_22), .Row_23(random_write_buffer_1_row_23),
    .Row_24(random_write_buffer_1_row_24), .Row_25(random_write_buffer_1_row_25),
    .Row_26(random_write_buffer_1_row_26), .Row_27(random_write_buffer_1_row_27),
    .Row_28(random_write_buffer_1_row_28), .Row_29(random_write_buffer_1_row_29),
    .Row_30(random_write_buffer_1_row_30), .Row_31(random_write_buffer_1_row_31),
    .Row_with_inverted_bit(inverted_row), .Y__row_index(multiplexer_2_out), .X__bit_index(multiplexer_3_out));
  Comparator comparator_1 (.a(IOaddr), .b({8{1'b1}}), .eq(comparator_1_eq));  // open: gt, lt
  and and_1 (and_1_out, comparator_1_eq, IOsel);
  Comparator comparator_2 (.a(IOaddr), .b(8'hf9), .eq(comparator_2_eq));  // open: gt, lt
  and and_2 (and_2_out, comparator_2_eq, IOsel);
  Comparator comparator_3 (.a(IOaddr), .b(8'hf3), .eq(comparator_3_eq));  // open: gt, lt
  Comparator comparator_4 (.a(IOaddr), .b(8'hf0), .eq(comparator_4_eq));  // open: gt, lt
  not not_14 (Setting_mode, playing);
  and and_3 (and_3_out, comparator_3_eq, IOsel);
  and and_4 (and_4_out, comparator_4_eq, IOsel);
  // Probe on inverted_row
  not not_15 (not_15_out, not_15_out);
  not not_16 (not_16_out, not_16_out);
  not not_17 (not_17_out, not_17_out);
  Comparator comparator_5 (.a(8'h40), .b(register_1_q), .eq(comparator_5_eq));  // open: gt, lt
  Comparator comparator_6 (.a(8'h41), .b(register_1_q), .eq(comparator_6_eq));  // open: gt, lt
  Comparator comparator_7 (.a(8'h42), .b(register_1_q), .eq(comparator_7_eq));  // open: gt, lt
  LED led_1 (.in(comparator_5_eq));
  LED led_2 (.in(comparator_6_eq));
  LED led_3 (.in(comparator_7_eq));
  assign controlled_buffer_3_out = decoder_6_out0 ? bus : 8'bz;  // Controlled_Buffer controlled_buffer_3
  not not_18 (not_18_out, Setting_mode);
  xnor xnor_2 (xnor_2_out, not_18_out, Setting_mode);
  not not_19 (not_19_out, update_generation);
  not not_20 (update_generation_slow, not_19_out);
  Register register_4 (.D(controlled_buffer_3_out), .Q({register_4_q, cpuX}), .clk(not_21_out));  // open: en, clr
  not not_21 (not_21_out, not_22_out);
  not not_22 (not_22_out, decoder_6_out0);
  assign bus = decoder_7_out1 ? register_5_q : 8'bz;  // Controlled_Buffer controlled_buffer_4
  Register register_5 (.D(Birth_condtitions), .Q(register_5_q), .clk(xnor_2_out));  // open: en, clr
  Stable_generation_s_buffer stable_generation_s_buffer_1 (
    .Save_generation_trigger(multiplexer_4_out), .Row_0(random_write_buffer_1_row_0),
    .Row_1(random_write_buffer_1_row_1), .Row_2(random_write_buffer_1_row_2),
    .Row_3(random_write_buffer_1_row_3), .Row_4(random_write_buffer_1_row_4),
    .Row_5(random_write_buffer_1_row_5), .Row_6(random_write_buffer_1_row_6),
    .Row_7(random_write_buffer_1_row_7), .Row_8(random_write_buffer_1_row_8),
    .Row_9(random_write_buffer_1_row_9), .Row_10(random_write_buffer_1_row_10),
    .Row_11(random_write_buffer_1_row_11), .Row_12(random_write_buffer_1_row_12),
    .Row_13(random_write_buffer_1_row_13), .Row_14(random_write_buffer_1_row_14),
    .Row_15(random_write_buffer_1_row_15), .Row_16(random_write_buffer_1_row_16),
    .Row_17(random_write_buffer_1_row_17), .Row_18(random_write_buffer_1_row_18),
    .Row_19(random_write_buffer_1_row_19), .Row_20(random_write_buffer_1_row_20),
    .Row_21(random_write_buffer_1_row_21), .Row_22(random_write_buffer_1_row_22),
    .Row_23(random_write_buffer_1_row_23), .Row_24(random_write_buffer_1_row_24),
    .Row_25(random_write_buffer_1_row_25), .Row_26(random_write_buffer_1_row_26),
    .Row_27(random_write_buffer_1_row_27), .Row_28(random_write_buffer_1_row_28),
    .Row_29(random_write_buffer_1_row_29), .Row_30(random_write_buffer_1_row_30),
    .Row_31(random_write_buffer_1_row_31), .Row_0_2(stable_generation_s_buffer_1_row_0_2),
    .Row_1_2(stable_generation_s_buffer_1_row_1_2), .Row_2_2(stable_generation_s_buffer_1_row_2_2),
    .Row_3_2(stable_generation_s_buffer_1_row_3_2), .Row_4_2(stable_generation_s_buffer_1_row_4_2),
    .Row_5_2(stable_generation_s_buffer_1_row_5_2), .Row_6_2(stable_generation_s_buffer_1_row_6_2),
    .Row_7_2(stable_generation_s_buffer_1_row_7_2), .Row_8_2(stable_generation_s_buffer_1_row_8_2),
    .Row_9_2(stable_generation_s_buffer_1_row_9_2), .Row_10_2(stable_generation_s_buffer_1_row_10_2),
    .Row_11_2(stable_generation_s_buffer_1_row_11_2), .Row_12_2(stable_generation_s_buffer_1_row_12_2),
    .Row_13_2(stable_generation_s_buffer_1_row_13_2), .Row_14_2(stable_generation_s_buffer_1_row_14_2),
    .Row_15_2(stable_generation_s_buffer_1_row_15_2), .Row_16_2(stable_generation_s_buffer_1_row_16_2),
    .Row_17_2(stable_generation_s_buffer_1_row_17_2), .Row_18_2(stable_generation_s_buffer_1_row_18_2),
    .Row_19_2(stable_generation_s_buffer_1_row_19_2), .Row_20_2(stable_generation_s_buffer_1_row_20_2),
    .Row_21_2(stable_generation_s_buffer_1_row_21_2), .Row_22_2(stable_generation_s_buffer_1_row_22_2),
    .Row_23_2(stable_generation_s_buffer_1_row_23_2), .Row_24_2(stable_generation_s_buffer_1_row_24_2),
    .Row_25_2(stable_generation_s_buffer_1_row_25_2), .Row_26_2(stable_generation_s_buffer_1_row_26_2),
    .Row_27_2(stable_generation_s_buffer_1_row_27_2), .Row_28_2(stable_generation_s_buffer_1_row_28_2),
    .Row_29_2(stable_generation_s_buffer_1_row_29_2), .Row_30_2(stable_generation_s_buffer_1_row_30_2),
    .Row_31_2(stable_generation_s_buffer_1_row_31_2));
  Multiplexer #(.disabled(0), .enable("false")) multiplexer_4 (
    .in0(clock), .in1(update_generation), .out(multiplexer_4_out), .sel(playing));
  Decoder #(.disabled(0)) decoder_5 (.out0(update_generation), .sel(in_out), .en(and_5_out));  // open: out1
  Decoder #(.disabled(0)) decoder_6 (.out0(decoder_6_out0), .sel(in_out), .en(and_6_out));  // open: out1
  Decoder #(.disabled(0)) decoder_7 (.out1(decoder_7_out1), .sel(in_out), .en(and_7_out));  // open: out0
  Comparator comparator_8 (.a(IOaddr), .b(8'hfa), .eq(comparator_8_eq));  // open: gt, lt
  and and_5 (and_5_out, comparator_8_eq, IOsel);
  Comparator comparator_9 (.a(IOaddr), .b(8'hf4), .eq(comparator_9_eq));  // open: gt, lt
  and and_6 (and_6_out, comparator_9_eq, IOsel);
  Comparator comparator_10 (.a(IOaddr), .b(8'hf1), .eq(comparator_10_eq));  // open: gt, lt
  and and_7 (and_7_out, comparator_10_eq, IOsel);
  // Probe on cdm_8_mark5_1_p1
  // Probe on cdm_8_mark5_1_p4
  // Probe on cdm_8_mark5_1_p2
  and and_8 (IOsel, not_25_out, clock, data);
  not not_23 (not_23_out, not_23_out);
  not not_24 (not_24_out, not_24_out);
  Environment_data_constructor environment_data_constructor_1 (
    .Row_0(stable_generation_s_buffer_1_row_0_2), .Row_1(stable_generation_s_buffer_1_row_1_2),
    .Row_2(stable_generation_s_buffer_1_row_2_2), .Row_3(stable_generation_s_buffer_1_row_3_2),
    .Row_4(stable_generation_s_buffer_1_row_4_2), .Row_5(stable_generation_s_buffer_1_row_5_2),
    .Row_6(stable_generation_s_buffer_1_row_6_2), .Row_7(stable_generation_s_buffer_1_row_7_2),
    .Row_8(stable_generation_s_buffer_1_row_8_2), .Row_9(stable_generation_s_buffer_1_row_9_2),
    .Row_10(stable_generation_s_buffer_1_row_10_2), .Row_11(stable_generation_s_buffer_1_row_11_2),
    .Row_12(stable_generation_s_buffer_1_row_12_2), .Row_13(stable_generation_s_buffer_1_row_13_2),
    .Row_14(stable_generation_s_buffer_1_row_14_2), .Row_15(stable_generation_s_buffer_1_row_15_2),
    .Row_16(stable_generation_s_buffer_1_row_16_2), .Row_17(stable_generation_s_buffer_1_row_17_2),
    .Row_18(stable_generation_s_buffer_1_row_18_2), .Row_19(stable_generation_s_buffer_1_row_19_2),
    .Row_20(stable_generation_s_buffer_1_row_20_2), .Row_21(stable_generation_s_buffer_1_row_21_2),
    .Row_22(stable_generation_s_buffer_1_row_22_2), .Row_23(stable_generation_s_buffer_1_row_23_2),
    .Row_24(stable_generation_s_buffer_1_row_24_2), .Row_25(stable_generation_s_buffer_1_row_25_2),
    .Row_26(stable_generation_s_buffer_1_row_26_2), .Row_27(stable_generation_s_buffer_1_row_27_2),
    .Row_28(stable_generation_s_buffer_1_row_28_2), .Row_29(stable_generation_s_buffer_1_row_29_2),
    .Row_30(stable_generation_s_buffer_1_row_30_2), .Row_31(stable_generation_s_buffer_1_row_31_2),
    .Is_byte_env__null(is_null_byte), .Y__row_index(multiplexer_2_out), .X__bit_index(multiplexer_3_out),
    .Is_row_env__null(is_row_null), .Sum(env_sum), .Bit(Selected_cell_s_state));
  // Probe on cdm_8_mark5_1_p5
  // Probe on cdm_8_mark5_1_p6
  // Probe on cdm_8_mark5_1_p7
  not not_25 (not_25_out, comparator_11_lt);
  // Probe on cdm_8_mark5_1_p8
  // CdM_8_mark5 cdm_8_mark5_1: pin names not known; wires that end beside it: cdm_8_mark5_1_p1, cdm_8_mark5_1_p2, clock, cdm_8_mark5_1_p4, cdm_8_mark5_1_p5, cdm_8_mark5_1_p6, cdm_8_mark5_1_p7, cdm_8_mark5_1_p8, cdm_8_mark5_1_p9, mem, in_out, IOaddr, cdm_8_mark5_1_p13, cdm_8_mark5_1_p14
  assign bus = not_26_out ? cdm_8_mark5_1_p13 : 8'bz;  // Controlled_Buffer controlled_buffer_5
  not not_26 (not_26_out, in_out);
  assign cdm_8_mark5_1_p14 = in_out ? bus : 8'bz;  // Controlled_Buffer controlled_buffer_6
  and and_9 (RAM, comparator_11_lt, data);
  assign not_27_out = ~Death_conditins;  // NOT_Gate not_27, 8 bits wide
  not not_28 (not_28_out, Setting_mode);
  // Probe on env_sum
  Decoder #(.disabled(0)) decoder_8 (.out0(code), .out1(data), .sel(cdm_8_mark5_1_p9), .en(mem));
  xnor xnor_3 (xnor_3_out, not_28_out, Setting_mode);
  // Probe on IOaddr
  Decoder #(.disabled(0)) decoder_9 (.out1(decoder_9_out1), .sel(in_out), .en(and_10_out));  // open: out0
  assign bus = decoder_9_out1 ? {{7{1'b0}}, Selected_cell_s_state} : 8'bz;  // Controlled_Buffer controlled_buffer_7
  Decoder #(.disabled(0)) decoder_10 (.out1(decoder_10_out1), .sel(in_out), .en(and_11_out));  // open: out0
  assign bus = decoder_10_out1 ? register_6_q : 8'bz;  // Controlled_Buffer controlled_buffer_8
  Register register_6 (.D(not_27_out), .Q(register_6_q), .clk(xnor_3_out));  // open: en, clr
  Blinker blinker_1 (
    .input0(stable_generation_s_buffer_1_row_0_2), .input1(stable_generation_s_buffer_1_row_1_2),
    .input2(stable_generation_s_buffer_1_row_2_2), .input3(stable_generation_s_buffer_1_row_3_2),
    .input4(stable_generation_s_buffer_1_row_4_2), .input5(stable_generation_s_buffer_1_row_5_2),
    .input6(stable_generation_s_buffer_1_row_6_2), .input7(stable_generation_s_buffer_1_row_7_2),
    .input8(stable_generation_s_buffer_1_row_8_2), .input9(stable_generation_s_buffer_1_row_9_2),
    .input10(stable_generation_s_buffer_1_row_10_2), .input11(stable_generation_s_buffer_1_row_11_2),
    .input12(stable_generation_s_buffer_1_row_12_2), .input13(stable_generation_s_buffer_1_row_13_2),
    .input14(stable_generation_s_buffer_1_row_14_2), .input15(stable_generation_s_buffer_1_row_15_2),
    .input16(stable_generation_s_buffer_1_row_16_2), .input17(stable_generation_s_buffer_1_row_17_2),
    .input18(stable_generation_s_buffer_1_row_18_2), .input19(stable_generation_s_buffer_1_row_19_2),
    .input20(stable_generation_s_buffer_1_row_20_2), .input21(stable_generation_s_buffer_1_row_21_2),
    .input22(stable_generation_s_buffer_1_row_22_2), .input23(stable_generation_s_buffer_1_row_23_2),
    .input24(stable_generation_s_buffer_1_row_24_2), .input25(stable_generation_s_buffer_1_row_25_2),
    .input26(stable_generation_s_buffer_1_row_26_2), .input27(stable_generation_s_buffer_1_row_27_2),
    .input28(stable_generation_s_buffer_1_row_28_2), .input29(stable_generation_s_buffer_1_row_29_2),
    .input30(stable_generation_s_buffer_1_row_30_2), .input31(stable_generation_s_buffer_1_row_31_2),
    .X(multiplexer_3_out), .Y(multiplexer_2_out), .SWITCH(clock), .output0(Row_0), .output1(Row_1),
    .output2(Row_2), .output3(Row_3), .output4(Row_4), .output5(Row_5), .output6(Row_6), .output7(Row_7),
    .output8(Row_8), .output9(Row_9), .output10(Row_10), .output11(Row_11), .output12(Row_12),
    .output13(Row_13), .output14(Row_14), .output15(Row_15), .output16(Row_16), .output17(Row_17),
    .output18(Row_18), .output19(Row_19), .output20(Row_20), .output21(Row_21), .output22(Row_22),
    .output23(Row_23), .output24(Row_24), .output25(Row_25), .output26(Row_26), .output27(Row_27),
    .output28(Row_28), .output29(Row_29), .output30(Row_30), .output31(Row_31));  // open: changed_string
  Comparator #(.mode("unsigned")) comparator_11 (.a(IOaddr), .b(8'hf0), .lt(comparator_11_lt));  // open: gt, eq
  Comparator comparator_12 (.a(IOaddr), .b(8'hf5), .eq(comparator_12_eq));  // open: gt, lt
  and and_10 (and_10_out, comparator_12_eq, IOsel);
  Comparator comparator_13 (.a(IOaddr), .b(8'hf2), .eq(comparator_13_eq));  // open: gt, lt
  // Probe on bus
  ROM rom_1 (.addr(IOaddr), .data(bus), .sel(code));
  RAM ram_1 (.addr(IOaddr), .data(bus), .sel(RAM), .clk(clock), .ld(in_out));  // open: clr
  and and_11 (and_11_out, comparator_13_eq, IOsel);
  not not_29 (not_29_out, not_29_out);
  assign bus = decoder_11_out1 ? env_sum : 8'bz;  // Controlled_Buffer controlled_buffer_9
  Decoder #(.disabled(0)) decoder_11 (.out1(decoder_11_out1), .sel(in_out), .en(and_12_out));  // open: out0
  Comparator comparator_14 (.a(IOaddr), .b(8'hf6), .eq(comparator_14_eq));  // open: gt, lt
  and and_12 (and_12_out, comparator_14_eq, IOsel);
  not not_30 (not_30_out, not_30_out);
  Decoder #(.disabled(0)) decoder_12 (.out1(decoder_12_out1), .sel(in_out), .en(and_13_out));  // open: out0
  assign bus = decoder_12_out1 ? {{7{1'b0}}, is_row_null} : 8'bz;  // Controlled_Buffer controlled_buffer_10
  Comparator comparator_15 (.a(IOaddr), .b(8'hf7), .eq(comparator_15_eq));  // open: gt, lt
  and and_13 (and_13_out, comparator_15_eq, IOsel);
  not not_31 (not_31_out, not_31_out);
  assign bus = decoder_13_out1 ? {{7{1'b0}}, is_null_byte} : 8'bz;  // Controlled_Buffer controlled_buffer_11
  Decoder #(.disabled(0)) decoder_13 (.out1(decoder_13_out1), .sel(in_out), .en(and_14_out));  // open: out0
  Comparator comparator_16 (.a(IOaddr), .b(8'hf8), .eq(comparator_16_eq));  // open: gt, lt
  and and_14 (and_14_out, comparator_16_eq, IOsel);

  // Other names for the same wires on the sheet: selected_bit = Selected_cell_s_state;
  //   birth_cond[7:0] = Birth_condtitions; IOdata[7:0] = bus; rd_wr = in_out; setting = Setting_mode;
  //   survival_cond[7:0] = Death_conditins

  // Notes on the sheet:
  //   DEV I/O REGS.
  //   ROW READ / WRITE
  //   (read only thus CdM -> buffer)
  //   PROCESSED CELL
  //   READ ONLY INPUTS
  //   (immutable game state)
  //   Cell 0xff (CPU status)
  //   Cell 0xf5 (invert signal)
  //   Cell 0xf3 (Y - row)
  //   Cell 0xf0 (state)
  //   waiting for start
  //   reading field
  //   processing field
  //   Cell 0xf4 (X - bit)
  //   Cell 0xf6 (update Stable generation's buffer)
  //   Cell 0xf1 (birth conditions)
  //   Cell 0xfa (bit value)
  //   Structure of I/O bus
  //   Cell 0xf2 (survival conditions)
  //   Harvard Architecture
  //   Minimal IO cell address
  //   contents of rom_1 (hex, n*v repeats v):
  //   ee 35 d2 8 d1 0 18 a e0 11 88 b3 95 1d 8a ee 7 4 d7 d3 8 f e0 21 d2 1 42 a6 8d 98 8b ee 15 d7 5 e1
  //   29 d2 60 ee 2b d2 68 88 12 ba a e0 34 d0 f9 a0 d7 cd 50 d0 ff d1 40 a1 d1 f0 b4 0 e0 3e d1 50 a4 d1
  //   f1 b4 d1 60 d6 13 d1 f2 b4 d1 68 d6 13 d0 fa a0 d0 ff d1 42 a1 d3 1f c3 d0 f3 a3 d3 f7 bf f e1 9c d1
  //   1f d3 4 c3 d0 f4 a1 d0 f8 b0 0 e1 95 d3 8 c1 d0 f4 a1 d0 f6 b0 d1 f5 b5 0 e0 88 d6 22 ee 8e 5 e0 8e
  //   d0 f9 a0 c5 89 8b e1 77 ee 98 d0 f8 11 c7 8b e1 6b c7 8b e5 5d ee 53 d4
  //   Cell 0xfb (env. sum)
  //   Cell 0xfc (is null rows env.)
  //   Cell 0xfd (is null byte env.)
endmodule

module Keyboard_controller (
  input  [6:0] ASCII_code,
  output [4:0] Y,
  output [4:0] X,
  output Switch
);

  wire _0x0y, _0x0y_A, _0x_y, _0x_y_A, _0x_y_A_t, _0x_y_t, minus_x0y, minus_x0y_A, minus_x_y, minus_x_y_A,
       minus_x_y_A_t, minus_x_y_t, or_1_out, or_2_out, or_3_out, or_4_out, or_5_out, or_6_out, or_7_out,
       or_8_out, or_9_out, or_10_out, or_11_out, or_12_out, or_13_out, or_14_out, or_15_out, or_16_out,
       or_17_out, or_18_out, plus_x0y, plus_x0y_A, plus_x_y, plus_x_y_A, plus_x_y_A_t, plus_x_y_t;
  wire [4:0] counter_2_q;

  Comparator #(.width(7)) comparator_1 (.a(ASCII_code), .b(7'b0110111), .eq(plus_x_y_t));  // open: gt, lt
  Comparator #(.width(7)) comparator_2 (.a(ASCII_code), .b(7'b0110100), .eq(plus_x0y));  // open: gt, lt
  Comparator #(.width(7)) comparator_3 (.a(ASCII_code), .b(7'b0110001), .eq(plus_x_y));  // open: gt, lt
  Comparator #(.width(7)) comparator_4 (.a(ASCII_code), .b(7'b1110001), .eq(plus_x_y_A_t));  // open: gt, lt
  Comparator #(.width(7)) comparator_5 (.a(ASCII_code), .b(7'b1100001), .eq(plus_x0y_A));  // open: gt, lt
  Comparator #(.width(7)) comparator_6 (.a(ASCII_code), .b(7'b1111010), .eq(plus_x_y_A));  // open: gt, lt
  Comparator #(.width(7)) comparator_7 (.a(ASCII_code), .b(7'b0111000), .eq(_0x_y_t));  // open: gt, lt
  Comparator #(.width(7)) comparator_8 (.a(ASCII_code), .b(7'b0110101), .eq(_0x0y));  // open: gt, lt
  Comparator #(.width(7)) comparator_9 (.a(ASCII_code), .b(7'b0110010), .eq(_0x_y));  // open: gt, lt
  Comparator #(.width(7)) comparator_10 (.a(ASCII_code), .b(7'b1110111), .eq(_0x_y_A_t));  // open: gt, lt
  Comparator #(.width(7)) comparator_11 (.a(ASCII_code), .b(7'b0100000), .eq(_0x0y_A));  // open: gt, lt
  Comparator #(.width(7)) comparator_12 (.a(ASCII_code), .b(7'b1110011), .eq(_0x_y_A));  // open: gt, lt
  Comparator #(.width(7)) comparator_13 (.a(ASCII_code), .b(7'b0111001), .eq(minus_x_y_t));  // open: gt, lt
  Comparator #(.width(7)) comparator_14 (.a(ASCII_code), .b(7'b0110110), .eq(minus_x0y));  // open: gt, lt
  Comparator #(.width(7)) comparator_15 (.a(ASCII_code), .b(7'b0110011), .eq(minus_x_y));  // open: gt, lt
  Comparator #(.width(7)) comparator_16 (.a(ASCII_code), .b(7'b1100101), .eq(minus_x_y_A_t));  // open: gt, lt
  Comparator #(.width(7)) comparator_17 (.a(ASCII_code), .b(7'b1100100), .eq(minus_x0y_A));  // open: gt, lt
  Comparator #(.width(7)) comparator_18 (.a(ASCII_code), .b(7'b1100011), .eq(minus_x_y_A));  // open: gt, lt
  or or_1 (or_1_out, minus_x_y_t, minus_x_y_A_t);
  or or_2 (or_2_out, _0x_y_t, _0x_y_A_t);
  or or_3 (or_3_out, plus_x_y_t, plus_x_y_A_t);
  or or_4 (or_4_out, minus_x_y, minus_x_y_A);
  or or_5 (or_5_out, _0x_y, _0x_y_A);
  or or_6 (or_6_out, plus_x_y, plus_x_y_A);
  or or_7 (or_7_out, minus_x_y_t, minus_x_y_A_t);
  or or_8 (or_8_out, minus_x0y, minus_x0y_A);
  or or_9 (or_9_out, minus_x_y, minus_x_y_A);
  or or_10 (or_10_out, plus_x_y_t, plus_x_y_A_t);
  or or_11 (or_11_out, plus_x0y, plus_x0y_A);
  or or_12 (or_12_out, plus_x_y, plus_x_y_A);
  or or_13 (or_13_out, or_1_out, or_2_out, or_3_out);
  or or_14 (or_14_out, or_13_out, or_15_out);
  or or_15 (or_15_out, or_4_out, or_5_out, or_6_out);
  or or_16 (or_16_out, or_7_out, or_8_out, or_9_out);
  or or_17 (or_17_out, or_16_out, or_18_out);
  or or_18 (or_18_out, or_10_out, or_11_out, or_12_out);
  // Probe on Y
  Counter #(.width(5), .max('h1f)) counter_1 (
    .load(or_13_out), .count(or_14_out), .Q(Y), .clk(or_14_out));  // open: D, carry, clr
  Counter #(.width(5), .max('h1f)) counter_2 (
    .load(or_16_out), .count(or_17_out), .Q(counter_2_q), .clk(or_17_out));  // open: D, carry, clr
  // Probe on X
  Adder #(.width(5)) adder_1 (.a({5{1'b1}}), .b(counter_2_q), .out(X));  // open: cin, cout
  or or_19 (Switch, _0x0y, _0x0y_A);

  // Notes on the sheet:
  //   Y position
  //   X position
endmodule

module Random_write_buffer (
  input  [31:0] Input_row,
  input  Write_row,
  input  [4:0] Row_selector,
  output [31:0] Row_0,
  output [31:0] Row_1,
  output [31:0] Row_2,
  output [31:0] Row_3,
  output [31:0] Row_4,
  output [31:0] Row_5,
  output [31:0] Row_6,
  output [31:0] Row_7,
  output [31:0] Row_8,
  output [31:0] Row_9,
  output [31:0] Row_10,
  output [31:0] Row_11,
  output [31:0] Row_12,
  output [31:0] Row_13,
  output [31:0] Row_14,
  output [31:0] Row_15,
  output [31:0] Row_16,
  output [31:0] Row_17,
  output [31:0] Row_18,
  output [31:0] Row_19,
  output [31:0] Row_20,
  output [31:0] Row_21,
  output [31:0] Row_22,
  output [31:0] Row_23,
  output [31:0] Row_24,
  output [31:0] Row_25,
  output [31:0] Row_26,
  output [31:0] Row_27,
  output [31:0] Row_28,
  output [31:0] Row_29,
  output [31:0] Row_30,
  output [31:0] Row_31
);

  wire decoder_1_out0, decoder_1_out1, decoder_1_out2, decoder_1_out3, decoder_1_out4, decoder_1_out5,
       decoder_1_out6, decoder_1_out7, decoder_1_out8, decoder_1_out9, decoder_1_out10, decoder_1_out11,
       decoder_1_out12, decoder_1_out13, decoder_1_out14, decoder_1_out15, decoder_1_out16, decoder_1_out17,
       decoder_1_out18, decoder_1_out19, decoder_1_out20, decoder_1_out21, decoder_1_out22, decoder_1_out23,
       decoder_1_out24, decoder_1_out25, decoder_1_out26, decoder_1_out27, decoder_1_out28, decoder_1_out29,
       decoder_1_out30, decoder_1_out31;

  Decoder #(.select(5), .disabled(0)) decoder_1 (
    .out0(decoder_1_out0), .out1(decoder_1_out1), .out2(decoder_1_out2), .out3(decoder_1_out3),
    .out4(decoder_1_out4), .out5(decoder_1_out5), .out6(decoder_1_out6), .out7(decoder_1_out7),
    .out8(decoder_1_out8), .out9(decoder_1_out9), .out10(decoder_1_out10), .out11(decoder_1_out11),
    .out12(decoder_1_out12), .out13(decoder_1_out13), .out14(decoder_1_out14), .out15(decoder_1_out15),
    .out16(decoder_1_out16), .out17(decoder_1_out17), .out18(decoder_1_out18), .out19(decoder_1_out19),
    .out20(decoder_1_out20), .out21(decoder_1_out21), .out22(decoder_1_out22), .out23(decoder_1_out23),
    .out24(decoder_1_out24), .out25(decoder_1_out25), .out26(decoder_1_out26), .out27(decoder_1_out27),
    .out28(decoder_1_out28), .out29(decoder_1_out29), .out30(decoder_1_out30), .out31(decoder_1_out31),
    .sel(Row_selector), .en(Write_row));
  Register #(.width(32)) register_1 (.D(Input_row), .Q(Row_0), .clk(decoder_1_out0));  // open: en, clr
  Register #(.width(32)) register_2 (.D(Input_row), .Q(Row_1), .clk(decoder_1_out1));  // open: en, clr
  Register #(.width(32)) register_3 (.D(Input_row), .Q(Row_2), .clk(decoder_1_out2));  // open: en, clr
  Register #(.width(32)) register_4 (.D(Input_row), .Q(Row_3), .clk(decoder_1_out3));  // open: en, clr
  Register #(.width(32)) register_5 (.D(Input_row), .Q(Row_4), .clk(decoder_1_out4));  // open: en, clr
  Register #(.width(32)) register_6 (.D(Input_row), .Q(Row_5), .clk(decoder_1_out5));  // open: en, clr
  Register #(.width(32)) register_7 (.D(Input_row), .Q(Row_6), .clk(decoder_1_out6));  // open: en, clr
  Register #(.width(32)) register_8 (.D(Input_row), .Q(Row_7), .clk(decoder_1_out7));  // open: en, clr
  Register #(.width(32)) register_9 (.D(Input_row), .Q(Row_8), .clk(decoder_1_out8));  // open: en, clr
  Register #(.width(32)) register_10 (.D(Input_row), .Q(Row_9), .clk(decoder_1_out9));  // open: en, clr
  Register #(.width(32)) register_11 (.D(Input_row), .Q(Row_10), .clk(decoder_1_out10));  // open: en, clr
  Register #(.width(32)) register_12 (.D(Input_row), .Q(Row_11), .clk(decoder_1_out11));  // open: en, clr
  Register #(.width(32)) register_13 (.D(Input_row), .Q(Row_12), .clk(decoder_1_out12));  // open: en, clr
  Register #(.width(32)) register_14 (.D(Input_row), .Q(Row_13), .clk(decoder_1_out13));  // open: en, clr
  Register #(.width(32)) register_15 (.D(Input_row), .Q(Row_14), .clk(decoder_1_out14));  // open: en, clr
  Register #(.width(32)) register_16 (.D(Input_row), .Q(Row_15), .clk(decoder_1_out15));  // open: en, clr
  Register #(.width(32)) register_17 (.D(Input_row), .Q(Row_16), .clk(decoder_1_out16));  // open: en, clr
  Register #(.width(32)) register_18 (.D(Input_row), .Q(Row_17), .clk(decoder_1_out17));  // open: en, clr
  Register #(.width(32)) register_19 (.D(Input_row), .Q(Row_18), .clk(decoder_1_out18));  // open: en, clr
  Register #(.width(32)) register_20 (.D(Input_row), .Q(Row_19), .clk(decoder_1_out19));  // open: en, clr
  Register #(.width(32)) register_21 (.D(Input_row), .Q(Row_20), .clk(decoder_1_out20));  // open: en, clr
  Register #(.width(32)) register_22 (.D(Input_row), .Q(Row_21), .clk(decoder_1_out21));  // open: en, clr
  Register #(.width(32)) register_23 (.D(Input_row), .Q(Row_22), .clk(decoder_1_out22));  // open: en, clr
  Register #(.width(32)) register_24 (.D(Input_row), .Q(Row_23), .clk(decoder_1_out23));  // open: en, clr
  Register #(.width(32)) register_25 (.D(Input_row), .Q(Row_24), .clk(decoder_1_out24));  // open: en, clr
  Register #(.width(32)) register_26 (.D(Input_row), .Q(Row_25), .clk(decoder_1_out25));  // open: en, clr
  Register #(.width(32)) register_27 (.D(Input_row), .Q(Row_26), .clk(decoder_1_out26));  // open: en, clr
  Register #(.width(32)) register_28 (.D(Input_row), .Q(Row_27), .clk(decoder_1_out27));  // open: en, clr
  Register #(.width(32)) register_29 (.D(Input_row), .Q(Row_28), .clk(decoder_1_out28));  // open: en, clr
  Register #(.width(32)) register_30 (.D(Input_row), .Q(Row_29), .clk(decoder_1_out29));  // open: en, clr
  Register #(.width(32)) register_31 (.D(Input_row), .Q(Row_30), .clk(decoder_1_out30));  // open: en, clr
  Register #(.width(32)) register_32 (.D(Input_row), .Q(Row_31), .clk(decoder_1_out31));  // open: en, clr

  // Other names for the same wires on the sheet: row0[31:0] = Row_0; row1[31:0] = Row_1; row2[31:0] = Row_2;
  //   row3[31:0] = Row_3; row4[31:0] = Row_4; row5[31:0] = Row_5; row6[31:0] = Row_6; row7[31:0] = Row_7;
  //   row8[31:0] = Row_8; row9[31:0] = Row_9; row10[31:0] = Row_10; row11[31:0] = Row_11; row12[31:0] = Row_12;
  //   row13[31:0] = Row_13; row14[31:0] = Row_14; row15[31:0] = Row_15; row16[31:0] = Row_16; row17[31:0] = Row_17;
  //   row18[31:0] = Row_18; row19[31:0] = Row_19; row20[31:0] = Row_20; row21[31:0] = Row_21; row22[31:0] = Row_22;
  //   row23[31:0] = Row_23; row24[31:0] = Row_24; row25[31:0] = Row_25; row26[31:0] = Row_26; row27[31:0] = Row_27;
  //   row28[31:0] = Row_28; row29[31:0] = Row_29; row30[31:0] = Row_30; row31[31:0] = Row_31
endmodule

module Stable_generation_s_buffer (
  input  Save_generation_trigger,
  input  [31:0] Row_0,
  input  [31:0] Row_1,
  input  [31:0] Row_2,
  input  [31:0] Row_3,
  input  [31:0] Row_4,
  input  [31:0] Row_5,
  input  [31:0] Row_6,
  input  [31:0] Row_7,
  input  [31:0] Row_8,
  input  [31:0] Row_9,
  input  [31:0] Row_10,
  input  [31:0] Row_11,
  input  [31:0] Row_12,
  input  [31:0] Row_13,
  input  [31:0] Row_14,
  input  [31:0] Row_15,
  input  [31:0] Row_16,
  input  [31:0] Row_17,
  input  [31:0] Row_18,
  input  [31:0] Row_19,
  input  [31:0] Row_20,
  input  [31:0] Row_21,
  input  [31:0] Row_22,
  input  [31:0] Row_23,
  input  [31:0] Row_24,
  input  [31:0] Row_25,
  input  [31:0] Row_26,
  input  [31:0] Row_27,
  input  [31:0] Row_28,
  input  [31:0] Row_29,
  input  [31:0] Row_30,
  input  [31:0] Row_31,
  output [31:0] Row_0_2,
  output [31:0] Row_1_2,
  output [31:0] Row_2_2,
  output [31:0] Row_3_2,
  output [31:0] Row_4_2,
  output [31:0] Row_5_2,
  output [31:0] Row_6_2,
  output [31:0] Row_7_2,
  output [31:0] Row_8_2,
  output [31:0] Row_9_2,
  output [31:0] Row_10_2,
  output [31:0] Row_11_2,
  output [31:0] Row_12_2,
  output [31:0] Row_13_2,
  output [31:0] Row_14_2,
  output [31:0] Row_15_2,
  output [31:0] Row_16_2,
  output [31:0] Row_17_2,
  output [31:0] Row_18_2,
  output [31:0] Row_19_2,
  output [31:0] Row_20_2,
  output [31:0] Row_21_2,
  output [31:0] Row_22_2,
  output [31:0] Row_23_2,
  output [31:0] Row_24_2,
  output [31:0] Row_25_2,
  output [31:0] Row_26_2,
  output [31:0] Row_27_2,
  output [31:0] Row_28_2,
  output [31:0] Row_29_2,
  output [31:0] Row_30_2,
  output [31:0] Row_31_2
);

  Register #(.width(32)) register_1 (.D(Row_0), .Q(Row_0_2), .clk(Save_generation_trigger));  // open: en, clr
  Register #(.width(32)) register_2 (.D(Row_1), .Q(Row_1_2), .clk(Save_generation_trigger));  // open: en, clr
  Register #(.width(32)) register_3 (.D(Row_2), .Q(Row_2_2), .clk(Save_generation_trigger));  // open: en, clr
  Register #(.width(32)) register_4 (.D(Row_3), .Q(Row_3_2), .clk(Save_generation_trigger));  // open: en, clr
  Register #(.width(32)) register_5 (.D(Row_4), .Q(Row_4_2), .clk(Save_generation_trigger));  // open: en, clr
  Register #(.width(32)) register_6 (.D(Row_5), .Q(Row_5_2), .clk(Save_generation_trigger));  // open: en, clr
  Register #(.width(32)) register_7 (.D(Row_6), .Q(Row_6_2), .clk(Save_generation_trigger));  // open: en, clr
  Register #(.width(32)) register_8 (.D(Row_7), .Q(Row_7_2), .clk(Save_generation_trigger));  // open: en, clr
  Register #(.width(32)) register_9 (.D(Row_8), .Q(Row_8_2), .clk(Save_generation_trigger));  // open: en, clr
  Register #(.width(32)) register_10 (.D(Row_9), .Q(Row_9_2), .clk(Save_generation_trigger));  // open: en, clr
  Register #(.width(32)) register_11 (.D(Row_10), .Q(Row_10_2), .clk(Save_generation_trigger));  // open: en, clr
  Register #(.width(32)) register_12 (.D(Row_11), .Q(Row_11_2), .clk(Save_generation_trigger));  // open: en, clr
  Register #(.width(32)) register_13 (.D(Row_12), .Q(Row_12_2), .clk(Save_generation_trigger));  // open: en, clr
  Register #(.width(32)) register_14 (.D(Row_13), .Q(Row_13_2), .clk(Save_generation_trigger));  // open: en, clr
  Register #(.width(32)) register_15 (.D(Row_14), .Q(Row_14_2), .clk(Save_generation_trigger));  // open: en, clr
  Register #(.width(32)) register_16 (.D(Row_15), .Q(Row_15_2), .clk(Save_generation_trigger));  // open: en, clr
  Register #(.width(32)) register_17 (.D(Row_16), .Q(Row_16_2), .clk(Save_generation_trigger));  // open: en, clr
  Register #(.width(32)) register_18 (.D(Row_17), .Q(Row_17_2), .clk(Save_generation_trigger));  // open: en, clr
  Register #(.width(32)) register_19 (.D(Row_18), .Q(Row_18_2), .clk(Save_generation_trigger));  // open: en, clr
  Register #(.width(32)) register_20 (.D(Row_19), .Q(Row_19_2), .clk(Save_generation_trigger));  // open: en, clr
  Register #(.width(32)) register_21 (.D(Row_20), .Q(Row_20_2), .clk(Save_generation_trigger));  // open: en, clr
  Register #(.width(32)) register_22 (.D(Row_21), .Q(Row_21_2), .clk(Save_generation_trigger));  // open: en, clr
  Register #(.width(32)) register_23 (.D(Row_22), .Q(Row_22_2), .clk(Save_generation_trigger));  // open: en, clr
  Register #(.width(32)) register_24 (.D(Row_23), .Q(Row_23_2), .clk(Save_generation_trigger));  // open: en, clr
  Register #(.width(32)) register_25 (.D(Row_24), .Q(Row_24_2), .clk(Save_generation_trigger));  // open: en, clr
  Register #(.width(32)) register_26 (.D(Row_25), .Q(Row_25_2), .clk(Save_generation_trigger));  // open: en, clr
  Register #(.width(32)) register_27 (.D(Row_26), .Q(Row_26_2), .clk(Save_generation_trigger));  // open: en, clr
  Register #(.width(32)) register_28 (.D(Row_27), .Q(Row_27_2), .clk(Save_generation_trigger));  // open: en, clr
  Register #(.width(32)) register_29 (.D(Row_28), .Q(Row_28_2), .clk(Save_generation_trigger));  // open: en, clr
  Register #(.width(32)) register_30 (.D(Row_29), .Q(Row_29_2), .clk(Save_generation_trigger));  // open: en, clr
  Register #(.width(32)) register_31 (.D(Row_30), .Q(Row_30_2), .clk(Save_generation_trigger));  // open: en, clr
  Register #(.width(32)) register_32 (.D(Row_31), .Q(Row_31_2), .clk(Save_generation_trigger));  // open: en, clr
endmodule

module Environment_data_constructor (
  input  [4:0] Y__row_index,
  input  [4:0] X__bit_index,
  input  [31:0] Row_0,
  input  [31:0] Row_1,
  input  [31:0] Row_2,
  input  [31:0] Row_3,
  input  [31:0] Row_4,
  input  [31:0] Row_5,
  input  [31:0] Row_6,
  input  [31:0] Row_7,
  input  [31:0] Row_8,
  input  [31:0] Row_9,
  input  [31:0] Row_10,
  input  [31:0] Row_11,
  input  [31:0] Row_12,
  input  [31:0] Row_13,
  input  [31:0] Row_14,
  input  [31:0] Row_15,
  input  [31:0] Row_16,
  input  [31:0] Row_17,
  input  [31:0] Row_18,
  input  [31:0] Row_19,
  input  [31:0] Row_20,
  input  [31:0] Row_21,
  input  [31:0] Row_22,
  input  [31:0] Row_23,
  input  [31:0] Row_24,
  input  [31:0] Row_25,
  input  [31:0] Row_26,
  input  [31:0] Row_27,
  input  [31:0] Row_28,
  input  [31:0] Row_29,
  input  [31:0] Row_30,
  input  [31:0] Row_31,
  output Is_row_env__null,
  output Is_byte_env__null,
  output [7:0] Sum,
  output Bit
);

  wire nor_1_out, nor_2_out, nor_3_out, nor_4_out, nor_5_out, nor_6_out, nor_7_out, nor_8_out, nor_9_out;
  wire [4:0] adder_1_out, adder_2_out, adder_3_out;
  wire [7:0] adder_4_out, adder_5_out, adder_6_out, adder_7_out, adder_8_out, adder_9_out, adder_10_out;
  wire [31:0] multiplexer_1_out, multiplexer_2_out, multiplexer_3_out, shifter_1_out, shifter_2_out,
       shifter_3_out;

  Adder #(.width(5)) adder_1 (.a({5{1'b1}}), .b(Y__row_index), .out(adder_1_out));  // open: cin, cout
  Adder #(.width(5)) adder_2 (.a(Y__row_index), .b(5'b00001), .out(adder_2_out));  // open: cin, cout
  Multiplexer #(.select(5), .width(32), .enable("false")) multiplexer_1 (
    .in0(Row_0), .in1(Row_1), .in2(Row_2), .in3(Row_3), .in4(Row_4), .in5(Row_5), .in6(Row_6), .in7(Row_7),
    .in8(Row_8), .in9(Row_9), .in10(Row_10), .in11(Row_11), .in12(Row_12), .in13(Row_13), .in14(Row_14),
    .in15(Row_15), .in16(Row_16), .in17(Row_17), .in18(Row_18), .in19(Row_19), .in20(Row_20), .in21(Row_21),
    .in22(Row_22), .in23(Row_23), .in24(Row_24), .in25(Row_25), .in26(Row_26), .in27(Row_27), .in28(Row_28),
    .in29(Row_29), .in30(Row_30), .in31(Row_31), .out(multiplexer_1_out), .sel(adder_1_out));
  Multiplexer #(.select(5), .width(32), .enable("false")) multiplexer_2 (
    .in0(Row_0), .in1(Row_1), .in2(Row_2), .in3(Row_3), .in4(Row_4), .in5(Row_5), .in6(Row_6), .in7(Row_7),
    .in8(Row_8), .in9(Row_9), .in10(Row_10), .in11(Row_11), .in12(Row_12), .in13(Row_13), .in14(Row_14),
    .in15(Row_15), .in16(Row_16), .in17(Row_17), .in18(Row_18), .in19(Row_19), .in20(Row_20), .in21(Row_21),
    .in22(Row_22), .in23(Row_23), .in24(Row_24), .in25(Row_25), .in26(Row_26), .in27(Row_27), .in28(Row_28),
    .in29(Row_29), .in30(Row_30), .in31(Row_31), .out(multiplexer_2_out), .sel(Y__row_index));
  Multiplexer #(.select(5), .width(32), .enable("false")) multiplexer_3 (
    .in0(Row_0), .in1(Row_1), .in2(Row_2), .in3(Row_3), .in4(Row_4), .in5(Row_5), .in6(Row_6), .in7(Row_7),
    .in8(Row_8), .in9(Row_9), .in10(Row_10), .in11(Row_11), .in12(Row_12), .in13(Row_13), .in14(Row_14),
    .in15(Row_15), .in16(Row_16), .in17(Row_17), .in18(Row_18), .in19(Row_19), .in20(Row_20), .in21(Row_21),
    .in22(Row_22), .in23(Row_23), .in24(Row_24), .in25(Row_25), .in26(Row_26), .in27(Row_27), .in28(Row_28),
    .in29(Row_29), .in30(Row_30), .in31(Row_31), .out(multiplexer_3_out), .sel(adder_2_out));
  // Probe on adder_3_out
  Adder #(.width(5)) adder_3 (.a(X__bit_index), .b({5{1'b1}}), .out(adder_3_out));  // open: cin, cout
  Adder adder_4 (.a({8{1'b0}}), .b({8{1'b0}}), .out(adder_4_out), .cin(shifter_3_out[2]));  // open: cout
  Shifter #(.width(32), .shift("rr")) shifter_1 (.in(multiplexer_1_out), .\dist (adder_3_out), .out(shifter_1_out));
  Shifter #(.width(32), .shift("rr")) shifter_2 (
    .in(multiplexer_2_out), .\dist (adder_3_out), .out({shifter_2_out[31:2], Bit, shifter_2_out[0]}));
  Shifter #(.width(32), .shift("rr")) shifter_3 (.in(multiplexer_3_out), .\dist (adder_3_out), .out(shifter_3_out));
  Adder adder_5 (.a({8{1'b0}}), .b(adder_4_out), .out(adder_5_out), .cin(shifter_3_out[1]));  // open: cout
  Adder adder_6 (.a(adder_5_out), .b({8{1'b0}}), .out(adder_6_out), .cin(shifter_3_out[0]));  // open: cout
  Adder adder_7 (.a({8{1'b0}}), .b(adder_6_out), .out(adder_7_out), .cin(shifter_2_out[2]));  // open: cout
  Adder adder_8 (.a(adder_7_out), .b({8{1'b0}}), .out(adder_8_out), .cin(shifter_2_out[0]));  // open: cout
  Adder adder_9 (.a({8{1'b0}}), .b(adder_8_out), .out(adder_9_out), .cin(shifter_1_out[2]));  // open: cout
  nor nor_1 (nor_1_out, shifter_1_out[31], shifter_1_out[30], shifter_1_out[29], shifter_1_out[28], shifter_1_out[27], shifter_1_out[26], shifter_1_out[25], shifter_1_out[24], shifter_1_out[23], shifter_1_out[22], shifter_1_out[21], shifter_1_out[20], shifter_1_out[19], shifter_1_out[18], shifter_1_out[17], shifter_1_out[16], shifter_1_out[14], shifter_1_out[13], shifter_1_out[12], shifter_1_out[11], shifter_1_out[10], shifter_1_out[9], shifter_1_out[8], shifter_1_out[7], shifter_1_out[6], shifter_1_out[5], shifter_1_out[4], shifter_1_out[3], shifter_1_out[2], shifter_1_out[1], shifter_1_out[0], shifter_1_out[15]);
  nor nor_2 (nor_2_out, shifter_2_out[31], shifter_2_out[30], shifter_2_out[29], shifter_2_out[28], shifter_2_out[27], shifter_2_out[26], shifter_2_out[25], shifter_2_out[24], shifter_2_out[23], shifter_2_out[22], shifter_2_out[21], shifter_2_out[20], shifter_2_out[19], shifter_2_out[18], shifter_2_out[17], shifter_2_out[16], shifter_2_out[14], shifter_2_out[13], shifter_2_out[12], shifter_2_out[11], shifter_2_out[10], shifter_2_out[9], shifter_2_out[8], shifter_2_out[7], shifter_2_out[6], shifter_2_out[5], shifter_2_out[4], shifter_2_out[3], shifter_2_out[2], Bit, shifter_2_out[0], shifter_2_out[15]);
  nor nor_3 (nor_3_out, shifter_3_out[31], shifter_3_out[30], shifter_3_out[29], shifter_3_out[28], shifter_3_out[27], shifter_3_out[26], shifter_3_out[25], shifter_3_out[24], shifter_3_out[23], shifter_3_out[22], shifter_3_out[21], shifter_3_out[20], shifter_3_out[19], shifter_3_out[18], shifter_3_out[17], shifter_3_out[16], shifter_3_out[14], shifter_3_out[13], shifter_3_out[12], shifter_3_out[11], shifter_3_out[10], shifter_3_out[9], shifter_3_out[8], shifter_3_out[7], shifter_3_out[6], shifter_3_out[5], shifter_3_out[4], shifter_3_out[3], shifter_3_out[2], shifter_3_out[1], shifter_3_out[0], shifter_3_out[15]);
  Adder adder_10 (.a(adder_9_out), .b({8{1'b0}}), .out(adder_10_out), .cin(shifter_1_out[1]));  // open: cout
  Adder adder_11 (.a({8{1'b0}}), .b(adder_10_out), .out(Sum), .cin(shifter_1_out[0]));  // open: cout
  and and_1 (Is_row_env__null, nor_1_out, nor_2_out, nor_3_out);
  nor nor_4 (nor_4_out, shifter_1_out[31], shifter_1_out[30], shifter_1_out[29], shifter_1_out[28], shifter_1_out[27], shifter_1_out[26], shifter_1_out[25]);
  nor nor_5 (nor_5_out, shifter_2_out[31], shifter_2_out[30], shifter_2_out[29], shifter_2_out[28], shifter_2_out[27], shifter_2_out[26], shifter_2_out[25]);
  nor nor_6 (nor_6_out, shifter_3_out[31], shifter_3_out[30], shifter_3_out[29], shifter_3_out[28], shifter_3_out[27], shifter_3_out[26], shifter_3_out[25]);
  nor nor_7 (nor_7_out, shifter_1_out[2], shifter_1_out[1], shifter_1_out[0]);
  nor nor_8 (nor_8_out, shifter_2_out[2], Bit, shifter_2_out[0]);
  nor nor_9 (nor_9_out, shifter_3_out[2], shifter_3_out[1], shifter_3_out[0]);
  and and_2 (Is_byte_env__null, nor_7_out, nor_4_out, nor_8_out, nor_5_out, nor_9_out, nor_6_out);

  // Other names for the same wires on the sheet: row0[31:0] = Row_0; row1[31:0] = Row_1; row2[31:0] = Row_2;
  //   row3[31:0] = Row_3; row4[31:0] = Row_4; row5[31:0] = Row_5; row6[31:0] = Row_6; row7[31:0] = Row_7;
  //   row8[31:0] = Row_8; row9[31:0] = Row_9; row10[31:0] = Row_10; row11[31:0] = Row_11; row12[31:0] = Row_12;
  //   row13[31:0] = Row_13; row14[31:0] = Row_14; row15[31:0] = Row_15; row16[31:0] = Row_16; row17[31:0] = Row_17;
  //   row18[31:0] = Row_18; row19[31:0] = Row_19; row20[31:0] = Row_20; row21[31:0] = Row_21; row22[31:0] = Row_22;
  //   row23[31:0] = Row_23; row24[31:0] = Row_24; row25[31:0] = Row_25; row26[31:0] = Row_26; row27[31:0] = Row_27;
  //   row28[31:0] = Row_28; row29[31:0] = Row_29; row30[31:0] = Row_30; row31[31:0] = Row_31
endmodule

module Row_s_bit_invertor (
  input  [4:0] Y__row_index,
  input  [4:0] X__bit_index,
  input  [31:0] Row_0,
  input  [31:0] Row_1,
  input  [31:0] Row_2,
  input  [31:0] Row_3,
  input  [31:0] Row_4,
  input  [31:0] Row_5,
  input  [31:0] Row_6,
  input  [31:0] Row_7,
  input  [31:0] Row_8,
  input  [31:0] Row_9,
  input  [31:0] Row_10,
  input  [31:0] Row_11,
  input  [31:0] Row_12,
  input  [31:0] Row_13,
  input  [31:0] Row_14,
  input  [31:0] Row_15,
  input  [31:0] Row_16,
  input  [31:0] Row_17,
  input  [31:0] Row_18,
  input  [31:0] Row_19,
  input  [31:0] Row_20,
  input  [31:0] Row_21,
  input  [31:0] Row_22,
  input  [31:0] Row_23,
  input  [31:0] Row_24,
  input  [31:0] Row_25,
  input  [31:0] Row_26,
  input  [31:0] Row_27,
  input  [31:0] Row_28,
  input  [31:0] Row_29,
  input  [31:0] Row_30,
  input  [31:0] Row_31,
  output [31:0] Row_with_inverted_bit
);

  wire [31:0] decoder_1_out0, multiplexer_1_out;

  Multiplexer #(.select(5), .width(32), .enable("false")) multiplexer_1 (
    .in0(Row_0), .in1(Row_1), .in2(Row_2), .in3(Row_3), .in4(Row_4), .in5(Row_5), .in6(Row_6), .in7(Row_7),
    .in8(Row_8), .in9(Row_9), .in10(Row_10), .in11(Row_11), .in12(Row_12), .in13(Row_13), .in14(Row_14),
    .in15(Row_15), .in16(Row_16), .in17(Row_17), .in18(Row_18), .in19(Row_19), .in20(Row_20), .in21(Row_21),
    .in22(Row_22), .in23(Row_23), .in24(Row_24), .in25(Row_25), .in26(Row_26), .in27(Row_27), .in28(Row_28),
    .in29(Row_29), .in30(Row_30), .in31(Row_31), .out(multiplexer_1_out), .sel(Y__row_index));
  Decoder #(.select(5), .disabled(0), .enable("false")) decoder_1 (
    .out0(decoder_1_out0[0]), .out1(decoder_1_out0[1]), .out2(decoder_1_out0[2]), .out3(decoder_1_out0[3]),
    .out4(decoder_1_out0[4]), .out5(decoder_1_out0[5]), .out6(decoder_1_out0[6]), .out7(decoder_1_out0[7]),
    .out8(decoder_1_out0[8]), .out9(decoder_1_out0[9]), .out10(decoder_1_out0[10]),
    .out11(decoder_1_out0[11]), .out12(decoder_1_out0[12]), .out13(decoder_1_out0[13]),
    .out14(decoder_1_out0[14]), .out15(decoder_1_out0[15]), .out16(decoder_1_out0[16]),
    .out17(decoder_1_out0[17]), .out18(decoder_1_out0[18]), .out19(decoder_1_out0[19]),
    .out20(decoder_1_out0[20]), .out21(decoder_1_out0[21]), .out22(decoder_1_out0[22]),
    .out23(decoder_1_out0[23]), .out24(decoder_1_out0[24]), .out25(decoder_1_out0[25]),
    .out26(decoder_1_out0[26]), .out27(decoder_1_out0[27]), .out28(decoder_1_out0[28]),
    .out29(decoder_1_out0[29]), .out30(decoder_1_out0[30]), .out31(decoder_1_out0[31]), .sel(X__bit_index));
  // Probe on decoder_1_out0
  assign Row_with_inverted_bit = decoder_1_out0 ^ multiplexer_1_out;  // XOR_Gate xor_1, 32 bits wide

  // Other names for the same wires on the sheet: row0[31:0] = Row_0; row1[31:0] = Row_1; row2[31:0] = Row_2;
  //   row3[31:0] = Row_3; row4[31:0] = Row_4; row5[31:0] = Row_5; row6[31:0] = Row_6; row7[31:0] = Row_7;
  //   row8[31:0] = Row_8; row9[31:0] = Row_9; row10[31:0] = Row_10; row11[31:0] = Row_11; row12[31:0] = Row_12;
  //   row13[31:0] = Row_13; row14[31:0] = Row_14; row15[31:0] = Row_15; row16[31:0] = Row_16; row17[31:0] = Row_17;
  //   row18[31:0] = Row_18; row19[31:0] = Row_19; row20[31:0] = Row_20; row21[31:0] = Row_21; row22[31:0] = Row_22;
  //   row23[31:0] = Row_23; row24[31:0] = Row_24; row25[31:0] = Row_25; row26[31:0] = Row_26; row27[31:0] = Row_27;
  //   row28[31:0] = Row_28; row29[31:0] = Row_29; row30[31:0] = Row_30; row31[31:0] = Row_31
endmodule

module Binary_selector (
  input  [31:0] input1,
  input  switch,
  input  [31:0] input2,
  output [31:0] \output 
);

  Multiplexer #(.width(32), .enable("false")) multiplexer_1 (.in0(input1), .in1(input2), .out(\output ), .sel(switch));
endmodule

module Blinker (
  input  [31:0] input0,
  input  [31:0] input1,
  input  [31:0] input2,
  input  [31:0] input3,
  input  [31:0] input4,
  input  [31:0] input5,
  input  [31:0] input6,
  input  [31:0] input7,
  input  [31:0] input8,
  input  [31:0] input9,
  input  [31:0] input10,
  input  [31:0] input11,
  input  [31:0] input12,
  input  [31:0] input13,
  input  [31:0] input14,
  input  [31:0] input15,
  input  [31:0] input16,
  input  [31:0] input17,
  input  [31:0] input18,
  input  [31:0] input19,
  input  [31:0] input20,
  input  [31:0] input21,
  input  [31:0] input22,
  input  [31:0] input23,
  input  [31:0] input24,
  input  [31:0] input25,
  input  [31:0] input26,
  input  [31:0] input27,
  input  [31:0] input28,
  input  [31:0] input29,
  input  [31:0] input30,
  input  [31:0] input31,
  input  [4:0] X,
  input  [4:0] Y,
  input  SWITCH,
  output [31:0] changed_string,
  output [31:0] output0,
  output [31:0] output1,
  output [31:0] output2,
  output [31:0] output3,
  output [31:0] output4,
  output [31:0] output5,
  output [31:0] output6,
  output [31:0] output7,
  output [31:0] output8,
  output [31:0] output9,
  output [31:0] output10,
  output [31:0] output11,
  output [31:0] output12,
  output [31:0] output13,
  output [31:0] output14,
  output [31:0] output15,
  output [31:0] output16,
  output [31:0] output17,
  output [31:0] output18,
  output [31:0] output19,
  output [31:0] output20,
  output [31:0] output21,
  output [31:0] output22,
  output [31:0] output23,
  output [31:0] output24,
  output [31:0] output25,
  output [31:0] output26,
  output [31:0] output27,
  output [31:0] output28,
  output [31:0] output29,
  output [31:0] output30,
  output [31:0] output31
);

  wire decoder_2_out0, decoder_2_out1, decoder_2_out2, decoder_2_out3, decoder_2_out4, decoder_2_out5,
       decoder_2_out6, decoder_2_out7, decoder_2_out8, decoder_2_out9, decoder_2_out10, decoder_2_out11,
       decoder_2_out12, decoder_2_out13, decoder_2_out14, decoder_2_out15, decoder_2_out16, decoder_2_out17,
       decoder_2_out18, decoder_2_out19, decoder_2_out20, decoder_2_out21, decoder_2_out22, decoder_2_out23,
       decoder_2_out24, decoder_2_out25, decoder_2_out26, decoder_2_out27, decoder_2_out28, decoder_2_out29,
       decoder_2_out30, decoder_2_out31;
  wire [31:0] binary_selector_2_output, binary_selector_4_output, binary_selector_6_output,
       binary_selector_8_output, binary_selector_10_output, binary_selector_12_output,
       binary_selector_14_output, binary_selector_16_output, binary_selector_18_output,
       binary_selector_20_output, binary_selector_22_output, binary_selector_24_output,
       binary_selector_26_output, binary_selector_28_output, binary_selector_30_output,
       binary_selector_32_output, binary_selector_34_output, binary_selector_36_output,
       binary_selector_38_output, binary_selector_40_output, binary_selector_42_output,
       binary_selector_44_output, binary_selector_46_output, binary_selector_48_output,
       binary_selector_50_output, binary_selector_52_output, binary_selector_54_output,
       binary_selector_56_output, binary_selector_58_output, binary_selector_60_output,
       binary_selector_62_output, binary_selector_64_output, decoder_1_out0, multiplexer_1_out, STRING;

  Multiplexer #(.select(5), .width(32), .disabled(0), .enable("false")) multiplexer_1 (
    .in0(input0), .in1(input1), .in2(input2), .in3(input3), .in4(input4), .in5(input5), .in6(input6),
    .in7(input7), .in8(input8), .in9(input9), .in10(input10), .in11(input11), .in12(input12), .in13(input13),
    .in14(input14), .in15(input15), .in16(input16), .in17(input17), .in18(input18), .in19(input19),
    .in20(input20), .in21(input21), .in22(input22), .in23(input23), .in24(input24), .in25(input25),
    .in26(input26), .in27(input27), .in28(input28), .in29(input29), .in30(input30), .in31(input31),
    .out(multiplexer_1_out), .sel(Y));
  Decoder #(.select(5), .disabled(0)) decoder_1 (
    .out0(decoder_1_out0[0]), .out1(decoder_1_out0[1]), .out2(decoder_1_out0[2]), .out3(decoder_1_out0[3]),
    .out4(decoder_1_out0[4]), .out5(decoder_1_out0[5]), .out6(decoder_1_out0[6]), .out7(decoder_1_out0[7]),
    .out8(decoder_1_out0[8]), .out9(decoder_1_out0[9]), .out10(decoder_1_out0[10]),
    .out11(decoder_1_out0[11]), .out12(decoder_1_out0[12]), .out13(decoder_1_out0[13]),
    .out14(decoder_1_out0[14]), .out15(decoder_1_out0[15]), .out16(decoder_1_out0[16]),
    .out17(decoder_1_out0[17]), .out18(decoder_1_out0[18]), .out19(decoder_1_out0[19]),
    .out20(decoder_1_out0[20]), .out21(decoder_1_out0[21]), .out22(decoder_1_out0[22]),
    .out23(decoder_1_out0[23]), .out24(decoder_1_out0[24]), .out25(decoder_1_out0[25]),
    .out26(decoder_1_out0[26]), .out27(decoder_1_out0[27]), .out28(decoder_1_out0[28]),
    .out29(decoder_1_out0[29]), .out30(decoder_1_out0[30]), .out31(decoder_1_out0[31]), .sel(X), .en(SWITCH));
  assign STRING = multiplexer_1_out ^ decoder_1_out0;  // XOR_Gate xor_1, 32 bits wide
  Binary_selector binary_selector_1 (
    .input1(multiplexer_1_out), .switch(SWITCH), .input2(STRING), .\output (changed_string));
  Binary_selector binary_selector_2 (
    .input1(input0), .switch(decoder_2_out0), .input2(STRING), .\output (binary_selector_2_output));
  Binary_selector binary_selector_3 (
    .input1(input0), .switch(SWITCH), .input2(binary_selector_2_output), .\output (output0));
  Binary_selector binary_selector_4 (
    .input1(input1), .switch(decoder_2_out1), .input2(STRING), .\output (binary_selector_4_output));
  Binary_selector binary_selector_5 (
    .input1(input1), .switch(SWITCH), .input2(binary_selector_4_output), .\output (output1));
  Binary_selector binary_selector_6 (
    .input1(input2), .switch(decoder_2_out2), .input2(STRING), .\output (binary_selector_6_output));
  Binary_selector binary_selector_7 (
    .input1(input2), .switch(SWITCH), .input2(binary_selector_6_output), .\output (output2));
  Binary_selector binary_selector_8 (
    .input1(input3), .switch(decoder_2_out3), .input2(STRING), .\output (binary_selector_8_output));
  Binary_selector binary_selector_9 (
    .input1(input3), .switch(SWITCH), .input2(binary_selector_8_output), .\output (output3));
  Binary_selector binary_selector_10 (
    .input1(input4), .switch(decoder_2_out4), .input2(STRING), .\output (binary_selector_10_output));
  Binary_selector binary_selector_11 (
    .input1(input4), .switch(SWITCH), .input2(binary_selector_10_output), .\output (output4));
  Binary_selector binary_selector_12 (
    .input1(input5), .switch(decoder_2_out5), .input2(STRING), .\output (binary_selector_12_output));
  Binary_selector binary_selector_13 (
    .input1(input5), .switch(SWITCH), .input2(binary_selector_12_output), .\output (output5));
  Binary_selector binary_selector_14 (
    .input1(input6), .switch(decoder_2_out6), .input2(STRING), .\output (binary_selector_14_output));
  Binary_selector binary_selector_15 (
    .input1(input6), .switch(SWITCH), .input2(binary_selector_14_output), .\output (output6));
  Binary_selector binary_selector_16 (
    .input1(input7), .switch(decoder_2_out7), .input2(STRING), .\output (binary_selector_16_output));
  Binary_selector binary_selector_17 (
    .input1(input7), .switch(SWITCH), .input2(binary_selector_16_output), .\output (output7));
  Binary_selector binary_selector_18 (
    .input1(input8), .switch(decoder_2_out8), .input2(STRING), .\output (binary_selector_18_output));
  Binary_selector binary_selector_19 (
    .input1(input8), .switch(SWITCH), .input2(binary_selector_18_output), .\output (output8));
  Binary_selector binary_selector_20 (
    .input1(input9), .switch(decoder_2_out9), .input2(STRING), .\output (binary_selector_20_output));
  Binary_selector binary_selector_21 (
    .input1(input9), .switch(SWITCH), .input2(binary_selector_20_output), .\output (output9));
  Binary_selector binary_selector_22 (
    .input1(input10), .switch(decoder_2_out10), .input2(STRING), .\output (binary_selector_22_output));
  Binary_selector binary_selector_23 (
    .input1(input10), .switch(SWITCH), .input2(binary_selector_22_output), .\output (output10));
  Binary_selector binary_selector_24 (
    .input1(input11), .switch(decoder_2_out11), .input2(STRING), .\output (binary_selector_24_output));
  Binary_selector binary_selector_25 (
    .input1(input11), .switch(SWITCH), .input2(binary_selector_24_output), .\output (output11));
  Binary_selector binary_selector_26 (
    .input1(input12), .switch(decoder_2_out12), .input2(STRING), .\output (binary_selector_26_output));
  Binary_selector binary_selector_27 (
    .input1(input12), .switch(SWITCH), .input2(binary_selector_26_output), .\output (output12));
  Binary_selector binary_selector_28 (
    .input1(input13), .switch(decoder_2_out13), .input2(STRING), .\output (binary_selector_28_output));
  Binary_selector binary_selector_29 (
    .input1(input13), .switch(SWITCH), .input2(binary_selector_28_output), .\output (output13));
  Binary_selector binary_selector_30 (
    .input1(input14), .switch(decoder_2_out14), .input2(STRING), .\output (binary_selector_30_output));
  Binary_selector binary_selector_31 (
    .input1(input14), .switch(SWITCH), .input2(binary_selector_30_output), .\output (output14));
  Decoder #(.select(5), .disabled(0)) decoder_2 (
    .out0(decoder_2_out0), .out1(decoder_2_out1), .out2(decoder_2_out2), .out3(decoder_2_out3),
    .out4(decoder_2_out4), .out5(decoder_2_out5), .out6(decoder_2_out6), .out7(decoder_2_out7),
    .out8(decoder_2_out8), .out9(decoder_2_out9), .out10(decoder_2_out10), .out11(decoder_2_out11),
    .out12(decoder_2_out12), .out13(decoder_2_out13), .out14(decoder_2_out14), .out15(decoder_2_out15),
    .out16(decoder_2_out16), .out17(decoder_2_out17), .out18(decoder_2_out18), .out19(decoder_2_out19),
    .out20(decoder_2_out20), .out21(decoder_2_out21), .out22(decoder_2_out22), .out23(decoder_2_out23),
    .out24(decoder_2_out24), .out25(decoder_2_out25), .out26(decoder_2_out26), .out27(decoder_2_out27),
    .out28(decoder_2_out28), .out29(decoder_2_out29), .out30(decoder_2_out30), .out31(decoder_2_out31),
    .sel(Y), .en(SWITCH));
  Binary_selector binary_selector_32 (
    .input1(input15), .switch(decoder_2_out15), .input2(STRING), .\output (binary_selector_32_output));
  Binary_selector binary_selector_33 (
    .input1(input15), .switch(SWITCH), .input2(binary_selector_32_output), .\output (output15));
  Binary_selector binary_selector_34 (
    .input1(input16), .switch(decoder_2_out16), .input2(STRING), .\output (binary_selector_34_output));
  Binary_selector binary_selector_35 (
    .input1(input16), .switch(SWITCH), .input2(binary_selector_34_output), .\output (output16));
  Binary_selector binary_selector_36 (
    .input1(input17), .switch(decoder_2_out17), .input2(STRING), .\output (binary_selector_36_output));
  Binary_selector binary_selector_37 (
    .input1(input17), .switch(SWITCH), .input2(binary_selector_36_output), .\output (output17));
  Binary_selector binary_selector_38 (
    .input1(input18), .switch(decoder_2_out18), .input2(STRING), .\output (binary_selector_38_output));
  Binary_selector binary_selector_39 (
    .input1(input18), .switch(SWITCH), .input2(binary_selector_38_output), .\output (output18));
  Binary_selector binary_selector_40 (
    .input1(input19), .switch(decoder_2_out19), .input2(STRING), .\output (binary_selector_40_output));
  Binary_selector binary_selector_41 (
    .input1(input19), .switch(SWITCH), .input2(binary_selector_40_output), .\output (output19));
  Binary_selector binary_selector_42 (
    .input1(input20), .switch(decoder_2_out20), .input2(STRING), .\output (binary_selector_42_output));
  Binary_selector binary_selector_43 (
    .input1(input20), .switch(SWITCH), .input2(binary_selector_42_output), .\output (output20));
  Binary_selector binary_selector_44 (
    .input1(input21), .switch(decoder_2_out21), .input2(STRING), .\output (binary_selector_44_output));
  Binary_selector binary_selector_45 (
    .input1(input21), .switch(SWITCH), .input2(binary_selector_44_output), .\output (output21));
  Binary_selector binary_selector_46 (
    .input1(input22), .switch(decoder_2_out22), .input2(STRING), .\output (binary_selector_46_output));
  Binary_selector binary_selector_47 (
    .input1(input22), .switch(SWITCH), .input2(binary_selector_46_output), .\output (output22));
  Binary_selector binary_selector_48 (
    .input1(input23), .switch(decoder_2_out23), .input2(STRING), .\output (binary_selector_48_output));
  Binary_selector binary_selector_49 (
    .input1(input23), .switch(SWITCH), .input2(binary_selector_48_output), .\output (output23));
  Binary_selector binary_selector_50 (
    .input1(input24), .switch(decoder_2_out24), .input2(STRING), .\output (binary_selector_50_output));
  Binary_selector binary_selector_51 (
    .input1(input24), .switch(SWITCH), .input2(binary_selector_50_output), .\output (output24));
  Binary_selector binary_selector_52 (
    .input1(input25), .switch(decoder_2_out25), .input2(STRING), .\output (binary_selector_52_output));
  Binary_selector binary_selector_53 (
    .input1(input25), .switch(SWITCH), .input2(binary_selector_52_output), .\output (output25));
  Binary_selector binary_selector_54 (
    .input1(input26), .switch(decoder_2_out26), .input2(STRING), .\output (binary_selector_54_output));
  Binary_selector binary_selector_55 (
    .input1(input26), .switch(SWITCH), .input2(binary_selector_54_output), .\output (output26));
  Binary_selector binary_selector_56 (
    .input1(input27), .switch(decoder_2_out27), .input2(STRING), .\output (binary_selector_56_output));
  Binary_selector binary_selector_57 (
    .input1(input27), .switch(SWITCH), .input2(binary_selector_56_output), .\output (output27));
  Binary_selector binary_selector_58 (
    .input1(input28), .switch(decoder_2_out28), .input2(STRING), .\output (binary_selector_58_output));
  Binary_selector binary_selector_59 (
    .input1(input28), .switch(SWITCH), .input2(binary_selector_58_output), .\output (output28));
  Binary_selector binary_selector_60 (
    .input1(input29), .switch(decoder_2_out29), .input2(STRING), .\output (binary_selector_60_output));
  Binary_selector binary_selector_61 (
    .input1(input29), .switch(SWITCH), .input2(binary_selector_60_output), .\output (output29));
  Binary_selector binary_selector_62 (
    .input1(input30), .switch(decoder_2_out30), .input2(STRING), .\output (binary_selector_62_output));
  Binary_selector binary_selector_63 (
    .input1(input30), .switch(SWITCH), .input2(binary_selector_62_output), .\output (output30));
  Binary_selector binary_selector_64 (
    .input1(input31), .switch(decoder_2_out31), .input2(STRING), .\output (binary_selector_64_output));
  Binary_selector binary_selector_65 (
    .input1(input31), .switch(SWITCH), .input2(binary_selector_64_output), .\output (output31));
endmodule

module engine_debug_version (
  input  [7:0] birth_input,
  input  [7:0] survival_input
);

  wire and_1_out, and_2_out, and_3_out, and_4_out, and_5_out, and_6_out, and_7_out, and_10_out, and_11_out,
       and_12_out, and_13_out, and_14_out, cdm_8_mark5_1_p1, cdm_8_mark5_1_p2, cdm_8_mark5_1_p4,
       cdm_8_mark5_1_p5, cdm_8_mark5_1_p6, cdm_8_mark5_1_p7, cdm_8_mark5_1_p8, cdm_8_mark5_1_p9, change_bit,
       change_bit_slow, clock, code, comparator_1_eq, comparator_2_eq, comparator_3_eq, comparator_4_eq,
       comparator_5_eq, comparator_6_eq, comparator_7_eq, comparator_8_eq, comparator_9_eq, comparator_10_eq,
       comparator_11_lt, comparator_12_eq, comparator_13_eq, comparator_14_eq, comparator_15_eq,
       comparator_16_eq, CPU_invert_bit, CPU_invert_bit_slow, data, decoder_1_out0, decoder_3_out0,
       decoder_4_out1, decoder_6_out0, decoder_7_out1, decoder_9_out1, decoder_10_out1, decoder_11_out1,
       decoder_12_out1, decoder_13_out1, in_out, IOsel, is_null_byte, is_row_null, mem, multiplexer_1_out,
       multiplexer_4_out, not_1_out, not_3_out, not_4_out, not_5_out, not_6_out, not_7_out, not_8_out,
       not_9_out, not_10_out, not_12_out, not_13_out, not_15_out, not_16_out, not_17_out, not_18_out,
       not_19_out, not_21_out, not_22_out, not_23_out, not_24_out, not_25_out, not_26_out, not_28_out,
       not_29_out, not_30_out, not_31_out, playing, RAM, selected_bit, setting, start, update_generation,
       update_generation_slow, xnor_1_out, xnor_2_out, xnor_3_out;
  wire [4:0] cpuX, cpuY, keyboard_controller_1_x, keyboard_controller_1_y, multiplexer_2_out,
       multiplexer_3_out;
  wire [6:0] keyboard_1_data;
  wire [7:0] bus, cdm_8_mark5_1_p13, cdm_8_mark5_1_p14, controlled_buffer_1_out, controlled_buffer_3_out,
       env_sum, IOaddr, not_27_out, register_1_q, register_5_q, register_6_q;
  wire [7:1] register_3_q;
  wire [7:5] register_2_q, register_4_q;
  wire [31:0] blinker_1_output0, blinker_1_output1, blinker_1_output2, blinker_1_output3, blinker_1_output4,
       blinker_1_output5, blinker_1_output6, blinker_1_output7, blinker_1_output8, blinker_1_output9,
       blinker_1_output10, blinker_1_output11, blinker_1_output12, blinker_1_output13, blinker_1_output14,
       blinker_1_output15, blinker_1_output16, blinker_1_output17, blinker_1_output18, blinker_1_output19,
       blinker_1_output20, blinker_1_output21, blinker_1_output22, blinker_1_output23, blinker_1_output24,
       blinker_1_output25, blinker_1_output26, blinker_1_output27, blinker_1_output28, blinker_1_output29,
       blinker_1_output30, blinker_1_output31, inverted_row, random_write_buffer_1_row_0,
       random_write_buffer_1_row_1, random_write_buffer_1_row_2, random_write_buffer_1_row_3,
       random_write_buffer_1_row_4, random_write_buffer_1_row_5, random_write_buffer_1_row_6,
       random_write_buffer_1_row_7, random_write_buffer_1_row_8, random_write_buffer_1_row_9,
       random_write_buffer_1_row_10, random_write_buffer_1_row_11, random_write_buffer_1_row_12,
       random_write_buffer_1_row_13, random_write_buffer_1_row_14, random_write_buffer_1_row_15,
       random_write_buffer_1_row_16, random_write_buffer_1_row_17, random_write_buffer_1_row_18,
       random_write_buffer_1_row_19, random_write_buffer_1_row_20, random_write_buffer_1_row_21,
       random_write_buffer_1_row_22, random_write_buffer_1_row_23, random_write_buffer_1_row_24,
       random_write_buffer_1_row_25, random_write_buffer_1_row_26, random_write_buffer_1_row_27,
       random_write_buffer_1_row_28, random_write_buffer_1_row_29, random_write_buffer_1_row_30,
       random_write_buffer_1_row_31, stable_generation_s_buffer_1_row_0_2,
       stable_generation_s_buffer_1_row_1_2, stable_generation_s_buffer_1_row_2_2,
       stable_generation_s_buffer_1_row_3_2, stable_generation_s_buffer_1_row_4_2,
       stable_generation_s_buffer_1_row_5_2, stable_generation_s_buffer_1_row_6_2,
       stable_generation_s_buffer_1_row_7_2, stable_generation_s_buffer_1_row_8_2,
       stable_generation_s_buffer_1_row_9_2, stable_generation_s_buffer_1_row_10_2,
       stable_generation_s_buffer_1_row_11_2, stable_generation_s_buffer_1_row_12_2,
       stable_generation_s_buffer_1_row_13_2, stable_generation_s_buffer_1_row_14_2,
       stable_generation_s_buffer_1_row_15_2, stable_generation_s_buffer_1_row_16_2,
       stable_generation_s_buffer_1_row_17_2, stable_generation_s_buffer_1_row_18_2,
       stable_generation_s_buffer_1_row_19_2, stable_generation_s_buffer_1_row_20_2,
       stable_generation_s_buffer_1_row_21_2, stable_generation_s_buffer_1_row_22_2,
       stable_generation_s_buffer_1_row_23_2, stable_generation_s_buffer_1_row_24_2,
       stable_generation_s_buffer_1_row_25_2, stable_generation_s_buffer_1_row_26_2,
       stable_generation_s_buffer_1_row_27_2, stable_generation_s_buffer_1_row_28_2,
       stable_generation_s_buffer_1_row_29_2, stable_generation_s_buffer_1_row_30_2,
       stable_generation_s_buffer_1_row_31_2;

  Keyboard keyboard_1 (.clk(clock), .re(setting), .data(keyboard_1_data));  // open: clr, avail
  Button u_Start (.out(start));
  Keyboard_controller keyboard_controller_1 (
    .ASCII_code(keyboard_1_data), .X(keyboard_controller_1_x), .Y(keyboard_controller_1_y),
    .Switch(change_bit));
  // Probe on keyboard_controller_1_y
  // Probe on keyboard_controller_1_x
  not not_1 (not_1_out, change_bit);
  not not_2 (change_bit_slow, not_1_out);
  not not_3 (not_3_out, not_3_out);
  not not_4 (not_4_out, not_4_out);
  not not_5 (not_5_out, not_5_out);
  not not_6 (not_6_out, not_6_out);
  Multiplexer #(.disabled(0), .enable("false")) multiplexer_1 (
    .in0(change_bit), .in1(CPU_invert_bit), .out(multiplexer_1_out), .sel(playing));
  // Probe on multiplexer_2_out
  Multiplexer #(.width(5), .disabled(0), .enable("false")) multiplexer_2 (
    .in0(cpuY), .in1(keyboard_controller_1_y), .out(multiplexer_2_out), .sel(setting));
  Multiplexer #(.width(5), .disabled(0), .enable("false")) multiplexer_3 (
    .in0(keyboard_controller_1_x), .in1(cpuX), .out(multiplexer_3_out), .sel(playing));
  // Probe on multiplexer_3_out
  not not_7 (not_7_out, start);
  Random_write_buffer random_write_buffer_1 (
    .Row_0(random_write_buffer_1_row_0), .Row_1(random_write_buffer_1_row_1),
    .Row_2(random_write_buffer_1_row_2), .Row_3(random_write_buffer_1_row_3),
    .Row_4(random_write_buffer_1_row_4), .Row_5(random_write_buffer_1_row_5),
    .Row_6(random_write_buffer_1_row_6), .Row_7(random_write_buffer_1_row_7),
    .Row_8(random_write_buffer_1_row_8), .Row_9(random_write_buffer_1_row_9),
    .Row_10(random_write_buffer_1_row_10), .Row_11(random_write_buffer_1_row_11),
    .Row_12(random_write_buffer_1_row_12), .Row_13(random_write_buffer_1_row_13),
    .Row_14(random_write_buffer_1_row_14), .Row_15(random_write_buffer_1_row_15),
    .Row_16(random_write_buffer_1_row_16), .Row_17(random_write_buffer_1_row_17),
    .Row_18(random_write_buffer_1_row_18), .Row_19(random_write_buffer_1_row_19),
    .Row_20(random_write_buffer_1_row_20), .Row_21(random_write_buffer_1_row_21),
    .Row_22(random_write_buffer_1_row_22), .Row_23(random_write_buffer_1_row_23),
    .Row_24(random_write_buffer_1_row_24), .Row_25(random_write_buffer_1_row_25),
    .Row_26(random_write_buffer_1_row_26), .Row_27(random_write_buffer_1_row_27),
    .Row_28(random_write_buffer_1_row_28), .Row_29(random_write_buffer_1_row_29),
    .Row_30(random_write_buffer_1_row_30), .Row_31(random_write_buffer_1_row_31),
    .Row_selector(multiplexer_2_out), .Write_row(multiplexer_1_out), .Input_row(inverted_row));
  Register register_1 (.D(bus), .Q(register_1_q), .clk(not_8_out));  // open: en, clr
  not not_8 (not_8_out, not_9_out);
  not not_9 (not_9_out, decoder_1_out0);
  not not_10 (not_10_out, CPU_invert_bit);
  not not_11 (CPU_invert_bit_slow, not_10_out);
  assign controlled_buffer_1_out = decoder_3_out0 ? bus : 8'bz;  // Controlled_Buffer controlled_buffer_1
  Register register_2 (.D(controlled_buffer_1_out), .Q({register_2_q, cpuY}), .clk(not_12_out));  // open: en, clr
  not not_12 (not_12_out, not_13_out);
  Register register_3 (.D(8'h1), .Q({register_3_q, playing}), .clk(xnor_1_out));  // open: en, clr
  xnor xnor_1 (xnor_1_out, not_7_out, start);
  Decoder #(.disabled(0)) decoder_1 (.out0(decoder_1_out0), .sel(in_out), .en(and_1_out));  // open: out1
  Decoder #(.disabled(0)) decoder_2 (.out0(CPU_invert_bit), .sel(in_out), .en(and_2_out));  // open: out1
  Decoder #(.disabled(0)) decoder_3 (.out0(decoder_3_out0), .sel(in_out), .en(and_3_out));  // open: out1
  not not_13 (not_13_out, decoder_3_out0);
  Decoder #(.disabled(0)) decoder_4 (.out1(decoder_4_out1), .sel(in_out), .en(and_4_out));  // open: out0
  assign bus = decoder_4_out1 ? {register_3_q, playing} : 8'bz;  // Controlled_Buffer controlled_buffer_2
  Row_s_bit_invertor row_s_bit_invertor_1 (
    .Row_0(random_write_buffer_1_row_0), .Row_1(random_write_buffer_1_row_1),
    .Row_2(random_write_buffer_1_row_2), .Row_3(random_write_buffer_1_row_3),
    .Row_4(random_write_buffer_1_row_4), .Row_5(random_write_buffer_1_row_5),
    .Row_6(random_write_buffer_1_row_6), .Row_7(random_write_buffer_1_row_7),
    .Row_8(random_write_buffer_1_row_8), .Row_9(random_write_buffer_1_row_9),
    .Row_10(random_write_buffer_1_row_10), .Row_11(random_write_buffer_1_row_11),
    .Row_12(random_write_buffer_1_row_12), .Row_13(random_write_buffer_1_row_13),
    .Row_14(random_write_buffer_1_row_14), .Row_15(random_write_buffer_1_row_15),
    .Row_16(random_write_buffer_1_row_16), .Row_17(random_write_buffer_1_row_17),
    .Row_18(random_write_buffer_1_row_18), .Row_19(random_write_buffer_1_row_19),
    .Row_20(random_write_buffer_1_row_20), .Row_21(random_write_buffer_1_row_21),
    .Row_22(random_write_buffer_1_row_22), .Row_23(random_write_buffer_1_row_23),
    .Row_24(random_write_buffer_1_row_24), .Row_25(random_write_buffer_1_row_25),
    .Row_26(random_write_buffer_1_row_26), .Row_27(random_write_buffer_1_row_27),
    .Row_28(random_write_buffer_1_row_28), .Row_29(random_write_buffer_1_row_29),
    .Row_30(random_write_buffer_1_row_30), .Row_31(random_write_buffer_1_row_31),
    .Row_with_inverted_bit(inverted_row), .Y__row_index(multiplexer_2_out), .X__bit_index(multiplexer_3_out));
  Comparator comparator_1 (.a(IOaddr), .b({8{1'b1}}), .eq(comparator_1_eq));  // open: gt, lt
  and and_1 (and_1_out, comparator_1_eq, IOsel);
  Comparator comparator_2 (.a(IOaddr), .b(8'hf9), .eq(comparator_2_eq));  // open: gt, lt
  and and_2 (and_2_out, comparator_2_eq, IOsel);
  Comparator comparator_3 (.a(IOaddr), .b(8'hf3), .eq(comparator_3_eq));  // open: gt, lt
  and and_3 (and_3_out, comparator_3_eq, IOsel);
  Comparator comparator_4 (.a(IOaddr), .b(8'hf0), .eq(comparator_4_eq));  // open: gt, lt
  and and_4 (and_4_out, comparator_4_eq, IOsel);
  not not_14 (setting, playing);
  not not_15 (not_15_out, not_15_out);
  // Probe on inverted_row
  not not_16 (not_16_out, not_16_out);
  not not_17 (not_17_out, not_17_out);
  LED led_1 (.in(comparator_5_eq));
  Comparator comparator_5 (.a(8'h40), .b(register_1_q), .eq(comparator_5_eq));  // open: gt, lt
  LED led_2 (.in(comparator_6_eq));
  Comparator comparator_6 (.a(8'h41), .b(register_1_q), .eq(comparator_6_eq));  // open: gt, lt
  Comparator comparator_7 (.a(8'h42), .b(register_1_q), .eq(comparator_7_eq));  // open: gt, lt
  not not_18 (not_18_out, setting);
  LED led_3 (.in(comparator_7_eq));
  assign controlled_buffer_3_out = decoder_6_out0 ? bus : 8'bz;  // Controlled_Buffer controlled_buffer_3
  xnor xnor_2 (xnor_2_out, not_18_out, setting);
  not not_19 (not_19_out, update_generation);
  not not_20 (update_generation_slow, not_19_out);
  Register register_4 (.D(controlled_buffer_3_out), .Q({register_4_q, cpuX}), .clk(not_21_out));  // open: en, clr
  not not_21 (not_21_out, not_22_out);
  not not_22 (not_22_out, decoder_6_out0);
  assign bus = decoder_7_out1 ? register_5_q : 8'bz;  // Controlled_Buffer controlled_buffer_4
  Register register_5 (.D(birth_input), .Q(register_5_q), .clk(xnor_2_out));  // open: en, clr
  Stable_generation_s_buffer stable_generation_s_buffer_1 (
    .Save_generation_trigger(multiplexer_4_out), .Row_0(random_write_buffer_1_row_0),
    .Row_1(random_write_buffer_1_row_1), .Row_2(random_write_buffer_1_row_2),
    .Row_3(random_write_buffer_1_row_3), .Row_4(random_write_buffer_1_row_4),
    .Row_5(random_write_buffer_1_row_5), .Row_6(random_write_buffer_1_row_6),
    .Row_7(random_write_buffer_1_row_7), .Row_8(random_write_buffer_1_row_8),
    .Row_9(random_write_buffer_1_row_9), .Row_10(random_write_buffer_1_row_10),
    .Row_11(random_write_buffer_1_row_11), .Row_12(random_write_buffer_1_row_12),
    .Row_13(random_write_buffer_1_row_13), .Row_14(random_write_buffer_1_row_14),
    .Row_15(random_write_buffer_1_row_15), .Row_16(random_write_buffer_1_row_16),
    .Row_17(random_write_buffer_1_row_17), .Row_18(random_write_buffer_1_row_18),
    .Row_19(random_write_buffer_1_row_19), .Row_20(random_write_buffer_1_row_20),
    .Row_21(random_write_buffer_1_row_21), .Row_22(random_write_buffer_1_row_22),
    .Row_23(random_write_buffer_1_row_23), .Row_24(random_write_buffer_1_row_24),
    .Row_25(random_write_buffer_1_row_25), .Row_26(random_write_buffer_1_row_26),
    .Row_27(random_write_buffer_1_row_27), .Row_28(random_write_buffer_1_row_28),
    .Row_29(random_write_buffer_1_row_29), .Row_30(random_write_buffer_1_row_30),
    .Row_31(random_write_buffer_1_row_31), .Row_0_2(stable_generation_s_buffer_1_row_0_2),
    .Row_1_2(stable_generation_s_buffer_1_row_1_2), .Row_2_2(stable_generation_s_buffer_1_row_2_2),
    .Row_3_2(stable_generation_s_buffer_1_row_3_2), .Row_4_2(stable_generation_s_buffer_1_row_4_2),
    .Row_5_2(stable_generation_s_buffer_1_row_5_2), .Row_6_2(stable_generation_s_buffer_1_row_6_2),
    .Row_7_2(stable_generation_s_buffer_1_row_7_2), .Row_8_2(stable_generation_s_buffer_1_row_8_2),
    .Row_9_2(stable_generation_s_buffer_1_row_9_2), .Row_10_2(stable_generation_s_buffer_1_row_10_2),
    .Row_11_2(stable_generation_s_buffer_1_row_11_2), .Row_12_2(stable_generation_s_buffer_1_row_12_2),
    .Row_13_2(stable_generation_s_buffer_1_row_13_2), .Row_14_2(stable_generation_s_buffer_1_row_14_2),
    .Row_15_2(stable_generation_s_buffer_1_row_15_2), .Row_16_2(stable_generation_s_buffer_1_row_16_2),
    .Row_17_2(stable_generation_s_buffer_1_row_17_2), .Row_18_2(stable_generation_s_buffer_1_row_18_2),
    .Row_19_2(stable_generation_s_buffer_1_row_19_2), .Row_20_2(stable_generation_s_buffer_1_row_20_2),
    .Row_21_2(stable_generation_s_buffer_1_row_21_2), .Row_22_2(stable_generation_s_buffer_1_row_22_2),
    .Row_23_2(stable_generation_s_buffer_1_row_23_2), .Row_24_2(stable_generation_s_buffer_1_row_24_2),
    .Row_25_2(stable_generation_s_buffer_1_row_25_2), .Row_26_2(stable_generation_s_buffer_1_row_26_2),
    .Row_27_2(stable_generation_s_buffer_1_row_27_2), .Row_28_2(stable_generation_s_buffer_1_row_28_2),
    .Row_29_2(stable_generation_s_buffer_1_row_29_2), .Row_30_2(stable_generation_s_buffer_1_row_30_2),
    .Row_31_2(stable_generation_s_buffer_1_row_31_2));
  Multiplexer #(.disabled(0), .enable("false")) multiplexer_4 (
    .in0(clock), .in1(update_generation), .out(multiplexer_4_out), .sel(playing));
  Decoder #(.disabled(0)) decoder_5 (.out0(update_generation), .sel(in_out), .en(and_5_out));  // open: out1
  Decoder #(.disabled(0)) decoder_6 (.out0(decoder_6_out0), .sel(in_out), .en(and_6_out));  // open: out1
  Decoder #(.disabled(0)) decoder_7 (.out1(decoder_7_out1), .sel(in_out), .en(and_7_out));  // open: out0
  Comparator comparator_8 (.a(IOaddr), .b(8'hfa), .eq(comparator_8_eq));  // open: gt, lt
  and and_5 (and_5_out, comparator_8_eq, IOsel);
  Comparator comparator_9 (.a(IOaddr), .b(8'hf4), .eq(comparator_9_eq));  // open: gt, lt
  and and_6 (and_6_out, comparator_9_eq, IOsel);
  Comparator comparator_10 (.a(IOaddr), .b(8'hf1), .eq(comparator_10_eq));  // open: gt, lt
  and and_7 (and_7_out, comparator_10_eq, IOsel);
  // Probe on cdm_8_mark5_1_p1
  // Probe on cdm_8_mark5_1_p4
  // Probe on cdm_8_mark5_1_p2
  Clock clock_1 (.out(clock));
  and and_8 (IOsel, not_25_out, clock, data);
  not not_23 (not_23_out, not_23_out);
  not not_24 (not_24_out, not_24_out);
  Environment_data_constructor environment_data_constructor_1 (
    .Row_0(stable_generation_s_buffer_1_row_0_2), .Row_1(stable_generation_s_buffer_1_row_1_2),
    .Row_2(stable_generation_s_buffer_1_row_2_2), .Row_3(stable_generation_s_buffer_1_row_3_2),
    .Row_4(stable_generation_s_buffer_1_row_4_2), .Row_5(stable_generation_s_buffer_1_row_5_2),
    .Row_6(stable_generation_s_buffer_1_row_6_2), .Row_7(stable_generation_s_buffer_1_row_7_2),
    .Row_8(stable_generation_s_buffer_1_row_8_2), .Row_9(stable_generation_s_buffer_1_row_9_2),
    .Row_10(stable_generation_s_buffer_1_row_10_2), .Row_11(stable_generation_s_buffer_1_row_11_2),
    .Row_12(stable_generation_s_buffer_1_row_12_2), .Row_13(stable_generation_s_buffer_1_row_13_2),
    .Row_14(stable_generation_s_buffer_1_row_14_2), .Row_15(stable_generation_s_buffer_1_row_15_2),
    .Row_16(stable_generation_s_buffer_1_row_16_2), .Row_17(stable_generation_s_buffer_1_row_17_2),
    .Row_18(stable_generation_s_buffer_1_row_18_2), .Row_19(stable_generation_s_buffer_1_row_19_2),
    .Row_20(stable_generation_s_buffer_1_row_20_2), .Row_21(stable_generation_s_buffer_1_row_21_2),
    .Row_22(stable_generation_s_buffer_1_row_22_2), .Row_23(stable_generation_s_buffer_1_row_23_2),
    .Row_24(stable_generation_s_buffer_1_row_24_2), .Row_25(stable_generation_s_buffer_1_row_25_2),
    .Row_26(stable_generation_s_buffer_1_row_26_2), .Row_27(stable_generation_s_buffer_1_row_27_2),
    .Row_28(stable_generation_s_buffer_1_row_28_2), .Row_29(stable_generation_s_buffer_1_row_29_2),
    .Row_30(stable_generation_s_buffer_1_row_30_2), .Row_31(stable_generation_s_buffer_1_row_31_2),
    .Is_byte_env__null(is_null_byte), .Y__row_index(multiplexer_2_out), .X__bit_index(multiplexer_3_out),
    .Is_row_env__null(is_row_null), .Sum(env_sum), .Bit(selected_bit));
  // Probe on cdm_8_mark5_1_p5
  // Probe on cdm_8_mark5_1_p6
  // Probe on cdm_8_mark5_1_p8
  // Probe on cdm_8_mark5_1_p7
  not not_25 (not_25_out, comparator_11_lt);
  // CdM_8_mark5 cdm_8_mark5_1: pin names not known; wires that end beside it: cdm_8_mark5_1_p1, cdm_8_mark5_1_p2, clock, cdm_8_mark5_1_p4, cdm_8_mark5_1_p5, cdm_8_mark5_1_p6, cdm_8_mark5_1_p7, cdm_8_mark5_1_p8, cdm_8_mark5_1_p9, mem, in_out, IOaddr, cdm_8_mark5_1_p13, cdm_8_mark5_1_p14
  assign bus = not_26_out ? cdm_8_mark5_1_p13 : 8'bz;  // Controlled_Buffer controlled_buffer_5
  not not_26 (not_26_out, in_out);
  assign cdm_8_mark5_1_p14 = in_out ? bus : 8'bz;  // Controlled_Buffer controlled_buffer_6
  and and_9 (RAM, comparator_11_lt, data);
  assign not_27_out = ~survival_input;  // NOT_Gate not_27, 8 bits wide
  not not_28 (not_28_out, setting);
  LED led_4 (.in(selected_bit));
  // Probe on env_sum
  Decoder #(.disabled(0)) decoder_8 (.out0(code), .out1(data), .sel(cdm_8_mark5_1_p9), .en(mem));
  Register register_6 (.D(not_27_out), .Q(register_6_q), .clk(xnor_3_out));  // open: en, clr
  xnor xnor_3 (xnor_3_out, not_28_out, setting);
  // Probe on IOaddr
  Comparator #(.mode("unsigned")) comparator_11 (.a(IOaddr), .b(8'hf0), .lt(comparator_11_lt));  // open: gt, eq
  Decoder #(.disabled(0)) decoder_9 (.out1(decoder_9_out1), .sel(in_out), .en(and_10_out));  // open: out0
  assign bus = decoder_9_out1 ? {{7{1'b0}}, selected_bit} : 8'bz;  // Controlled_Buffer controlled_buffer_7
  Decoder #(.disabled(0)) decoder_10 (.out1(decoder_10_out1), .sel(in_out), .en(and_11_out));  // open: out0
  assign bus = decoder_10_out1 ? register_6_q : 8'bz;  // Controlled_Buffer controlled_buffer_8
  Blinker blinker_1 (
    .input0(stable_generation_s_buffer_1_row_0_2), .input1(stable_generation_s_buffer_1_row_1_2),
    .input2(stable_generation_s_buffer_1_row_2_2), .input3(stable_generation_s_buffer_1_row_3_2),
    .input4(stable_generation_s_buffer_1_row_4_2), .input5(stable_generation_s_buffer_1_row_5_2),
    .input6(stable_generation_s_buffer_1_row_6_2), .input7(stable_generation_s_buffer_1_row_7_2),
    .input8(stable_generation_s_buffer_1_row_8_2), .input9(stable_generation_s_buffer_1_row_9_2),
    .input10(stable_generation_s_buffer_1_row_10_2), .input11(stable_generation_s_buffer_1_row_11_2),
    .input12(stable_generation_s_buffer_1_row_12_2), .input13(stable_generation_s_buffer_1_row_13_2),
    .input14(stable_generation_s_buffer_1_row_14_2), .input15(stable_generation_s_buffer_1_row_15_2),
    .input16(stable_generation_s_buffer_1_row_16_2), .input17(stable_generation_s_buffer_1_row_17_2),
    .input18(stable_generation_s_buffer_1_row_18_2), .input19(stable_generation_s_buffer_1_row_19_2),
    .input20(stable_generation_s_buffer_1_row_20_2), .input21(stable_generation_s_buffer_1_row_21_2),
    .input22(stable_generation_s_buffer_1_row_22_2), .input23(stable_generation_s_buffer_1_row_23_2),
    .input24(stable_generation_s_buffer_1_row_24_2), .input25(stable_generation_s_buffer_1_row_25_2),
    .input26(stable_generation_s_buffer_1_row_26_2), .input27(stable_generation_s_buffer_1_row_27_2),
    .input28(stable_generation_s_buffer_1_row_28_2), .input29(stable_generation_s_buffer_1_row_29_2),
    .input30(stable_generation_s_buffer_1_row_30_2), .input31(stable_generation_s_buffer_1_row_31_2),
    .X(multiplexer_3_out), .Y(multiplexer_2_out), .SWITCH(clock), .output0(blinker_1_output0),
    .output1(blinker_1_output1), .output2(blinker_1_output2), .output3(blinker_1_output3),
    .output4(blinker_1_output4), .output5(blinker_1_output5), .output6(blinker_1_output6),
    .output7(blinker_1_output7), .output8(blinker_1_output8), .output9(blinker_1_output9),
    .output10(blinker_1_output10), .output11(blinker_1_output11), .output12(blinker_1_output12),
    .output13(blinker_1_output13), .output14(blinker_1_output14), .output15(blinker_1_output15),
    .output16(blinker_1_output16), .output17(blinker_1_output17), .output18(blinker_1_output18),
    .output19(blinker_1_output19), .output20(blinker_1_output20), .output21(blinker_1_output21),
    .output22(blinker_1_output22), .output23(blinker_1_output23), .output24(blinker_1_output24),
    .output25(blinker_1_output25), .output26(blinker_1_output26), .output27(blinker_1_output27),
    .output28(blinker_1_output28), .output29(blinker_1_output29), .output30(blinker_1_output30),
    .output31(blinker_1_output31));  // open: changed_string
  Comparator comparator_12 (.a(IOaddr), .b(8'hf5), .eq(comparator_12_eq));  // open: gt, lt
  and and_10 (and_10_out, comparator_12_eq, IOsel);
  Comparator comparator_13 (.a(IOaddr), .b(8'hf2), .eq(comparator_13_eq));  // open: gt, lt
  and and_11 (and_11_out, comparator_13_eq, IOsel);
  // Probe on bus
  ROM rom_1 (.addr(IOaddr), .data(bus), .sel(code));
  RAM ram_1 (.addr(IOaddr), .data(bus), .sel(RAM), .clk(clock), .ld(in_out));  // open: clr
  DotMatrix #(.inputtype("row"), .matrixcols(32), .matrixrows(32)) dotmatrix_1 (
    .row0(blinker_1_output0), .row1(blinker_1_output1), .row2(blinker_1_output2), .row3(blinker_1_output3),
    .row4(blinker_1_output4), .row5(blinker_1_output5), .row6(blinker_1_output6), .row7(blinker_1_output7),
    .row8(blinker_1_output8), .row9(blinker_1_output9), .row10(blinker_1_output10),
    .row11(blinker_1_output11), .row12(blinker_1_output12), .row13(blinker_1_output13),
    .row14(blinker_1_output14), .row15(blinker_1_output15), .row16(blinker_1_output16),
    .row17(blinker_1_output17), .row18(blinker_1_output18), .row19(blinker_1_output19),
    .row20(blinker_1_output20), .row21(blinker_1_output21), .row22(blinker_1_output22),
    .row23(blinker_1_output23), .row24(blinker_1_output24), .row25(blinker_1_output25),
    .row26(blinker_1_output26), .row27(blinker_1_output27), .row28(blinker_1_output28),
    .row29(blinker_1_output29), .row30(blinker_1_output30), .row31(blinker_1_output31));
  not not_29 (not_29_out, not_29_out);
  assign bus = decoder_11_out1 ? env_sum : 8'bz;  // Controlled_Buffer controlled_buffer_9
  Comparator comparator_14 (.a(IOaddr), .b(8'hf6), .eq(comparator_14_eq));  // open: gt, lt
  Decoder #(.disabled(0)) decoder_11 (.out1(decoder_11_out1), .sel(in_out), .en(and_12_out));  // open: out0
  and and_12 (and_12_out, comparator_14_eq, IOsel);
  not not_30 (not_30_out, not_30_out);
  assign bus = decoder_12_out1 ? {{7{1'b0}}, is_row_null} : 8'bz;  // Controlled_Buffer controlled_buffer_10
  Decoder #(.disabled(0)) decoder_12 (.out1(decoder_12_out1), .sel(in_out), .en(and_13_out));  // open: out0
  Comparator comparator_15 (.a(IOaddr), .b(8'hf7), .eq(comparator_15_eq));  // open: gt, lt
  and and_13 (and_13_out, comparator_15_eq, IOsel);
  not not_31 (not_31_out, not_31_out);
  assign bus = decoder_13_out1 ? {{7{1'b0}}, is_null_byte} : 8'bz;  // Controlled_Buffer controlled_buffer_11
  Comparator comparator_16 (.a(IOaddr), .b(8'hf8), .eq(comparator_16_eq));  // open: gt, lt
  Decoder #(.disabled(0)) decoder_13 (.out1(decoder_13_out1), .sel(in_out), .en(and_14_out));  // open: out0
  and and_14 (and_14_out, comparator_16_eq, IOsel);

  // Other names for the same wires on the sheet: birth_cond[7:0] = birth_input; IOdata[7:0] = bus; rd_wr = in_out;
  //   survival_cond[7:0] = survival_input

  // Notes on the sheet:
  //   Keyboard
  //   DEV I/O REGS.
  //   ROW READ / WRITE
  //   (read only thus CdM -> buffer)
  //   PROCESSED CELL
  //   READ ONLY INPUTS
  //   (immutable game state)
  //   Cell 0xff (CPU status)
  //   Cell 0xf3 (Y - row)
  //   Cell 0xf5 (invert signal)
  //   Cell 0xf0 (state)
  //   waiting for start
  //   reading field
  //   processing field
  //   Cell 0xf6 (update Stable generation's buffer)
  //   Cell 0xf4 (X - bit)
  //   Cell 0xf1 (birth conditions)
  //   Structure of I/O bus
  //   Cell 0xfa (bit value)
  //   Cell 0xf2 (survival conditions)
  //   Harvard Architecture
  //   Minimal IO cell address
  //   contents of rom_1 (hex, n*v repeats v):
  //   ee 35 d2 8 d1 0 18 a e0 11 88 b3 95 1d 8a ee 7 4 d7 d3 8 f e0 21 d2 1 42 a6 8d 98 8b ee 15 d7 5 e1
  //   29 d2 60 ee 2b d2 68 88 12 ba a e0 34 d0 f9 a0 d7 cd 50 d0 ff d1 40 a1 d1 f0 b4 0 e0 3e d1 50 a4 d1
  //   f1 b4 d1 60 d6 13 d1 f2 b4 d1 68 d6 13 d0 fa a0 d0 ff d1 42 a1 d3 1f c3 d0 f3 a3 d3 f7 bf f e1 9c d1
  //   1f d3 4 c3 d0 f4 a1 d0 f8 b0 0 e1 95 d3 8 c1 d0 f4 a1 d0 f6 b0 d1 f5 b5 0 e0 88 d6 22 ee 8e 5 e0 8e
  //   d0 f9 a0 c5 89 8b e1 77 ee 98 d0 f8 11 c7 8b e1 6b c7 8b e5 5d ee 53 d4
  //   Cell 0xfb (env. sum)
  //   Cell 0xfc (is null rows env.)
  //   Cell 0xfd (is null byte env.)
endmodule
