// Logisim project matrix.circ as structural Verilog
module _16_16_matrix (
  input  [7:0] Lo_byte,
  input  Lo_byte_on,
  input  [7:0] Hi_byte,
  input  Hi_byte_On,
  input  [7:0] Selector,
  input  Selection_On,
  input  Bus_0
);

  wire clk, demultiplexer_1_out0, demultiplexer_1_out1, demultiplexer_1_out2, demultiplexer_1_out3,
       demultiplexer_1_out4, demultiplexer_1_out5, demultiplexer_1_out6, demultiplexer_1_out7,
       demultiplexer_1_out8, demultiplexer_1_out9, demultiplexer_1_out10, demultiplexer_1_out11,
       demultiplexer_1_out12, demultiplexer_1_out13, demultiplexer_1_out14, demultiplexer_1_out15;
  wire [7:0] register_1_q, register_2_q, register_3_q;
  wire [15:0] register_4_q, register_5_q, register_6_q, register_7_q, register_8_q, register_9_q,
       register_10_q, register_11_q, register_12_q, register_13_q, register_14_q, register_15_q,
       register_16_q, register_17_q, register_18_q, register_19_q;

  Clock clock_1 (.out(clk));
  Register register_1 (.D(Lo_byte), .en(Lo_byte_on), .Q(register_1_q), .clk(clk));  // open: clr
  Register register_2 (.D(Hi_byte), .en(Hi_byte_On), .Q(register_2_q), .clk(clk));  // open: clr
  Register #(.trigger("high")) register_3 (.D(Selector), .en(Selection_On), .Q(register_3_q), .clk(clk));  // open: clr
  // Probe on register_3_q
  Demultiplexer #(.select(4), .disabled(0)) demultiplexer_1 (
    .out0(demultiplexer_1_out0), .out1(demultiplexer_1_out1), .out2(demultiplexer_1_out2),
    .out3(demultiplexer_1_out3), .out4(demultiplexer_1_out4), .out5(demultiplexer_1_out5),
    .out6(demultiplexer_1_out6), .out7(demultiplexer_1_out7), .out8(demultiplexer_1_out8),
    .out9(demultiplexer_1_out9), .out10(demultiplexer_1_out10), .out11(demultiplexer_1_out11),
    .out12(demultiplexer_1_out12), .out13(demultiplexer_1_out13), .out14(demultiplexer_1_out14),
    .out15(demultiplexer_1_out15), .in(Selection_On), .sel(register_3_q[3:0]), .en(Selection_On));
  Register #(.width(16)) register_4 (
    .D({register_2_q, register_1_q}), .en(demultiplexer_1_out0), .Q(register_4_q), .clk(clk));  // open: clr
  Register #(.width(16)) register_5 (
    .D({register_2_q, register_1_q}), .en(demultiplexer_1_out1), .Q(register_5_q), .clk(clk));  // open: clr
  Register #(.width(16)) register_6 (
    .D({register_2_q, register_1_q}), .en(demultiplexer_1_out2), .Q(register_6_q), .clk(clk));  // open: clr
  Register #(.width(16)) register_7 (
    .D({register_2_q, register_1_q}), .en(demultiplexer_1_out3), .Q(register_7_q), .clk(clk));  // open: clr
  Register #(.width(16)) register_8 (
    .D({register_2_q, register_1_q}), .en(demultiplexer_1_out4), .Q(register_8_q), .clk(clk));  // open: clr
  Register #(.width(16)) register_9 (
    .D({register_2_q, register_1_q}), .en(demultiplexer_1_out5), .Q(register_9_q), .clk(clk));  // open: clr
  Register #(.width(16)) register_10 (
    .D({register_2_q, register_1_q}), .en(demultiplexer_1_out6), .Q(register_10_q), .clk(clk));  // open: clr
  Register #(.width(16)) register_11 (
    .D({register_2_q, register_1_q}), .en(demultiplexer_1_out7), .Q(register_11_q), .clk(clk));  // open: clr
  Register #(.width(16)) register_12 (
    .D({register_2_q, register_1_q}), .en(demultiplexer_1_out8), .Q(register_12_q), .clk(clk));  // open: clr
  Register #(.width(16)) register_13 (
    .D({register_2_q, register_1_q}), .en(demultiplexer_1_out9), .Q(register_13_q), .clk(clk));  // open: clr
  Register #(.width(16)) register_14 (
    .D({register_2_q, register_1_q}), .en(demultiplexer_1_out10), .Q(register_14_q), .clk(clk));  // open: clr
  Register #(.width(16)) register_15 (
    .D({register_2_q, register_1_q}), .en(demultiplexer_1_out11), .Q(register_15_q), .clk(clk));  // open: clr
  Register #(.width(16)) register_16 (
    .D({register_2_q, register_1_q}), .en(demultiplexer_1_out12), .Q(register_16_q), .clk(clk));  // open: clr
  Register #(.width(16)) register_17 (
    .D({register_2_q, register_1_q}), .en(demultiplexer_1_out13), .Q(register_17_q), .clk(clk));  // open: clr
  Register #(.width(16)) register_18 (
    .D({register_2_q, register_1_q}), .en(demultiplexer_1_out14), .Q(register_18_q), .clk(clk));  // open: clr
  Register #(.width(16)) register_19 (
    .D({register_2_q, register_1_q}), .en(demultiplexer_1_out15), .Q(register_19_q), .clk(clk));  // open: clr
  DotMatrix #(.inputtype("row"), .matrixcols(16), .matrixrows(16)) dotmatrix_1 (
    .row0(register_4_q), .row1(register_5_q), .row2(register_6_q), .row3(register_7_q), .row4(register_8_q),
    .row5(register_9_q), .row6(register_10_q), .row7(register_11_q), .row8(register_12_q),
    .row9(register_13_q), .row10(register_14_q), .row11(register_15_q), .row12(register_16_q),
    .row13(register_17_q), .row14(register_18_q), .row15(register_19_q));
endmodule

module _16_16_demonstration (
  input  Full_On,
  input  Selection_On,
  input  Bus_0
);

  wire clk, demultiplexer_1_out0, demultiplexer_1_out1, demultiplexer_1_out2, demultiplexer_1_out3,
       demultiplexer_1_out4, demultiplexer_1_out5, demultiplexer_1_out6, demultiplexer_1_out7,
       demultiplexer_1_out8, demultiplexer_1_out9, demultiplexer_1_out10, demultiplexer_1_out11,
       demultiplexer_1_out12, demultiplexer_1_out13, demultiplexer_1_out14, demultiplexer_1_out15, rst;
  wire [3:0] random_1_out;
  wire [15:0] random_2_out, register_1_q, register_2_q, register_3_q, register_4_q, register_5_q,
       register_6_q, register_7_q, register_8_q, register_9_q, register_10_q, register_11_q, register_12_q,
       register_13_q, register_14_q, register_15_q, register_16_q;

  Clock clock_1 (.out(clk));
  Button Reset (.out(rst));
  Demultiplexer #(.select(4), .disabled(0)) demultiplexer_1 (
    .out0(demultiplexer_1_out0), .out1(demultiplexer_1_out1), .out2(demultiplexer_1_out2),
    .out3(demultiplexer_1_out3), .out4(demultiplexer_1_out4), .out5(demultiplexer_1_out5),
    .out6(demultiplexer_1_out6), .out7(demultiplexer_1_out7), .out8(demultiplexer_1_out8),
    .out9(demultiplexer_1_out9), .out10(demultiplexer_1_out10), .out11(demultiplexer_1_out11),
    .out12(demultiplexer_1_out12), .out13(demultiplexer_1_out13), .out14(demultiplexer_1_out14),
    .out15(demultiplexer_1_out15), .in(Selection_On), .sel(random_1_out), .en(Selection_On));
  Random #(.width(4)) random_1 (.clk(clk), .next(Full_On), .out(random_1_out), .clr(rst));
  Random #(.width(16), .seed(5)) random_2 (.clk(clk), .next(Full_On), .out(random_2_out), .clr(rst));
  Register #(.width(16)) register_1 (
    .D(random_2_out), .en(demultiplexer_1_out0), .Q(register_1_q), .clk(clk), .clr(rst));
  Register #(.width(16)) register_2 (
    .D(random_2_out), .en(demultiplexer_1_out1), .Q(register_2_q), .clk(clk), .clr(rst));
  Register #(.width(16)) register_3 (
    .D(random_2_out), .en(demultiplexer_1_out2), .Q(register_3_q), .clk(clk), .clr(rst));
  Register #(.width(16)) register_4 (
    .D(random_2_out), .en(demultiplexer_1_out3), .Q(register_4_q), .clk(clk), .clr(rst));
  Register #(.width(16)) register_5 (
    .D(random_2_out), .en(demultiplexer_1_out4), .Q(register_5_q), .clk(clk), .clr(rst));
  Register #(.width(16)) register_6 (
    .D(random_2_out), .en(demultiplexer_1_out5), .Q(register_6_q), .clk(clk), .clr(rst));
  Register #(.width(16)) register_7 (
    .D(random_2_out), .en(demultiplexer_1_out6), .Q(register_7_q), .clk(clk), .clr(rst));
  Register #(.width(16)) register_8 (
    .D(random_2_out), .en(demultiplexer_1_out7), .Q(register_8_q), .clk(clk), .clr(rst));
  Register #(.width(16)) register_9 (
    .D(random_2_out), .en(demultiplexer_1_out8), .Q(register_9_q), .clk(clk), .clr(rst));
  Register #(.width(16)) register_10 (
    .D(random_2_out), .en(demultiplexer_1_out9), .Q(register_10_q), .clk(clk), .clr(rst));
  Register #(.width(16)) register_11 (
    .D(random_2_out), .en(demultiplexer_1_out10), .Q(register_11_q), .clk(clk), .clr(rst));
  Register #(.width(16)) register_12 (
    .D(random_2_out), .en(demultiplexer_1_out11), .Q(register_12_q), .clk(clk), .clr(rst));
  Register #(.width(16)) register_13 (
    .D(random_2_out), .en(demultiplexer_1_out12), .Q(register_13_q), .clk(clk), .clr(rst));
  Register #(.width(16)) register_14 (
    .D(random_2_out), .en(demultiplexer_1_out13), .Q(register_14_q), .clk(clk), .clr(rst));
  Register #(.width(16)) register_15 (
    .D(random_2_out), .en(demultiplexer_1_out14), .Q(register_15_q), .clk(clk), .clr(rst));
  Register #(.width(16)) register_16 (
    .D(random_2_out), .en(demultiplexer_1_out15), .Q(register_16_q), .clk(clk), .clr(rst));
  DotMatrix #(.inputtype("row"), .matrixcols(16), .matrixrows(16)) dotmatrix_1 (
    .row0(register_1_q), .row1(register_2_q), .row2(register_3_q), .row3(register_4_q), .row4(register_5_q),
    .row5(register_6_q), .row6(register_7_q), .row7(register_8_q), .row8(register_9_q), .row9(register_10_q),
    .row10(register_11_q), .row11(register_12_q), .row12(register_13_q), .row13(register_14_q),
    .row14(register_15_q), .row15(register_16_q));

  // Other names for the same wires on the sheet: on = Full_On
endmodule

module _32_32_matrix (
  input  [7:0] _0_byte,
  input  _0_byte_on,
  input  [7:0] _1_byte,
  input  _1_byte_On,
  input  [7:0] _2_byte,
  input  _2_byte_on,
  input  [7:0] _3_byte,
  input  _3_byte_On,
  input  [7:0] Selector,
  input  Selection_On,
  input  Bus_0
);

  wire clk, demultiplexer_1_out0, demultiplexer_1_out1, demultiplexer_1_out2, demultiplexer_1_out3,
       demultiplexer_1_out4, demultiplexer_1_out5, demultiplexer_1_out6, demultiplexer_1_out7,
       demultiplexer_1_out8, demultiplexer_1_out9, demultiplexer_1_out10, demultiplexer_1_out11,
       demultiplexer_1_out12, demultiplexer_1_out13, demultiplexer_1_out14, demultiplexer_1_out15,
       demultiplexer_1_out16, demultiplexer_1_out17, demultiplexer_1_out18, demultiplexer_1_out19,
       demultiplexer_1_out20, demultiplexer_1_out21, demultiplexer_1_out22, demultiplexer_1_out23,
       demultiplexer_1_out24, demultiplexer_1_out25, demultiplexer_1_out26, demultiplexer_1_out27,
       demultiplexer_1_out28, demultiplexer_1_out29, demultiplexer_1_out30, demultiplexer_1_out31;
  wire [7:0] register_1_q, register_2_q, register_3_q, register_4_q, register_5_q;
  wire [31:0] register_6_q, register_7_q, register_8_q, register_9_q, register_10_q, register_11_q,
       register_12_q, register_13_q, register_14_q, register_15_q, register_16_q, register_17_q,
       register_18_q, register_19_q, register_20_q, register_21_q, register_22_q, register_23_q,
       register_24_q, register_25_q, register_26_q, register_27_q, register_28_q, register_29_q,
       register_30_q, register_31_q, register_32_q, register_33_q, register_34_q, register_35_q,
       register_36_q, register_37_q;

  Clock clock_1 (.out(clk));
  Register register_1 (.D(_0_byte), .en(_0_byte_on), .Q(register_1_q), .clk(clk));  // open: clr
  Register register_2 (.D(_1_byte), .en(_1_byte_On), .Q(register_2_q), .clk(clk));  // open: clr
  Register register_3 (.D(_2_byte), .en(_2_byte_on), .Q(register_3_q), .clk(clk));  // open: clr
  Register register_4 (.D(_3_byte), .en(_3_byte_On), .Q(register_4_q), .clk(clk));  // open: clr
  Register #(.trigger("high")) register_5 (.D(Selector), .en(Selection_On), .Q(register_5_q), .clk(clk));  // open: clr
  // Probe on register_5_q
  Demultiplexer #(.select(5), .disabled(0)) demultiplexer_1 (
    .out0(demultiplexer_1_out0), .out1(demultiplexer_1_out1), .out2(demultiplexer_1_out2),
    .out3(demultiplexer_1_out3), .out4(demultiplexer_1_out4), .out5(demultiplexer_1_out5),
    .out6(demultiplexer_1_out6), .out7(demultiplexer_1_out7), .out8(demultiplexer_1_out8),
    .out9(demultiplexer_1_out9), .out10(demultiplexer_1_out10), .out11(demultiplexer_1_out11),
    .out12(demultiplexer_1_out12), .out13(demultiplexer_1_out13), .out14(demultiplexer_1_out14),
    .out15(demultiplexer_1_out15), .out16(demultiplexer_1_out16), .out17(demultiplexer_1_out17),
    .out18(demultiplexer_1_out18), .out19(demultiplexer_1_out19), .out20(demultiplexer_1_out20),
    .out21(demultiplexer_1_out21), .out22(demultiplexer_1_out22), .out23(demultiplexer_1_out23),
    .out24(demultiplexer_1_out24), .out25(demultiplexer_1_out25), .out26(demultiplexer_1_out26),
    .out27(demultiplexer_1_out27), .out28(demultiplexer_1_out28), .out29(demultiplexer_1_out29),
    .out30(demultiplexer_1_out30), .out31(demultiplexer_1_out31), .in(Selection_On), .sel(register_5_q[4:0]));  // open: en
  Register #(.width(32)) register_6 (
    .D({register_4_q, register_3_q, register_2_q, register_1_q}), .en(demultiplexer_1_out0),
    .Q(register_6_q), .clk(clk));  // open: clr
  Register #(.width(32)) register_7 (
    .D({register_4_q, register_3_q, register_2_q, register_1_q}), .en(demultiplexer_1_out1),
    .Q(register_7_q), .clk(clk));  // open: clr
  Register #(.width(32)) register_8 (
    .D({register_4_q, register_3_q, register_2_q, register_1_q}), .en(demultiplexer_1_out2),
    .Q(register_8_q), .clk(clk));  // open: clr
  Register #(.width(32)) register_9 (
    .D({register_4_q, register_3_q, register_2_q, register_1_q}), .en(demultiplexer_1_out3),
    .Q(register_9_q), .clk(clk));  // open: clr
  Register #(.width(32)) register_10 (
    .D({register_4_q, register_3_q, register_2_q, register_1_q}), .en(demultiplexer_1_out4),
    .Q(register_10_q), .clk(clk));  // open: clr
  Register #(.width(32)) register_11 (
    .D({register_4_q, register_3_q, register_2_q, register_1_q}), .en(demultiplexer_1_out5),
    .Q(register_11_q), .clk(clk));  // open: clr
  Register #(.width(32)) register_12 (
    .D({register_4_q, register_3_q, register_2_q, register_1_q}), .en(demultiplexer_1_out6),
    .Q(register_12_q), .clk(clk));  // open: clr
  Register #(.width(32)) register_13 (
    .D({register_4_q, register_3_q, register_2_q, register_1_q}), .en(demultiplexer_1_out7),
    .Q(register_13_q), .clk(clk));  // open: clr
  Register #(.width(32)) register_14 (
    .D({register_4_q, register_3_q, register_2_q, register_1_q}), .en(demultiplexer_1_out8),
    .Q(register_14_q), .clk(clk));  // open: clr
  Register #(.width(32)) register_15 (
    .D({register_4_q, register_3_q, register_2_q, register_1_q}), .en(demultiplexer_1_out9),
    .Q(register_15_q), .clk(clk));  // open: clr
  Register #(.width(32)) register_16 (
    .D({register_4_q, register_3_q, register_2_q, register_1_q}), .en(demultiplexer_1_out10),
    .Q(register_16_q), .clk(clk));  // open: clr
  Register #(.width(32)) register_17 (
    .D({register_4_q, register_3_q, register_2_q, register_1_q}), .en(demultiplexer_1_out11),
    .Q(register_17_q), .clk(clk));  // open: clr
  Register #(.width(32)) register_18 (
    .D({register_4_q, register_3_q, register_2_q, register_1_q}), .en(demultiplexer_1_out12),
    .Q(register_18_q), .clk(clk));  // open: clr
  Register #(.width(32)) register_19 (
    .D({register_4_q, register_3_q, register_2_q, register_1_q}), .en(demultiplexer_1_out13),
    .Q(register_19_q), .clk(clk));  // open: clr
  Register #(.width(32)) register_20 (
    .D({register_4_q, register_3_q, register_2_q, register_1_q}), .en(demultiplexer_1_out14),
    .Q(register_20_q), .clk(clk));  // open: clr
  Register #(.width(32)) register_21 (
    .D({register_4_q, register_3_q, register_2_q, register_1_q}), .en(demultiplexer_1_out15),
    .Q(register_21_q), .clk(clk));  // open: clr
  Register #(.width(32)) register_22 (
    .D({register_4_q, register_3_q, register_2_q, register_1_q}), .en(demultiplexer_1_out16),
    .Q(register_22_q), .clk(clk));  // open: clr
  Register #(.width(32)) register_23 (
    .D({register_4_q, register_3_q, register_2_q, register_1_q}), .en(demultiplexer_1_out17),
    .Q(register_23_q), .clk(clk));  // open: clr
  Register #(.width(32)) register_24 (
    .D({register_4_q, register_3_q, register_2_q, register_1_q}), .en(demultiplexer_1_out18),
    .Q(register_24_q), .clk(clk));  // open: clr
  Register #(.width(32)) register_25 (
    .D({register_4_q, register_3_q, register_2_q, register_1_q}), .en(demultiplexer_1_out19),
    .Q(register_25_q), .clk(clk));  // open: clr
  Register #(.width(32)) register_26 (
    .D({register_4_q, register_3_q, register_2_q, register_1_q}), .en(demultiplexer_1_out20),
    .Q(register_26_q), .clk(clk));  // open: clr
  Register #(.width(32)) register_27 (
    .D({register_4_q, register_3_q, register_2_q, register_1_q}), .en(demultiplexer_1_out21),
    .Q(register_27_q), .clk(clk));  // open: clr
  Register #(.width(32)) register_28 (
    .D({register_4_q, register_3_q, register_2_q, register_1_q}), .en(demultiplexer_1_out22),
    .Q(register_28_q), .clk(clk));  // open: clr
  Register #(.width(32)) register_29 (
    .D({register_4_q, register_3_q, register_2_q, register_1_q}), .en(demultiplexer_1_out23),
    .Q(register_29_q), .clk(clk));  // open: clr
  Register #(.width(32)) register_30 (
    .D({register_4_q, register_3_q, register_2_q, register_1_q}), .en(demultiplexer_1_out24),
    .Q(register_30_q), .clk(clk));  // open: clr
  Register #(.width(32)) register_31 (
    .D({register_4_q, register_3_q, register_2_q, register_1_q}), .en(demultiplexer_1_out25),
    .Q(register_31_q), .clk(clk));  // open: clr
  Register #(.width(32)) register_32 (
    .D({register_4_q, register_3_q, register_2_q, register_1_q}), .en(demultiplexer_1_out26),
    .Q(register_32_q), .clk(clk));  // open: clr
  Register #(.width(32)) register_33 (
    .D({register_4_q, register_3_q, register_2_q, register_1_q}), .en(demultiplexer_1_out27),
    .Q(register_33_q), .clk(clk));  // open: clr
  Register #(.width(32)) register_34 (
    .D({register_4_q, register_3_q, register_2_q, register_1_q}), .en(demultiplexer_1_out28),
    .Q(register_34_q), .clk(clk));  // open: clr
  Register #(.width(32)) register_35 (
    .D({register_4_q, register_3_q, register_2_q, register_1_q}), .en(demultiplexer_1_out29),
    .Q(register_35_q), .clk(clk));  // open: clr
  Register #(.width(32)) register_36 (
    .D({register_4_q, register_3_q, register_2_q, register_1_q}), .en(demultiplexer_1_out30),
    .Q(register_36_q), .clk(clk));  // open: clr
  Register #(.width(32)) register_37 (
    .D({register_4_q, register_3_q, register_2_q, register_1_q}), .en(demultiplexer_1_out31),
    .Q(register_37_q), .clk(clk));  // open: clr
  DotMatrix #(.inputtype("row"), .matrixcols(32), .matrixrows(32)) dotmatrix_1 (
    .row0(register_6_q), .row1(register_7_q), .row2(register_8_q), .row3(register_9_q), .row4(register_10_q),
    .row5(register_11_q), .row6(register_12_q), .row7(register_13_q), .row8(register_14_q),
    .row9(register_15_q), .row10(register_16_q), .row11(register_17_q), .row12(register_18_q),
    .row13(register_19_q), .row14(register_20_q), .row15(register_21_q), .row16(register_22_q),
    .row17(register_23_q), .row18(register_24_q), .row19(register_25_q), .row20(register_26_q),
    .row21(register_27_q), .row22(register_28_q), .row23(register_29_q), .row24(register_30_q),
    .row25(register_31_q), .row26(register_32_q), .row27(register_33_q), .row28(register_34_q),
    .row29(register_35_q), .row30(register_36_q), .row31(register_37_q));
endmodule

module _32_32_demo (
  input  Full_On,
  input  Selection_On,
  input  Bus_0
);

  wire clk, decoder_1_out0, decoder_1_out1, decoder_1_out2, decoder_1_out3, decoder_1_out4, decoder_1_out5,
       decoder_1_out6, decoder_1_out7, decoder_1_out8, decoder_1_out9, decoder_1_out10, decoder_1_out11,
       decoder_1_out12, decoder_1_out13, decoder_1_out14, decoder_1_out15, decoder_1_out16, decoder_1_out17,
       decoder_1_out18, decoder_1_out19, decoder_1_out20, decoder_1_out21, decoder_1_out22, decoder_1_out23,
       decoder_1_out24, decoder_1_out25, decoder_1_out26, decoder_1_out27, decoder_1_out28, decoder_1_out29,
       decoder_1_out30, decoder_1_out31;
  wire [4:0] random_2_out;
  wire [31:0] random_1_out, register_1_q, register_2_q, register_3_q, register_4_q, register_5_q,
       register_6_q, register_7_q, register_8_q, register_9_q, register_10_q, register_11_q, register_12_q,
       register_13_q, register_14_q, register_15_q, register_16_q, register_17_q, register_18_q,
       register_19_q, register_20_q, register_21_q, register_22_q, register_23_q, register_24_q,
       register_25_q, register_26_q, register_27_q, register_28_q, register_29_q, register_30_q,
       register_31_q, register_32_q;

  Clock clock_1 (.out(clk));
  Random #(.width(32), .seed(5)) random_1 (.clk(clk), .next(Full_On), .out(random_1_out));  // open: clr
  Random #(.width(5)) random_2 (.clk(clk), .next(Full_On), .out(random_2_out));  // open: clr
  Decoder #(.select(5), .disabled(0)) decoder_1 (
    .out0(decoder_1_out0), .out1(decoder_1_out1), .out2(decoder_1_out2), .out3(decoder_1_out3),
    .out4(decoder_1_out4), .out5(decoder_1_out5), .out6(decoder_1_out6), .out7(decoder_1_out7),
    .out8(decoder_1_out8), .out9(decoder_1_out9), .out10(decoder_1_out10), .out11(decoder_1_out11),
    .out12(decoder_1_out12), .out13(decoder_1_out13), .out14(decoder_1_out14), .out15(decoder_1_out15),
    .out16(decoder_1_out16), .out17(decoder_1_out17), .out18(decoder_1_out18), .out19(decoder_1_out19),
    .out20(decoder_1_out20), .out21(decoder_1_out21), .out22(decoder_1_out22), .out23(decoder_1_out23),
    .out24(decoder_1_out24), .out25(decoder_1_out25), .out26(decoder_1_out26), .out27(decoder_1_out27),
    .out28(decoder_1_out28), .out29(decoder_1_out29), .out30(decoder_1_out30), .out31(decoder_1_out31),
    .sel(random_2_out), .en(Selection_On));
  Register #(.width(32)) register_1 (.D(random_1_out), .en(decoder_1_out0), .Q(register_1_q), .clk(clk));  // open: clr
  Register #(.width(32)) register_2 (.D(random_1_out), .en(decoder_1_out1), .Q(register_2_q), .clk(clk));  // open: clr
  Register #(.width(32)) register_3 (.D(random_1_out), .en(decoder_1_out2), .Q(register_3_q), .clk(clk));  // open: clr
  Register #(.width(32)) register_4 (.D(random_1_out), .en(decoder_1_out3), .Q(register_4_q), .clk(clk));  // open: clr
  Register #(.width(32)) register_5 (.D(random_1_out), .en(decoder_1_out4), .Q(register_5_q), .clk(clk));  // open: clr
  Register #(.width(32)) register_6 (.D(random_1_out), .en(decoder_1_out5), .Q(register_6_q), .clk(clk));  // open: clr
  Register #(.width(32)) register_7 (.D(random_1_out), .en(decoder_1_out6), .Q(register_7_q), .clk(clk));  // open: clr
  Register #(.width(32)) register_8 (.D(random_1_out), .en(decoder_1_out7), .Q(register_8_q), .clk(clk));  // open: clr
  Register #(.width(32)) register_9 (.D(random_1_out), .en(decoder_1_out8), .Q(register_9_q), .clk(clk));  // open: clr
  Register #(.width(32)) register_10 (
    .D(random_1_out), .en(decoder_1_out9), .Q(register_10_q), .clk(clk));  // open: clr
  Register #(.width(32)) register_11 (
    .D(random_1_out), .en(decoder_1_out10), .Q(register_11_q), .clk(clk));  // open: clr
  Register #(.width(32)) register_12 (
    .D(random_1_out), .en(decoder_1_out11), .Q(register_12_q), .clk(clk));  // open: clr
  Register #(.width(32)) register_13 (
    .D(random_1_out), .en(decoder_1_out12), .Q(register_13_q), .clk(clk));  // open: clr
  Register #(.width(32)) register_14 (
    .D(random_1_out), .en(decoder_1_out13), .Q(register_14_q), .clk(clk));  // open: clr
  Register #(.width(32)) register_15 (
    .D(random_1_out), .en(decoder_1_out14), .Q(register_15_q), .clk(clk));  // open: clr
  Register #(.width(32)) register_16 (
    .D(random_1_out), .en(decoder_1_out15), .Q(register_16_q), .clk(clk));  // open: clr
  Register #(.width(32)) register_17 (
    .D(random_1_out), .en(decoder_1_out16), .Q(register_17_q), .clk(clk));  // open: clr
  Register #(.width(32)) register_18 (
    .D(random_1_out), .en(decoder_1_out17), .Q(register_18_q), .clk(clk));  // open: clr
  Register #(.width(32)) register_19 (
    .D(random_1_out), .en(decoder_1_out18), .Q(register_19_q), .clk(clk));  // open: clr
  Register #(.width(32)) register_20 (
    .D(random_1_out), .en(decoder_1_out19), .Q(register_20_q), .clk(clk));  // open: clr
  Register #(.width(32)) register_21 (
    .D(random_1_out), .en(decoder_1_out20), .Q(register_21_q), .clk(clk));  // open: clr
  Register #(.width(32)) register_22 (
    .D(random_1_out), .en(decoder_1_out21), .Q(register_22_q), .clk(clk));  // open: clr
  Register #(.width(32)) register_23 (
    .D(random_1_out), .en(decoder_1_out22), .Q(register_23_q), .clk(clk));  // open: clr
  Register #(.width(32)) register_24 (
    .D(random_1_out), .en(decoder_1_out23), .Q(register_24_q), .clk(clk));  // open: clr
  Register #(.width(32)) register_25 (
    .D(random_1_out), .en(decoder_1_out24), .Q(register_25_q), .clk(clk));  // open: clr
  Register #(.width(32)) register_26 (
    .D(random_1_out), .en(decoder_1_out25), .Q(register_26_q), .clk(clk));  // open: clr
  Register #(.width(32)) register_27 (
    .D(random_1_out), .en(decoder_1_out26), .Q(register_27_q), .clk(clk));  // open: clr
  Register #(.width(32)) register_28 (
    .D(random_1_out), .en(decoder_1_out27), .Q(register_28_q), .clk(clk));  // open: clr
  Register #(.width(32)) register_29 (
    .D(random_1_out), .en(decoder_1_out28), .Q(register_29_q), .clk(clk));  // open: clr
  Register #(.width(32)) register_30 (
    .D(random_1_out), .en(decoder_1_out29), .Q(register_30_q), .clk(clk));  // open: clr
  Register #(.width(32)) register_31 (
    .D(random_1_out), .en(decoder_1_out30), .Q(register_31_q), .clk(clk));  // open: clr
  Register #(.width(32)) register_32 (
    .D(random_1_out), .en(decoder_1_out31), .Q(register_32_q), .clk(clk));  // open: clr
  DotMatrix #(.inputtype("row"), .matrixcols(32), .matrixrows(32)) dotmatrix_1 (
    .row0(register_1_q), .row1(register_2_q), .row2(register_3_q), .row3(register_4_q), .row4(register_5_q),
    .row5(register_6_q), .row6(register_7_q), .row7(register_8_q), .row8(register_9_q), .row9(register_10_q),
    .row10(register_11_q), .row11(register_12_q), .row12(register_13_q), .row13(register_14_q),
    .row14(register_15_q), .row15(register_16_q), .row16(register_17_q), .row17(register_18_q),
    .row18(register_19_q), .row19(register_20_q), .row20(register_21_q), .row21(register_22_q),
    .row22(register_23_q), .row23(register_24_q), .row24(register_25_q), .row25(register_26_q),
    .row26(register_27_q), .row27(register_28_q), .row28(register_29_q), .row29(register_30_q),
    .row30(register_31_q), .row31(register_32_q));
  DotMatrix #(.inputtype("row"), .matrixcols(32), .matrixrows(32)) dotmatrix_2 (
    .row0(register_1_q), .row1(register_2_q), .row2(register_3_q), .row3(register_4_q), .row4(register_5_q),
    .row5(register_6_q), .row6(register_7_q), .row7(register_8_q), .row8(register_9_q), .row9(register_10_q),
    .row10(register_11_q), .row11(register_12_q), .row12(register_13_q), .row13(register_14_q),
    .row14(register_15_q), .row15(register_16_q), .row16(register_17_q), .row17(register_18_q),
    .row18(register_19_q), .row19(register_20_q), .row20(register_21_q), .row21(register_22_q),
    .row22(register_23_q), .row23(register_24_q), .row24(register_25_q), .row25(register_26_q),
    .row26(register_27_q), .row27(register_28_q), .row28(register_29_q), .row29(register_30_q),
    .row30(register_31_q), .row31(register_32_q));

  // Other names for the same wires on the sheet: on = Full_On
endmodule

module _32_32_buffer (
  input  [7:0] _0_byte,
  input  _0_byte_on,
  input  [7:0] _1_byte,
  input  _1_byte_On,
  input  [7:0] _2_byte,
  input  _2_byte_on,
  input  [7:0] _3_byte,
  input  _3_byte_On,
  input  [7:0] Selector,
  input  Selection_On,
  input  Bus_0
);

  wire clk, demultiplexer_1_out0, demultiplexer_1_out1, demultiplexer_1_out2, demultiplexer_1_out3,
       demultiplexer_1_out4, demultiplexer_1_out5, demultiplexer_1_out6, demultiplexer_1_out7,
       demultiplexer_1_out8, demultiplexer_1_out9, demultiplexer_1_out10, demultiplexer_1_out11,
       demultiplexer_1_out12, demultiplexer_1_out13, demultiplexer_1_out14, demultiplexer_1_out15,
       demultiplexer_1_out16, demultiplexer_1_out17, demultiplexer_1_out18, demultiplexer_1_out19,
       demultiplexer_1_out20, demultiplexer_1_out21, demultiplexer_1_out22, demultiplexer_1_out23,
       demultiplexer_1_out24, demultiplexer_1_out25, demultiplexer_1_out26, demultiplexer_1_out27,
       demultiplexer_1_out28, demultiplexer_1_out29, demultiplexer_1_out30, demultiplexer_1_out31;
  wire [4:0] undriven;
  wire [7:0] register_1_q, register_2_q, register_3_q, register_4_q, register_5_q;
  wire [31:0] register_6_q, register_7_q, register_8_q, register_9_q, register_10_q, register_11_q,
       register_12_q, register_13_q, register_14_q, register_15_q, register_16_q, register_17_q,
       register_18_q, register_19_q, register_20_q, register_21_q, register_22_q, register_23_q,
       register_24_q, register_25_q, register_26_q, register_27_q, register_28_q, register_29_q,
       register_30_q, register_31_q, register_32_q, register_33_q, register_34_q, register_35_q,
       register_36_q, register_37_q;

  Clock clock_1 (.out(clk));
  Register register_1 (.D(_0_byte), .en(_0_byte_on), .Q(register_1_q), .clk(clk));  // open: clr
  Register register_2 (.D(_1_byte), .en(_1_byte_On), .Q(register_2_q), .clk(clk));  // open: clr
  Register register_3 (.D(_2_byte), .en(_2_byte_on), .Q(register_3_q), .clk(clk));  // open: clr
  Register register_4 (.D(_3_byte), .en(_3_byte_On), .Q(register_4_q), .clk(clk));  // open: clr
  Register #(.trigger("high")) register_5 (.D(Selector), .en(Selection_On), .Q(register_5_q), .clk(clk));  // open: clr
  // Probe on register_5_q
  Demultiplexer #(.select(5), .disabled(0)) demultiplexer_1 (
    .out0(demultiplexer_1_out0), .out1(demultiplexer_1_out1), .out2(demultiplexer_1_out2),
    .out3(demultiplexer_1_out3), .out4(demultiplexer_1_out4), .out5(demultiplexer_1_out5),
    .out6(demultiplexer_1_out6), .out7(demultiplexer_1_out7), .out8(demultiplexer_1_out8),
    .out9(demultiplexer_1_out9), .out10(demultiplexer_1_out10), .out11(demultiplexer_1_out11),
    .out12(demultiplexer_1_out12), .out13(demultiplexer_1_out13), .out14(demultiplexer_1_out14),
    .out15(demultiplexer_1_out15), .out16(demultiplexer_1_out16), .out17(demultiplexer_1_out17),
    .out18(demultiplexer_1_out18), .out19(demultiplexer_1_out19), .out20(demultiplexer_1_out20),
    .out21(demultiplexer_1_out21), .out22(demultiplexer_1_out22), .out23(demultiplexer_1_out23),
    .out24(demultiplexer_1_out24), .out25(demultiplexer_1_out25), .out26(demultiplexer_1_out26),
    .out27(demultiplexer_1_out27), .out28(demultiplexer_1_out28), .out29(demultiplexer_1_out29),
    .out30(demultiplexer_1_out30), .out31(demultiplexer_1_out31), .in(Selection_On), .sel(register_5_q[4:0]));  // open: en
  Register #(.width(32)) register_6 (
    .D({register_4_q, register_3_q, register_2_q, register_1_q}), .en(demultiplexer_1_out0),
    .Q(register_6_q), .clk(clk));  // open: clr
  Register #(.width(32)) register_7 (
    .D({register_4_q, register_3_q, register_2_q, register_1_q}), .en(demultiplexer_1_out1),
    .Q(register_7_q), .clk(clk));  // open: clr
  Register #(.width(32)) register_8 (
    .D({register_4_q, register_3_q, register_2_q, register_1_q}), .en(demultiplexer_1_out2),
    .Q(register_8_q), .clk(clk));  // open: clr
  Register #(.width(32)) register_9 (
    .D({register_4_q, register_3_q, register_2_q, register_1_q}), .en(demultiplexer_1_out3),
    .Q(register_9_q), .clk(clk));  // open: clr
  Register #(.width(32)) register_10 (
    .D({register_4_q, register_3_q, register_2_q, register_1_q}), .en(demultiplexer_1_out4),
    .Q(register_10_q), .clk(clk));  // open: clr
  Register #(.width(32)) register_11 (
    .D({register_4_q, register_3_q, register_2_q, register_1_q}), .en(demultiplexer_1_out5),
    .Q(register_11_q), .clk(clk));  // open: clr
  Register #(.width(32)) register_12 (
    .D({register_4_q, register_3_q, register_2_q, register_1_q}), .en(demultiplexer_1_out6),
    .Q(register_12_q), .clk(clk));  // open: clr
  Register #(.width(32)) register_13 (
    .D({register_4_q, register_3_q, register_2_q, register_1_q}), .en(demultiplexer_1_out7),
    .Q(register_13_q), .clk(clk));  // open: clr
  Register #(.width(32)) register_14 (
    .D({register_4_q, register_3_q, register_2_q, register_1_q}), .en(demultiplexer_1_out8),
    .Q(register_14_q), .clk(clk));  // open: clr
  Register #(.width(32)) register_15 (
    .D({register_4_q, register_3_q, register_2_q, register_1_q}), .en(demultiplexer_1_out9),
    .Q(register_15_q), .clk(clk));  // open: clr
  Register #(.width(32)) register_16 (
    .D({register_4_q, register_3_q, register_2_q, register_1_q}), .en(demultiplexer_1_out10),
    .Q(register_16_q), .clk(clk));  // open: clr
  Register #(.width(32)) register_17 (
    .D({register_4_q, register_3_q, register_2_q, register_1_q}), .en(demultiplexer_1_out11),
    .Q(register_17_q), .clk(clk));  // open: clr
  Register #(.width(32)) register_18 (
    .D({register_4_q, register_3_q, register_2_q, register_1_q}), .en(demultiplexer_1_out12),
    .Q(register_18_q), .clk(clk));  // open: clr
  Register #(.width(32)) register_19 (
    .D({register_4_q, register_3_q, register_2_q, register_1_q}), .en(demultiplexer_1_out13),
    .Q(register_19_q), .clk(clk));  // open: clr
  Register #(.width(32)) register_20 (
    .D({register_4_q, register_3_q, register_2_q, register_1_q}), .en(demultiplexer_1_out14),
    .Q(register_20_q), .clk(clk));  // open: clr
  Register #(.width(32)) register_21 (
    .D({register_4_q, register_3_q, register_2_q, register_1_q}), .en(demultiplexer_1_out15),
    .Q(register_21_q), .clk(clk));  // open: clr
  Register #(.width(32)) register_22 (
    .D({register_4_q, register_3_q, register_2_q, register_1_q}), .en(demultiplexer_1_out16),
    .Q(register_22_q), .clk(clk));  // open: clr
  Register #(.width(32)) register_23 (
    .D({register_4_q, register_3_q, register_2_q, register_1_q}), .en(demultiplexer_1_out17),
    .Q(register_23_q), .clk(clk));  // open: clr
  Register #(.width(32)) register_24 (
    .D({register_4_q, register_3_q, register_2_q, register_1_q}), .en(demultiplexer_1_out18),
    .Q(register_24_q), .clk(clk));  // open: clr
  Register #(.width(32)) register_25 (
    .D({register_4_q, register_3_q, register_2_q, register_1_q}), .en(demultiplexer_1_out19),
    .Q(register_25_q), .clk(clk));  // open: clr
  Register #(.width(32)) register_26 (
    .D({register_4_q, register_3_q, register_2_q, register_1_q}), .en(demultiplexer_1_out20),
    .Q(register_26_q), .clk(clk));  // open: clr
  Register #(.width(32)) register_27 (
    .D({register_4_q, register_3_q, register_2_q, register_1_q}), .en(demultiplexer_1_out21),
    .Q(register_27_q), .clk(clk));  // open: clr
  Register #(.width(32)) register_28 (
    .D({register_4_q, register_3_q, register_2_q, register_1_q}), .en(demultiplexer_1_out22),
    .Q(register_28_q), .clk(clk));  // open: clr
  Register #(.width(32)) register_29 (
    .D({register_4_q, register_3_q, register_2_q, register_1_q}), .en(demultiplexer_1_out23),
    .Q(register_29_q), .clk(clk));  // open: clr
  Register #(.width(32)) register_30 (
    .D({register_4_q, register_3_q, register_2_q, register_1_q}), .en(demultiplexer_1_out24),
    .Q(register_30_q), .clk(clk));  // open: clr
  Register #(.width(32)) register_31 (
    .D({register_4_q, register_3_q, register_2_q, register_1_q}), .en(demultiplexer_1_out25),
    .Q(register_31_q), .clk(clk));  // open: clr
  Register #(.width(32)) register_32 (
    .D({register_4_q, register_3_q, register_2_q, register_1_q}), .en(demultiplexer_1_out26),
    .Q(register_32_q), .clk(clk));  // open: clr
  Register #(.width(32)) register_33 (
    .D({register_4_q, register_3_q, register_2_q, register_1_q}), .en(demultiplexer_1_out27),
    .Q(register_33_q), .clk(clk));  // open: clr
  Register #(.width(32)) register_34 (
    .D({register_4_q, register_3_q, register_2_q, register_1_q}), .en(demultiplexer_1_out28),
    .Q(register_34_q), .clk(clk));  // open: clr
  Register #(.width(32)) register_35 (
    .D({register_4_q, register_3_q, register_2_q, register_1_q}), .en(demultiplexer_1_out29),
    .Q(register_35_q), .clk(clk));  // open: clr
  Register #(.width(32)) register_36 (
    .D({register_4_q, register_3_q, register_2_q, register_1_q}), .en(demultiplexer_1_out30),
    .Q(register_36_q), .clk(clk));  // open: clr
  Register #(.width(32)) register_37 (
    .D({register_4_q, register_3_q, register_2_q, register_1_q}), .en(demultiplexer_1_out31),
    .Q(register_37_q), .clk(clk));  // open: clr
  Multiplexer #(.select(5), .width(32)) multiplexer_1 (
    .in0(register_6_q), .in1(register_7_q), .in2(register_8_q), .in3(register_9_q), .in4(register_10_q),
    .in5(register_11_q), .in6(register_12_q), .in7(register_13_q), .in8(register_14_q), .in9(register_15_q),
    .in10(register_16_q), .in11(register_17_q), .in12(register_18_q), .in13(register_19_q),
    .in14(register_20_q), .in15(register_21_q), .in16(register_22_q), .in17(register_23_q),
    .in18(register_24_q), .in19(register_25_q), .in20(register_26_q), .in21(register_27_q),
    .in22(register_28_q), .in23(register_29_q), .in24(register_30_q), .in25(register_31_q),
    .in26(register_32_q), .in27(register_33_q), .in28(register_34_q), .in29(register_35_q),
    .in30(register_36_q), .in31(register_37_q), .sel(undriven));  // open: out, en
endmodule
