// Logisim project new_bit_invertor.circ as structural Verilog: 2 circuits, main circuit NEW_select
module NEW_select (
  input  [31:0] input1,
  input  switch,
  input  [31:0] input2,
  output [31:0] \output 
);

  wire not_1_out;

  not not_1 (not_1_out, switch);
  assign \output  = not_1_out ? input1 : 32'bz;  // Controlled_Buffer controlled_buffer_1
  assign \output  = switch ? input2 : 32'bz;  // Controlled_Buffer controlled_buffer_2
endmodule

module NEW_bit_invertor (
  input  [31:0] input0,
  input  [31:0] input1,
  input  [31:0] input2,
  input  [31:0] input3,
  input  [31:0] input4,
  input  [31:0] input5,
  input  [31:0] input6,
  input  [31:0] input7,
  input  [31:0] input8,
  input  [31:0] input9,
  input  [31:0] input10,
  input  [31:0] input11,
  input  [31:0] input12,
  input  [31:0] input13,
  input  [31:0] input14,
  input  [31:0] input15,
  input  [31:0] input16,
  input  [31:0] input17,
  input  [31:0] input18,
  input  [31:0] input19,
  input  [31:0] input20,
  input  [31:0] input21,
  input  [31:0] input22,
  input  [31:0] input23,
  input  [31:0] input24,
  input  [31:0] input25,
  input  [31:0] input26,
  input  [31:0] input27,
  input  [31:0] input28,
  input  [31:0] input29,
  input  [31:0] input30,
  input  [31:0] input31,
  input  [4:0] X,
  input  [4:0] Y,
  input  SWITCH,
  output [31:0] changed_string,
  output [31:0] output0,
  output [31:0] output1,
  output [31:0] output2,
  output [31:0] output3,
  output [31:0] output4,
  output [31:0] output5,
  output [31:0] output6,
  output [31:0] output7,
  output [31:0] output8,
  output [31:0] output9,
  output [31:0] output10,
  output [31:0] output11,
  output [31:0] output12,
  output [31:0] output13,
  output [31:0] output14,
  output [31:0] output15,
  output [31:0] output16,
  output [31:0] output17,
  output [31:0] output18,
  output [31:0] output19,
  output [31:0] output20,
  output [31:0] output21,
  output [31:0] output22,
  output [31:0] output23,
  output [31:0] output24,
  output [31:0] output25,
  output [31:0] output26,
  output [31:0] output27,
  output [31:0] output28,
  output [31:0] output29,
  output [31:0] output30,
  output [31:0] output31
);

  wire decoder_2_out0, decoder_2_out1, decoder_2_out2, decoder_2_out3, decoder_2_out4, decoder_2_out5,
       decoder_2_out6, decoder_2_out7, decoder_2_out8, decoder_2_out9, decoder_2_out10, decoder_2_out11,
       decoder_2_out12, decoder_2_out13, decoder_2_out14, decoder_2_out15, decoder_2_out16, decoder_2_out17,
       decoder_2_out18, decoder_2_out19, decoder_2_out20, decoder_2_out21, decoder_2_out22, decoder_2_out23,
       decoder_2_out24, decoder_2_out25, decoder_2_out26, decoder_2_out27, decoder_2_out28, decoder_2_out29,
       decoder_2_out30, decoder_2_out31;
  wire [31:0] decoder_1_out0, multiplexer_1_out, new_select_2_output, new_select_4_output,
       new_select_6_output, new_select_8_output, new_select_10_output, new_select_12_output,
       new_select_14_output, new_select_16_output, new_select_18_output, new_select_20_output,
       new_select_22_output, new_select_24_output, new_select_26_output, new_select_28_output,
       new_select_30_output, new_select_32_output, new_select_34_output, new_select_36_output,
       new_select_38_output, new_select_40_output, new_select_42_output, new_select_44_output,
       new_select_46_output, new_select_48_output, new_select_50_output, new_select_52_output,
       new_select_54_output, new_select_56_output, new_select_58_output, new_select_60_output,
       new_select_62_output, new_select_64_output, STRING;

  Multiplexer #(.select(5), .width(32), .disabled(0)) multiplexer_1 (
    .in0(input0), .in1(input1), .in2(input2), .in3(input3), .in4(input4), .in5(input5), .in6(input6),
    .in7(input7), .in8(input8), .in9(input9), .in10(input10), .in11(input11), .in12(input12), .in13(input13),
    .in14(input14), .in15(input15), .in16(input16), .in17(input17), .in18(input18), .in19(input19),
    .in20(input20), .in21(input21), .in22(input22), .in23(input23), .in24(input24), .in25(input25),
    .in26(input26), .in27(input27), .in28(input28), .in29(input29), .in30(input30), .in31(input31),
    .out(multiplexer_1_out), .sel(Y), .en(1'b1));
  Decoder #(.select(5), .disabled(0)) decoder_1 (
    .out0(decoder_1_out0[0]), .out1(decoder_1_out0[1]), .out2(decoder_1_out0[2]), .out3(decoder_1_out0[3]),
    .out4(decoder_1_out0[4]), .out5(decoder_1_out0[5]), .out6(decoder_1_out0[6]), .out7(decoder_1_out0[7]),
    .out8(decoder_1_out0[8]), .out9(decoder_1_out0[9]), .out10(decoder_1_out0[10]),
    .out11(decoder_1_out0[11]), .out12(decoder_1_out0[12]), .out13(decoder_1_out0[13]),
    .out14(decoder_1_out0[14]), .out15(decoder_1_out0[15]), .out16(decoder_1_out0[16]),
    .out17(decoder_1_out0[17]), .out18(decoder_1_out0[18]), .out19(decoder_1_out0[19]),
    .out20(decoder_1_out0[20]), .out21(decoder_1_out0[21]), .out22(decoder_1_out0[22]),
    .out23(decoder_1_out0[23]), .out24(decoder_1_out0[24]), .out25(decoder_1_out0[25]),
    .out26(decoder_1_out0[26]), .out27(decoder_1_out0[27]), .out28(decoder_1_out0[28]),
    .out29(decoder_1_out0[29]), .out30(decoder_1_out0[30]), .out31(decoder_1_out0[31]), .sel(X), .en(SWITCH));
  assign STRING = multiplexer_1_out ^ decoder_1_out0;  // XOR_Gate xor_1, 32 bits wide
  NEW_select new_select_1 (.switch(SWITCH), .input2(STRING), .\output (changed_string), .input1(multiplexer_1_out));
  NEW_select new_select_2 (.switch(decoder_2_out0), .input2(STRING), .\output (new_select_2_output), .input1(input0));
  NEW_select new_select_3 (.switch(SWITCH), .input2(new_select_2_output), .\output (output0), .input1(input0));
  NEW_select new_select_4 (.switch(decoder_2_out1), .input2(STRING), .\output (new_select_4_output), .input1(input1));
  NEW_select new_select_5 (.switch(SWITCH), .input2(new_select_4_output), .\output (output1), .input1(input1));
  NEW_select new_select_6 (.switch(decoder_2_out2), .input2(STRING), .\output (new_select_6_output), .input1(input2));
  NEW_select new_select_7 (.switch(SWITCH), .input2(new_select_6_output), .\output (output2), .input1(input2));
  NEW_select new_select_8 (.switch(decoder_2_out3), .input2(STRING), .\output (new_select_8_output), .input1(input3));
  NEW_select new_select_9 (.switch(SWITCH), .input2(new_select_8_output), .\output (output3), .input1(input3));
  NEW_select new_select_10 (.switch(decoder_2_out4), .input2(STRING), .\output (new_select_10_output), .input1(input4));
  NEW_select new_select_11 (.switch(SWITCH), .input2(new_select_10_output), .\output (output4), .input1(input4));
  NEW_select new_select_12 (.switch(decoder_2_out5), .input2(STRING), .\output (new_select_12_output), .input1(input5));
  NEW_select new_select_13 (.switch(SWITCH), .input2(new_select_12_output), .\output (output5), .input1(input5));
  NEW_select new_select_14 (.switch(decoder_2_out6), .input2(STRING), .\output (new_select_14_output), .input1(input6));
  NEW_select new_select_15 (.switch(SWITCH), .input2(new_select_14_output), .\output (output6), .input1(input6));
  NEW_select new_select_16 (.switch(decoder_2_out7), .input2(STRING), .\output (new_select_16_output), .input1(input7));
  NEW_select new_select_17 (.switch(SWITCH), .input2(new_select_16_output), .\output (output7), .input1(input7));
  NEW_select new_select_18 (.switch(decoder_2_out8), .input2(STRING), .\output (new_select_18_output), .input1(input8));
  NEW_select new_select_19 (.switch(SWITCH), .input2(new_select_18_output), .\output (output8), .input1(input8));
  NEW_select new_select_20 (.switch(decoder_2_out9), .input2(STRING), .\output (new_select_20_output), .input1(input9));
  NEW_select new_select_21 (.switch(SWITCH), .input2(new_select_20_output), .\output (output9), .input1(input9));
  NEW_select new_select_22 (
    .switch(decoder_2_out10), .input2(STRING), .\output (new_select_22_output), .input1(input10));
  NEW_select new_select_23 (.switch(SWITCH), .input2(new_select_22_output), .\output (output10), .input1(input10));
  NEW_select new_select_24 (
    .switch(decoder_2_out11), .input2(STRING), .\output (new_select_24_output), .input1(input11));
  NEW_select new_select_25 (.switch(SWITCH), .input2(new_select_24_output), .\output (output11), .input1(input11));
  NEW_select new_select_26 (
    .switch(decoder_2_out12), .input2(STRING), .\output (new_select_26_output), .input1(input12));
  NEW_select new_select_27 (.switch(SWITCH), .input2(new_select_26_output), .\output (output12), .input1(input12));
  NEW_select new_select_28 (
    .switch(decoder_2_out13), .input2(STRING), .\output (new_select_28_output), .input1(input13));
  NEW_select new_select_29 (.switch(SWITCH), .input2(new_select_28_output), .\output (output13), .input1(input13));
  NEW_select new_select_30 (
    .switch(decoder_2_out14), .input2(STRING), .\output (new_select_30_output), .input1(input14));
  NEW_select new_select_31 (.switch(SWITCH), .input2(new_select_30_output), .\output (output14), .input1(input14));
  Decoder #(.select(5), .disabled(0)) decoder_2 (
    .out0(decoder_2_out0), .out1(decoder_2_out1), .out2(decoder_2_out2), .out3(decoder_2_out3),
    .out4(decoder_2_out4), .out5(decoder_2_out5), .out6(decoder_2_out6), .out7(decoder_2_out7),
    .out8(decoder_2_out8), .out9(decoder_2_out9), .out10(decoder_2_out10), .out11(decoder_2_out11),
    .out12(decoder_2_out12), .out13(decoder_2_out13), .out14(decoder_2_out14), .out15(decoder_2_out15),
    .out16(decoder_2_out16), .out17(decoder_2_out17), .out18(decoder_2_out18), .out19(decoder_2_out19),
    .out20(decoder_2_out20), .out21(decoder_2_out21), .out22(decoder_2_out22), .out23(decoder_2_out23),
    .out24(decoder_2_out24), .out25(decoder_2_out25), .out26(decoder_2_out26), .out27(decoder_2_out27),
    .out28(decoder_2_out28), .out29(decoder_2_out29), .out30(decoder_2_out30), .out31(decoder_2_out31),
    .sel(Y), .en(SWITCH));
  NEW_select new_select_32 (
    .switch(decoder_2_out15), .input2(STRING), .\output (new_select_32_output), .input1(input15));
  NEW_select new_select_33 (.switch(SWITCH), .input2(new_select_32_output), .\output (output15), .input1(input15));
  NEW_select new_select_34 (
    .switch(decoder_2_out16), .input2(STRING), .\output (new_select_34_output), .input1(input16));
  NEW_select new_select_35 (.switch(SWITCH), .input2(new_select_34_output), .\output (output16), .input1(input16));
  NEW_select new_select_36 (
    .switch(decoder_2_out17), .input2(STRING), .\output (new_select_36_output), .input1(input17));
  NEW_select new_select_37 (.switch(SWITCH), .input2(new_select_36_output), .\output (output17), .input1(input17));
  NEW_select new_select_38 (
    .switch(decoder_2_out18), .input2(STRING), .\output (new_select_38_output), .input1(input18));
  NEW_select new_select_39 (.switch(SWITCH), .input2(new_select_38_output), .\output (output18), .input1(input18));
  NEW_select new_select_40 (
    .switch(decoder_2_out19), .input2(STRING), .\output (new_select_40_output), .input1(input19));
  NEW_select new_select_41 (.switch(SWITCH), .input2(new_select_40_output), .\output (output19), .input1(input19));
  NEW_select new_select_42 (
    .switch(decoder_2_out20), .input2(STRING), .\output (new_select_42_output), .input1(input20));
  NEW_select new_select_43 (.switch(SWITCH), .input2(new_select_42_output), .\output (output20), .input1(input20));
  NEW_select new_select_44 (
    .switch(decoder_2_out21), .input2(STRING), .\output (new_select_44_output), .input1(input21));
  NEW_select new_select_45 (.switch(SWITCH), .input2(new_select_44_output), .\output (output21), .input1(input21));
  NEW_select new_select_46 (
    .switch(decoder_2_out22), .input2(STRING), .\output (new_select_46_output), .input1(input22));
  NEW_select new_select_47 (.switch(SWITCH), .input2(new_select_46_output), .\output (output22), .input1(input22));
  NEW_select new_select_48 (
    .switch(decoder_2_out23), .input2(STRING), .\output (new_select_48_output), .input1(input23));
  NEW_select new_select_49 (.switch(SWITCH), .input2(new_select_48_output), .\output (output23), .input1(input23));
  NEW_select new_select_50 (
    .switch(decoder_2_out24), .input2(STRING), .\output (new_select_50_output), .input1(input24));
  NEW_select new_select_51 (.switch(SWITCH), .input2(new_select_50_output), .\output (output24), .input1(input24));
  NEW_select new_select_52 (
    .switch(decoder_2_out25), .input2(STRING), .\output (new_select_52_output), .input1(input25));
  NEW_select new_select_53 (.switch(SWITCH), .input2(new_select_52_output), .\output (output25), .input1(input25));
  NEW_select new_select_54 (
    .switch(decoder_2_out26), .input2(STRING), .\output (new_select_54_output), .input1(input26));
  NEW_select new_select_55 (.switch(SWITCH), .input2(new_select_54_output), .\output (output26), .input1(input26));
  NEW_select new_select_56 (
    .switch(decoder_2_out27), .input2(STRING), .\output (new_select_56_output), .input1(input27));
  NEW_select new_select_57 (.switch(SWITCH), .input2(new_select_56_output), .\output (output27), .input1(input27));
  NEW_select new_select_58 (
    .switch(decoder_2_out28), .input2(STRING), .\output (new_select_58_output), .input1(input28));
  NEW_select new_select_59 (.switch(SWITCH), .input2(new_select_58_output), .\output (output28), .input1(input28));
  NEW_select new_select_60 (
    .switch(decoder_2_out29), .input2(STRING), .\output (new_select_60_output), .input1(input29));
  NEW_select new_select_61 (.switch(SWITCH), .input2(new_select_60_output), .\output (output29), .input1(input29));
  NEW_select new_select_62 (
    .switch(decoder_2_out30), .input2(STRING), .\output (new_select_62_output), .input1(input30));
  NEW_select new_select_63 (.switch(SWITCH), .input2(new_select_62_output), .\output (output30), .input1(input30));
  NEW_select new_select_64 (
    .switch(decoder_2_out31), .input2(STRING), .\output (new_select_64_output), .input1(input31));
  NEW_select new_select_65 (.switch(SWITCH), .input2(new_select_64_output), .\output (output31), .input1(input31));
endmodule
