// Logisim project task1.circ as structural Verilog: 3 circuits, main circuit main
module main (
  input  [31:0] in_1,
  input  [31:0] in_2,
  input  [31:0] in_3,
  input  [31:0] in_4,
  input  [31:0] in_5,
  input  [31:0] in_6,
  input  Switch,
  input  [4:0] Y,
  input  [4:0] X,
  input  [31:0] in_10,
  input  [31:0] in_11,
  input  [31:0] in_12,
  input  [31:0] in_13,
  input  [31:0] in_14,
  input  [31:0] in_15,
  input  [31:0] in_16,
  input  [31:0] in_17,
  input  [31:0] in_18,
  input  [31:0] in_19,
  input  [31:0] in_20,
  input  [31:0] in_21,
  input  [31:0] in_22,
  input  [31:0] in_23,
  input  [31:0] in_24,
  input  [31:0] in_25,
  input  [31:0] in_26,
  input  [31:0] in_27,
  input  [31:0] in_28,
  input  [31:0] in_29,
  input  [31:0] in_30,
  input  [31:0] in_31,
  input  [31:0] in_32,
  input  [31:0] in_33,
  input  [31:0] in_34,
  input  [31:0] in_35,
  output [31:0] out_36
);

  wire [31:0] bit_invertor_1_output1, bit_invertor_1_output2, bit_invertor_1_output3, bit_invertor_1_output4,
       bit_invertor_1_output5, bit_invertor_1_output6, bit_invertor_1_output7, bit_invertor_1_output8,
       bit_invertor_1_output9, bit_invertor_1_output10, bit_invertor_1_output11, bit_invertor_1_output12,
       bit_invertor_1_output13, bit_invertor_1_output14, bit_invertor_1_output15, bit_invertor_1_output16,
       bit_invertor_1_output17, bit_invertor_1_output18, bit_invertor_1_output19, bit_invertor_1_output20,
       bit_invertor_1_output21, bit_invertor_1_output22, bit_invertor_1_output23, bit_invertor_1_output24,
       bit_invertor_1_output25, bit_invertor_1_output26, bit_invertor_1_output27, bit_invertor_1_output28,
       bit_invertor_1_output29, bit_invertor_1_output30, bit_invertor_1_output31, bit_invertor_1_output32;

  DotMatrix #(.inputtype("row"), .matrixcols(32), .matrixrows(32)) dotmatrix_1 (
    .row0(in_1), .row1(in_2), .row2(in_3), .row3(in_4), .row4(in_5), .row5(in_6), .row6(in_10), .row7(in_11),
    .row8(in_12), .row9(in_13), .row10(in_14), .row11(in_15), .row12(in_16), .row13(in_17), .row14(in_18),
    .row15(in_19), .row16(in_20), .row17(in_21), .row18(in_22), .row19(in_23), .row20(in_24), .row21(in_25),
    .row22(in_26), .row23(in_27), .row24(in_28), .row25(in_29), .row26(in_30), .row27(in_31), .row28(in_32),
    .row29(in_33), .row30(in_34), .row31(in_35));
  DotMatrix #(.inputtype("row"), .matrixcols(32), .matrixrows(32)) dotmatrix_2 (
    .row0(bit_invertor_1_output1), .row1(bit_invertor_1_output2), .row2(bit_invertor_1_output3),
    .row3(bit_invertor_1_output4), .row4(bit_invertor_1_output5), .row5(bit_invertor_1_output6),
    .row6(bit_invertor_1_output7), .row7(bit_invertor_1_output8), .row8(bit_invertor_1_output9),
    .row9(bit_invertor_1_output10), .row10(bit_invertor_1_output11), .row11(bit_invertor_1_output12),
    .row12(bit_invertor_1_output13), .row13(bit_invertor_1_output14), .row14(bit_invertor_1_output15),
    .row15(bit_invertor_1_output16), .row16(bit_invertor_1_output17), .row17(bit_invertor_1_output18),
    .row18(bit_invertor_1_output19), .row19(bit_invertor_1_output20), .row20(bit_invertor_1_output21),
    .row21(bit_invertor_1_output22), .row22(bit_invertor_1_output23), .row23(bit_invertor_1_output24),
    .row24(bit_invertor_1_output25), .row25(bit_invertor_1_output26), .row26(bit_invertor_1_output27),
    .row27(bit_invertor_1_output28), .row28(bit_invertor_1_output29), .row29(bit_invertor_1_output30),
    .row30(bit_invertor_1_output31), .row31(bit_invertor_1_output32));
  bit_invertor bit_invertor_1 (
    .INPUT9(in_12), .INPUT1(in_1), .INPUT10(in_13), .INPUT17(in_20), .INPUT2(in_2), .INPUT11(in_14),
    .INPUT18(in_21), .INPUT25(in_28), .INPUT3(in_3), .INPUT12(in_15), .INPUT19(in_22), .INPUT26(in_29),
    .INPUT4(in_4), .SWITCH(Switch), .INPUT13(in_16), .INPUT20(in_23), .INPUT27(in_30), .Y(Y), .INPUT5(in_5),
    .X(X), .INPUT14(in_17), .INPUT21(in_24), .INPUT28(in_31), .INPUT6(in_6), .INPUT15(in_18),
    .INPUT22(in_25), .INPUT29(in_32), .INPUT7(in_10), .INPUT16(in_19), .INPUT23(in_26), .INPUT30(in_33),
    .INPUT8(in_11), .INPUT24(in_27), .INPUT31(in_34), .INPUT32(in_35), .CHANGED_STRING(out_36),
    .OUTPUT1(bit_invertor_1_output1), .OUTPUT2(bit_invertor_1_output2), .OUTPUT3(bit_invertor_1_output3),
    .OUTPUT4(bit_invertor_1_output4), .OUTPUT5(bit_invertor_1_output5), .OUTPUT6(bit_invertor_1_output6),
    .OUTPUT7(bit_invertor_1_output7), .OUTPUT8(bit_invertor_1_output8), .OUTPUT9(bit_invertor_1_output9),
    .OUTPUT10(bit_invertor_1_output10), .OUTPUT11(bit_invertor_1_output11),
    .OUTPUT12(bit_invertor_1_output12), .OUTPUT13(bit_invertor_1_output13),
    .OUTPUT14(bit_invertor_1_output14), .OUTPUT15(bit_invertor_1_output15),
    .OUTPUT16(bit_invertor_1_output16), .OUTPUT17(bit_invertor_1_output17),
    .OUTPUT18(bit_invertor_1_output18), .OUTPUT19(bit_invertor_1_output19),
    .OUTPUT20(bit_invertor_1_output20), .OUTPUT21(bit_invertor_1_output21),
    .OUTPUT22(bit_invertor_1_output22), .OUTPUT23(bit_invertor_1_output23),
    .OUTPUT24(bit_invertor_1_output24), .OUTPUT25(bit_invertor_1_output25),
    .OUTPUT26(bit_invertor_1_output26), .OUTPUT27(bit_invertor_1_output27),
    .OUTPUT28(bit_invertor_1_output28), .OUTPUT29(bit_invertor_1_output29),
    .OUTPUT30(bit_invertor_1_output30), .OUTPUT31(bit_invertor_1_output31), .OUTPUT32(bit_invertor_1_output32));
endmodule

module SELECT (
  input  [31:0] Input1,
  input  Switch,
  input  [31:0] Input2,
  output [31:0] Output
);

  wire not_1_out;

  not not_1 (not_1_out, Switch);
  assign Output = not_1_out ? Input1 : 32'bz;  // Controlled_Buffer controlled_buffer_1
  assign Output = Switch ? Input2 : 32'bz;  // Controlled_Buffer controlled_buffer_2
endmodule

module bit_invertor (
  input  [31:0] INPUT9,
  input  [31:0] INPUT1,
  input  [31:0] INPUT10,
  input  [31:0] INPUT17,
  input  [31:0] INPUT2,
  input  [31:0] INPUT11,
  input  [31:0] INPUT18,
  input  [31:0] INPUT25,
  input  [31:0] INPUT3,
  input  [31:0] INPUT12,
  input  [31:0] INPUT19,
  input  [31:0] INPUT26,
  input  [31:0] INPUT4,
  input  SWITCH,
  input  [31:0] INPUT13,
  input  [31:0] INPUT20,
  input  [31:0] INPUT27,
  input  [4:0] Y,
  input  [31:0] INPUT5,
  input  [4:0] X,
  input  [31:0] INPUT14,
  input  [31:0] INPUT21,
  input  [31:0] INPUT28,
  input  [31:0] INPUT6,
  input  [31:0] INPUT15,
  input  [31:0] INPUT22,
  input  [31:0] INPUT29,
  input  [31:0] INPUT7,
  input  [31:0] INPUT16,
  input  [31:0] INPUT23,
  input  [31:0] INPUT30,
  input  [31:0] INPUT8,
  input  [31:0] INPUT24,
  input  [31:0] INPUT31,
  input  [31:0] INPUT32,
  output [31:0] CHANGED_STRING,
  output [31:0] OUTPUT1,
  output [31:0] OUTPUT2,
  output [31:0] OUTPUT3,
  output [31:0] OUTPUT4,
  output [31:0] OUTPUT5,
  output [31:0] OUTPUT6,
  output [31:0] OUTPUT7,
  output [31:0] OUTPUT8,
  output [31:0] OUTPUT9,
  output [31:0] OUTPUT10,
  output [31:0] OUTPUT11,
  output [31:0] OUTPUT12,
  output [31:0] OUTPUT13,
  output [31:0] OUTPUT14,
  output [31:0] OUTPUT15,
  output [31:0] OUTPUT16,
  output [31:0] OUTPUT17,
  output [31:0] OUTPUT18,
  output [31:0] OUTPUT19,
  output [31:0] OUTPUT20,
  output [31:0] OUTPUT21,
  output [31:0] OUTPUT22,
  output [31:0] OUTPUT23,
  output [31:0] OUTPUT24,
  output [31:0] OUTPUT25,
  output [31:0] OUTPUT26,
  output [31:0] OUTPUT27,
  output [31:0] OUTPUT28,
  output [31:0] OUTPUT29,
  output [31:0] OUTPUT30,
  output [31:0] OUTPUT31,
  output [31:0] OUTPUT32
);

  wire decoder_2_out0, decoder_2_out1, decoder_2_out2, decoder_2_out3, decoder_2_out4, decoder_2_out5,
       decoder_2_out6, decoder_2_out7, decoder_2_out8, decoder_2_out9, decoder_2_out10, decoder_2_out11,
       decoder_2_out12, decoder_2_out13, decoder_2_out14, decoder_2_out15, decoder_2_out16, decoder_2_out17,
       decoder_2_out18, decoder_2_out19, decoder_2_out20, decoder_2_out21, decoder_2_out22, decoder_2_out23,
       decoder_2_out24, decoder_2_out25, decoder_2_out26, decoder_2_out27, decoder_2_out28, decoder_2_out29,
       decoder_2_out30, decoder_2_out31;
  wire [31:0] decoder_1_out0, multiplexer_1_out, select_22_output, select_23_output, select_24_output,
       select_25_output, select_26_output, select_27_output, select_28_output, select_29_output,
       select_30_output, select_31_output, select_32_output, select_33_output, select_34_output,
       select_35_output, select_36_output, select_37_output, select_38_output, select_39_output,
       select_40_output, select_41_output, select_42_output, select_43_output, select_44_output,
       select_45_output, select_46_output, select_47_output, select_48_output, select_49_output,
       select_50_output, select_51_output, select_52_output, select_53_output, xor_1_out;

  SELECT select_1 (.Input1(INPUT1), .Switch(SWITCH), .Input2(select_22_output), .Output(OUTPUT1));
  SELECT select_2 (.Input1(INPUT2), .Switch(SWITCH), .Input2(select_23_output), .Output(OUTPUT2));
  SELECT select_3 (.Input1(INPUT3), .Switch(SWITCH), .Input2(select_24_output), .Output(OUTPUT3));
  SELECT select_4 (.Input1(INPUT4), .Switch(SWITCH), .Input2(select_25_output), .Output(OUTPUT4));
  SELECT select_5 (.Input1(INPUT5), .Switch(SWITCH), .Input2(select_26_output), .Output(OUTPUT5));
  SELECT select_6 (.Input1(INPUT6), .Switch(SWITCH), .Input2(select_27_output), .Output(OUTPUT6));
  SELECT select_7 (.Input1(INPUT7), .Switch(SWITCH), .Input2(select_28_output), .Output(OUTPUT7));
  SELECT select_8 (.Input1(INPUT8), .Switch(SWITCH), .Input2(select_29_output), .Output(OUTPUT8));
  SELECT select_9 (.Input1(INPUT9), .Switch(SWITCH), .Input2(select_30_output), .Output(OUTPUT9));
  SELECT select_10 (.Input1(INPUT10), .Switch(SWITCH), .Input2(select_31_output), .Output(OUTPUT10));
  SELECT select_11 (.Input1(INPUT11), .Switch(SWITCH), .Input2(select_32_output), .Output(OUTPUT11));
  Multiplexer #(.select(5), .width(32)) multiplexer_1 (
    .in0(INPUT1), .in1(INPUT2), .in2(INPUT3), .in3(INPUT4), .in4(INPUT5), .in5(INPUT6), .in6(INPUT7),
    .in7(INPUT8), .in8(INPUT9), .in9(INPUT10), .in10(INPUT11), .in11(INPUT12), .in12(INPUT13),
    .in13(INPUT14), .in14(INPUT15), .in15(INPUT16), .in16(INPUT17), .in17(INPUT18), .in18(INPUT19),
    .in19(INPUT20), .in20(INPUT21), .in21(INPUT22), .in22(INPUT23), .in23(INPUT24), .in24(INPUT25),
    .in25(INPUT26), .in26(INPUT27), .in27(INPUT28), .in28(INPUT29), .in29(INPUT30), .in30(INPUT31),
    .in31(INPUT32), .out(multiplexer_1_out), .sel(Y), .en(1'b1));
  SELECT select_12 (.Input1(INPUT12), .Switch(SWITCH), .Input2(select_33_output), .Output(OUTPUT12));
  Decoder #(.select(5), .disabled(0)) decoder_1 (
    .out0(decoder_1_out0[0]), .out1(decoder_1_out0[1]), .out2(decoder_1_out0[2]), .out3(decoder_1_out0[3]),
    .out4(decoder_1_out0[4]), .out5(decoder_1_out0[5]), .out6(decoder_1_out0[6]), .out7(decoder_1_out0[7]),
    .out8(decoder_1_out0[8]), .out9(decoder_1_out0[9]), .out10(decoder_1_out0[10]),
    .out11(decoder_1_out0[11]), .out12(decoder_1_out0[12]), .out13(decoder_1_out0[13]),
    .out14(decoder_1_out0[14]), .out15(decoder_1_out0[15]), .out16(decoder_1_out0[16]),
    .out17(decoder_1_out0[17]), .out18(decoder_1_out0[18]), .out19(decoder_1_out0[19]),
    .out20(decoder_1_out0[20]), .out21(decoder_1_out0[21]), .out22(decoder_1_out0[22]),
    .out23(decoder_1_out0[23]), .out24(decoder_1_out0[24]), .out25(decoder_1_out0[25]),
    .out26(decoder_1_out0[26]), .out27(decoder_1_out0[27]), .out28(decoder_1_out0[28]),
    .out29(decoder_1_out0[29]), .out30(decoder_1_out0[30]), .out31(decoder_1_out0[31]), .sel(X), .en(SWITCH));
  Decoder #(.select(5), .disabled(0)) decoder_2 (
    .out0(decoder_2_out0), .out1(decoder_2_out1), .out2(decoder_2_out2), .out3(decoder_2_out3),
    .out4(decoder_2_out4), .out5(decoder_2_out5), .out6(decoder_2_out6), .out7(decoder_2_out7),
    .out8(decoder_2_out8), .out9(decoder_2_out9), .out10(decoder_2_out10), .out11(decoder_2_out11),
    .out12(decoder_2_out12), .out13(decoder_2_out13), .out14(decoder_2_out14), .out15(decoder_2_out15),
    .out16(decoder_2_out16), .out17(decoder_2_out17), .out18(decoder_2_out18), .out19(decoder_2_out19),
    .out20(decoder_2_out20), .out21(decoder_2_out21), .out22(decoder_2_out22), .out23(decoder_2_out23),
    .out24(decoder_2_out24), .out25(decoder_2_out25), .out26(decoder_2_out26), .out27(decoder_2_out27),
    .out28(decoder_2_out28), .out29(decoder_2_out29), .out30(decoder_2_out30), .out31(decoder_2_out31),
    .sel(Y), .en(SWITCH));
  SELECT select_13 (.Input1(INPUT13), .Switch(SWITCH), .Input2(select_34_output), .Output(OUTPUT13));
  SELECT select_14 (.Input1(INPUT14), .Switch(SWITCH), .Input2(select_35_output), .Output(OUTPUT14));
  assign xor_1_out = multiplexer_1_out ^ decoder_1_out0;  // XOR_Gate xor_1, 32 bits wide
  SELECT select_15 (.Input1(INPUT15), .Switch(SWITCH), .Input2(select_36_output), .Output(OUTPUT15));
  SELECT select_16 (.Input1(INPUT16), .Switch(SWITCH), .Input2(select_37_output), .Output(OUTPUT16));
  SELECT select_17 (.Input1(INPUT17), .Switch(SWITCH), .Input2(select_38_output), .Output(OUTPUT17));
  SELECT select_18 (.Input1(multiplexer_1_out), .Switch(SWITCH), .Input2(xor_1_out), .Output(CHANGED_STRING));
  SELECT select_19 (.Input1(INPUT18), .Switch(SWITCH), .Input2(select_39_output), .Output(OUTPUT18));
  SELECT select_20 (.Input1(INPUT19), .Switch(SWITCH), .Input2(select_40_output), .Output(OUTPUT19));
  SELECT select_21 (.Input1(INPUT20), .Switch(SWITCH), .Input2(select_41_output), .Output(OUTPUT20));
  SELECT select_22 (.Input1(INPUT1), .Switch(decoder_2_out0), .Input2(xor_1_out), .Output(select_22_output));
  SELECT select_23 (.Input1(INPUT2), .Switch(decoder_2_out1), .Input2(xor_1_out), .Output(select_23_output));
  SELECT select_24 (.Input1(INPUT3), .Switch(decoder_2_out2), .Input2(xor_1_out), .Output(select_24_output));
  SELECT select_25 (.Input1(INPUT4), .Switch(decoder_2_out3), .Input2(xor_1_out), .Output(select_25_output));
  SELECT select_26 (.Input1(INPUT5), .Switch(decoder_2_out4), .Input2(xor_1_out), .Output(select_26_output));
  SELECT select_27 (.Input1(INPUT6), .Switch(decoder_2_out5), .Input2(xor_1_out), .Output(select_27_output));
  SELECT select_28 (.Input1(INPUT7), .Switch(decoder_2_out6), .Input2(xor_1_out), .Output(select_28_output));
  SELECT select_29 (.Input1(INPUT8), .Switch(decoder_2_out7), .Input2(xor_1_out), .Output(select_29_output));
  SELECT select_30 (.Input1(INPUT9), .Switch(decoder_2_out8), .Input2(xor_1_out), .Output(select_30_output));
  SELECT select_31 (.Input1(INPUT10), .Switch(decoder_2_out9), .Input2(xor_1_out), .Output(select_31_output));
  SELECT select_32 (.Input1(INPUT11), .Switch(decoder_2_out10), .Input2(xor_1_out), .Output(select_32_output));
  SELECT select_33 (.Input1(INPUT12), .Switch(decoder_2_out11), .Input2(xor_1_out), .Output(select_33_output));
  SELECT select_34 (.Input1(INPUT13), .Switch(decoder_2_out12), .Input2(xor_1_out), .Output(select_34_output));
  SELECT select_35 (.Input1(INPUT14), .Switch(decoder_2_out13), .Input2(xor_1_out), .Output(select_35_output));
  SELECT select_36 (.Input1(INPUT15), .Switch(decoder_2_out14), .Input2(xor_1_out), .Output(select_36_output));
  SELECT select_37 (.Input1(INPUT16), .Switch(decoder_2_out15), .Input2(xor_1_out), .Output(select_37_output));
  SELECT select_38 (.Input1(INPUT17), .Switch(decoder_2_out16), .Input2(xor_1_out), .Output(select_38_output));
  SELECT select_39 (.Input1(INPUT18), .Switch(decoder_2_out17), .Input2(xor_1_out), .Output(select_39_output));
  SELECT select_40 (.Input1(INPUT19), .Switch(decoder_2_out18), .Input2(xor_1_out), .Output(select_40_output));
  SELECT select_41 (.Input1(INPUT20), .Switch(decoder_2_out19), .Input2(xor_1_out), .Output(select_41_output));
  SELECT select_42 (.Input1(INPUT21), .Switch(decoder_2_out20), .Input2(xor_1_out), .Output(select_42_output));
  SELECT select_43 (.Input1(INPUT22), .Switch(decoder_2_out21), .Input2(xor_1_out), .Output(select_43_output));
  SELECT select_44 (.Input1(INPUT23), .Switch(decoder_2_out22), .Input2(xor_1_out), .Output(select_44_output));
  SELECT select_45 (.Input1(INPUT24), .Switch(decoder_2_out23), .Input2(xor_1_out), .Output(select_45_output));
  SELECT select_46 (.Input1(INPUT25), .Switch(decoder_2_out24), .Input2(xor_1_out), .Output(select_46_output));
  SELECT select_47 (.Input1(INPUT26), .Switch(decoder_2_out25), .Input2(xor_1_out), .Output(select_47_output));
  SELECT select_48 (.Input1(INPUT27), .Switch(decoder_2_out26), .Input2(xor_1_out), .Output(select_48_output));
  SELECT select_49 (.Input1(INPUT28), .Switch(decoder_2_out27), .Input2(xor_1_out), .Output(select_49_output));
  SELECT select_50 (.Input1(INPUT29), .Switch(decoder_2_out28), .Input2(xor_1_out), .Output(select_50_output));
  SELECT select_51 (.Input1(INPUT30), .Switch(decoder_2_out29), .Input2(xor_1_out), .Output(select_51_output));
  SELECT select_52 (.Input1(INPUT31), .Switch(decoder_2_out30), .Input2(xor_1_out), .Output(select_52_output));
  SELECT select_53 (.Input1(INPUT32), .Switch(decoder_2_out31), .Input2(xor_1_out), .Output(select_53_output));
  SELECT select_54 (.Input1(INPUT21), .Switch(SWITCH), .Input2(select_42_output), .Output(OUTPUT21));
  SELECT select_55 (.Input1(INPUT22), .Switch(SWITCH), .Input2(select_43_output), .Output(OUTPUT22));
  SELECT select_56 (.Input1(INPUT23), .Switch(SWITCH), .Input2(select_44_output), .Output(OUTPUT23));
  SELECT select_57 (.Input1(INPUT24), .Switch(SWITCH), .Input2(select_45_output), .Output(OUTPUT24));
  SELECT select_58 (.Input1(INPUT25), .Switch(SWITCH), .Input2(select_46_output), .Output(OUTPUT25));
  SELECT select_59 (.Input1(INPUT26), .Switch(SWITCH), .Input2(select_47_output), .Output(OUTPUT26));
  SELECT select_60 (.Input1(INPUT27), .Switch(SWITCH), .Input2(select_48_output), .Output(OUTPUT27));
  SELECT select_61 (.Input1(INPUT28), .Switch(SWITCH), .Input2(select_49_output), .Output(OUTPUT28));
  SELECT select_62 (.Input1(INPUT29), .Switch(SWITCH), .Input2(select_50_output), .Output(OUTPUT29));
  SELECT select_63 (.Input1(INPUT30), .Switch(SWITCH), .Input2(select_51_output), .Output(OUTPUT30));
  SELECT select_64 (.Input1(INPUT31), .Switch(SWITCH), .Input2(select_52_output), .Output(OUTPUT31));
  SELECT select_65 (.Input1(INPUT32), .Switch(SWITCH), .Input2(select_53_output), .Output(OUTPUT32));
endmodule
